// Logisim project 16-bit CPU.circ as structural Verilog
module add_2 (
  input  A,
  input  B,
  input  Carry_In,
  output Sum_out,
  output Carry_out
);

  wire and_1_out, and_2_out, xor_1_out;

  xor xor_1 (xor_1_out, A, B);
  and and_1 (and_1_out, A, B);
  xor xor_2 (Sum_out, Carry_In, xor_1_out);
  and and_2 (and_2_out, Carry_In, xor_1_out);
  LED led_1 (.in(Sum_out));
  or or_1 (Carry_out, and_2_out, and_1_out);
  LED led_2 (.in(Carry_out));
endmodule

module add_4 (
  input  [3:0] A,
  input  Carry_In,
  input  [3:0] B,
  output [3:0] Sum_out,
  output Carry_out
);

  wire add_2_1_carry_out, add_2_3_carry_out, add_2_4_carry_out;

  // Probe on A
  // Probe on B
  add_2 add_2_1 (.A(A[0]), .B(B[0]), .Carry_In(Carry_In), .Sum_out(Sum_out[0]), .Carry_out(add_2_1_carry_out));
  add_2 add_2_2 (.A(A[3]), .B(B[3]), .Carry_In(add_2_4_carry_out), .Sum_out(Sum_out[3]), .Carry_out(Carry_out));
  add_2 add_2_3 (.A(A[1]), .B(B[1]), .Carry_In(add_2_1_carry_out), .Sum_out(Sum_out[1]), .Carry_out(add_2_3_carry_out));
  add_2 add_2_4 (.A(A[2]), .B(B[2]), .Carry_In(add_2_3_carry_out), .Sum_out(Sum_out[2]), .Carry_out(add_2_4_carry_out));
  // Probe on Sum_out
  LED led_1 (.in(Carry_out));
endmodule

module add_8 (
  input  [7:0] A,
  input  Carry_In,
  input  [7:0] B,
  output [7:0] sum_out,
  output Carry_out
);

  wire add_4_1_carry_out;

  // Probe on A
  // Probe on B
  add_4 add_4_1 (.A(A[3:0]), .Carry_In(Carry_In), .B(B[3:0]), .Sum_out(sum_out[3:0]), .Carry_out(add_4_1_carry_out));
  add_4 add_4_2 (.A(A[7:4]), .Carry_In(add_4_1_carry_out), .B(B[7:4]), .Sum_out(sum_out[7:4]), .Carry_out(Carry_out));
  LED led_1 (.in(Carry_out));
  // Probe on sum_out
endmodule

module add_16 (
  input  [15:0] A,
  input  Carry_In,
  input  [15:0] B,
  output [15:0] Sum_out,
  output Carry_out
);

  wire add_8_1_carry_out;

  // Probe on A
  // Probe on B
  add_8 add_8_1 (.A(A[7:0]), .Carry_In(Carry_In), .B(B[7:0]), .sum_out(Sum_out[7:0]), .Carry_out(add_8_1_carry_out));
  add_8 add_8_2 (
    .A(A[15:8]), .Carry_In(add_8_1_carry_out), .B(B[15:8]), .sum_out(Sum_out[15:8]), .Carry_out(Carry_out));
  // Probe on Sum_out
  LED led_1 (.in(Carry_out));
endmodule

module sub_8 (
  input  [7:0] A,
  input  Carry_In,
  input  [7:0] B,
  input  [7:0] Sub,
  output [7:0] sum_out,
  output Carry_out
);

  wire [7:0] xor_1_out;

  // Probe on A
  // Probe on B
  assign xor_1_out = B ^ Sub;  // XOR_Gate xor_1, 8 bits wide
  add_8 add_8_1 (.A(A), .Carry_In(Carry_In), .B(xor_1_out), .sum_out(sum_out), .Carry_out(Carry_out));
  // Probe on sum_out
endmodule

module sub_16 (
  input  [15:0] A,
  input  [15:0] B,
  output [15:0] sum_out
);

  wire [15:0] add_16_2_sum_out, not_1_out;

  // Probe on A
  // Probe on B
  assign not_1_out = ~B;  // NOT_Gate not_1, 16 bits wide
  add_16 add_16_1 (.A(A), .B(add_16_2_sum_out), .Sum_out(sum_out));  // open: Carry_In, Carry_out
  add_16 add_16_2 (.A(not_1_out), .B(16'h1), .Sum_out(add_16_2_sum_out));  // open: Carry_In, Carry_out
  // Probe on sum_out
endmodule

module mult_4 (
  input  [3:0] A,
  input  [3:0] B,
  output [7:0] product
);

  wire [3:0] add_4_3_sum_out, and_4_out, and_8_out, and_12_out, and_15_out;
  wire [3:1] add_4_2_sum_out;
  wire [3:3] add_4_2_carry_out;

  // Probe on A
  and and_1 (and_4_out[3], A[3], B[3]);
  and and_2 (and_4_out[2], A[3], B[2]);
  and and_3 (and_4_out[1], A[3], B[1]);
  and and_4 (and_4_out[0], A[3], B[0]);
  and and_5 (and_8_out[3], A[2], B[3]);
  and and_6 (and_8_out[2], A[2], B[2]);
  and and_7 (and_8_out[1], A[2], B[1]);
  and and_8 (and_8_out[0], A[2], B[0]);
  and and_9 (and_12_out[3], A[1], B[3]);
  and and_10 (and_12_out[2], A[1], B[2]);
  and and_11 (and_12_out[1], A[1], B[1]);
  // Probe on product
  and and_12 (and_12_out[0], A[1], B[0]);
  add_4 add_4_1 (.A(add_4_3_sum_out), .B(and_4_out), .Sum_out(product[6:3]), .Carry_out(product[7]));  // open: Carry_In
  add_4 add_4_2 (
    .A(and_15_out), .B(and_12_out), .Sum_out({add_4_2_sum_out, product[1]}), .Carry_out(add_4_2_carry_out[3]));  // open: Carry_In
  add_4 add_4_3 (
    .A({add_4_2_carry_out[3], add_4_2_sum_out}), .B(and_8_out), .Sum_out({add_4_3_sum_out[2:0], product[2]}),
    .Carry_out(add_4_3_sum_out[3]));  // open: Carry_In
  // Probe on B
  and and_13 (and_15_out[2], A[0], B[3]);
  and and_14 (and_15_out[1], A[0], B[2]);
  and and_15 (and_15_out[0], A[0], B[1]);
  and and_16 (product[0], A[0], B[0]);
endmodule

module full_sub (
  input  A,
  input  B,
  input  Carry_In,
  output sum_out,
  output carry_out
);

  wire and_1_out, and_2_out, not_1_out, not_2_out, xor_1_out;

  xor xor_1 (xor_1_out, A, B);
  not not_1 (not_1_out, A);
  and and_1 (and_1_out, not_1_out, B);
  xor xor_2 (sum_out, xor_1_out, Carry_In);
  not not_2 (not_2_out, xor_1_out);
  and and_2 (and_2_out, not_2_out, Carry_In);
  or or_1 (carry_out, and_2_out, and_1_out);
endmodule

module full_sub4 (
  input  [3:0] in_1,
  input  in_2,
  input  [3:0] in_3
);
endmodule

module mult_8 (
  input  [7:0] A,
  input  [7:0] B,
  output [15:0] product,
  output carry_out
);

  wire [3:0] undriven_2, undriven_3, undriven_5, undriven_6;
  wire [7:0] mult_4_1_product, mult_4_2_product, mult_4_3_product, mult_4_4_product, undriven, undriven_4;
  wire [15:0] add_16_1_sum_out, add_16_2_sum_out;

  // Probe on A
  // Probe on B[3:0]
  // Probe on B
  // Probe on A[3:0]
  // Probe on mult_4_1_product
  mult_4 mult_4_1 (.A(A[3:0]), .B(B[3:0]), .product(mult_4_1_product));
  mult_4 mult_4_2 (.A(A[3:0]), .B(B[7:4]), .product(mult_4_2_product));
  mult_4 mult_4_3 (.A(A[7:4]), .B(B[3:0]), .product(mult_4_3_product));
  mult_4 mult_4_4 (.A(A[7:4]), .B(B[7:4]), .product(mult_4_4_product));
  // Probe on mult_4_2_product
  // Probe on mult_4_3_product
  // Probe on mult_4_4_product
  add_16 add_16_1 (
    .A({undriven, mult_4_1_product}), .B({undriven_3, mult_4_2_product, undriven_2}),
    .Sum_out(add_16_1_sum_out));  // open: Carry_In, Carry_out
  add_16 add_16_2 (
    .A({undriven_6, mult_4_3_product, undriven_5}), .B({mult_4_4_product, undriven_4}),
    .Sum_out(add_16_2_sum_out));  // open: Carry_In, Carry_out
  // Probe on add_16_1_sum_out
  // Probe on add_16_2_sum_out
  add_16 add_16_3 (
    .A(add_16_1_sum_out), .B(add_16_2_sum_out), .Sum_out(product), .Carry_out(carry_out));  // open: Carry_In
  // Probe on product
endmodule

module Spliitter (
  input  [15:0] Instruction,
  input  WE,
  input  clk,
  output [4:0] Add_B,
  output [4:0] Add_A,
  output [4:0] opcode,
  output flag
);

  Register #(.width(16)) register_1 (
    .D(Instruction), .en(WE), .clk(clk), .Q({flag, opcode, Add_A, Add_B}));  // open: clr
endmodule

module decode (
  input  a_in,
  input  b_in,
  input  c_in,
  output o_1,
  output o_2,
  output o_3,
  output o_4,
  output o_5,
  output o_6,
  output o_7,
  output o_8
);

  wire not_1_out, not_2_out, not_3_out;

  not not_1 (not_1_out, c_in);
  not not_2 (not_2_out, b_in);
  not not_3 (not_3_out, a_in);
  and and_1 (o_1, not_3_out, not_2_out, not_1_out);
  and and_2 (o_2, not_3_out, not_2_out, c_in);
  and and_3 (o_3, not_3_out, b_in, not_1_out);
  and and_4 (o_4, not_3_out, b_in, c_in);
  and and_5 (o_5, a_in, not_2_out, not_1_out);
  and and_6 (o_6, a_in, not_2_out, c_in);
  and and_7 (o_7, a_in, b_in, not_1_out);
  and and_8 (o_8, a_in, b_in, c_in);

  // Notes on the sheet:
  //   B
  //   C
  //   A
  //   C'
  //   A'
  //   B'
  //   A'B'C'
  //   A'B'C
  //   A'BC'
  //   A'BC
  //   AB'C'
  //   AB'C
  //   ABC'
  //   ABC
endmodule

module memory (
  input  [4:0] Mem_Add,
  input  [4:0] in_2,
  input  WE,
  input  in_4,
  input  OE,
  input  in_6,
  input  Clk1,
  input  in_8,
  input  [15:0] Mem_In,
  input  [15:0] in_10,
  input  [4:0] in_11,
  input  [4:0] in_12,
  input  in_13,
  input  in_14,
  input  in_15,
  input  in_16,
  input  in_17,
  input  in_18,
  input  [15:0] in_19,
  input  [15:0] in_20,
  output [15:0] Mem_out,
  output [15:0] out_22,
  output [15:0] out_23,
  output [15:0] out_24
);

  RAM #(.addrWidth(5), .dataWidth(16)) ram_1 (
    .addr(Mem_Add), .we(WE), .oe(OE), .clk(Clk1), .din(Mem_In), .dout(Mem_out));
  RAM #(.addrWidth(5), .dataWidth(16)) ram_2 (
    .addr(in_11), .we(in_13), .oe(in_15), .clk(in_17), .din(in_19), .dout(out_23));
  RAM #(.addrWidth(5), .dataWidth(16)) ram_3 (
    .addr(in_2), .we(in_4), .oe(in_6), .clk(in_8), .din(in_10), .dout(out_22));
  RAM #(.addrWidth(5), .dataWidth(16)) ram_4 (
    .addr(in_12), .we(in_14), .oe(in_16), .clk(in_18), .din(in_20), .dout(out_24));
endmodule

module decoder_32 (
  input  Input_1,
  input  Input_2,
  input  Input_3,
  input  Input_4,
  input  Input_5,
  output out_0,
  output out_1,
  output out_2,
  output out_3,
  output out_4,
  output out_5,
  output out_6,
  output out_7,
  output out_8,
  output out_9,
  output out_10,
  output out_11,
  output out_12,
  output out_13,
  output out_14,
  output out_15,
  output out_16,
  output out_17,
  output out_18,
  output out_19,
  output out_20,
  output out_21,
  output out_22,
  output out_23,
  output out_24,
  output out_25,
  output out_26,
  output out_27,
  output out_28,
  output out_29,
  output out_30,
  output out_31
);

  wire not_1_out, not_2_out, not_3_out, not_4_out, not_5_out;

  not not_1 (not_1_out, Input_1);
  not not_2 (not_2_out, Input_2);
  not not_3 (not_3_out, Input_3);
  not not_4 (not_4_out, Input_4);
  not not_5 (not_5_out, Input_5);
  and and_1 (out_0, not_1_out, not_2_out, not_3_out, not_4_out, not_5_out);
  and and_2 (out_1, not_1_out, not_2_out, not_3_out, not_4_out, Input_5);
  and and_3 (out_2, not_1_out, not_2_out, not_3_out, Input_4, not_5_out);
  and and_4 (out_3, not_1_out, not_2_out, not_3_out, Input_4, Input_5);
  and and_5 (out_4, not_1_out, not_2_out, Input_3, not_4_out, not_5_out);
  and and_6 (out_5, not_1_out, not_2_out, Input_3, not_4_out, Input_5);
  and and_7 (out_6, not_1_out, not_2_out, Input_3, Input_4, not_5_out);
  and and_8 (out_7, not_1_out, not_2_out, Input_3, Input_4, Input_5);
  and and_9 (out_8, not_1_out, Input_2, not_3_out, not_4_out, not_5_out);
  and and_10 (out_9, not_1_out, Input_2, not_3_out, not_4_out, Input_5);
  and and_11 (out_10, not_1_out, Input_2, not_3_out, Input_4, not_5_out);
  and and_12 (out_11, not_1_out, Input_2, not_3_out, Input_4, Input_5);
  and and_13 (out_12, not_1_out, Input_2, Input_3, not_4_out, not_5_out);
  and and_14 (out_13, not_1_out, Input_2, Input_3, not_4_out, Input_5);
  and and_15 (out_14, not_1_out, Input_2, Input_3, Input_4, not_5_out);
  and and_16 (out_15, not_1_out, Input_2, Input_3, Input_4, Input_5);
  and and_17 (out_16, Input_1, not_2_out, not_3_out, not_4_out, not_5_out);
  and and_18 (out_17, Input_1, not_2_out, not_3_out, not_4_out, Input_5);
  and and_19 (out_18, Input_1, not_2_out, not_3_out, Input_4, not_5_out);
  and and_20 (out_19, Input_1, not_2_out, not_3_out, Input_4, Input_5);
  and and_21 (out_20, Input_1, not_2_out, Input_3, not_4_out, not_5_out);
  and and_22 (out_21, Input_1, not_2_out, Input_3, not_4_out, Input_5);
  and and_23 (out_22, Input_1, not_2_out, Input_3, Input_4, not_5_out);
  and and_24 (out_23, Input_1, not_2_out, Input_3, Input_4, Input_5);
  and and_25 (out_24, Input_1, Input_2, not_3_out, not_4_out, not_5_out);
  and and_26 (out_25, Input_1, Input_2, not_3_out, not_4_out, Input_5);
  and and_27 (out_26, Input_1, Input_2, not_3_out, Input_4, not_5_out);
  and and_28 (out_27, Input_1, Input_2, not_3_out, Input_4, Input_5);
  and and_29 (out_28, Input_1, Input_2, Input_3, not_4_out, not_5_out);
  and and_30 (out_29, Input_1, Input_2, Input_3, not_4_out, Input_5);
  and and_31 (out_30, Input_1, Input_2, Input_3, Input_4, not_5_out);
  and and_32 (out_31, Input_1, Input_2, Input_3, Input_4, Input_5);
endmodule

module temp (
  input  in_1,
  input  in_2,
  input  in_3,
  input  in_4,
  input  in_5,
  input  in_6,
  input  in_7,
  input  in_8,
  input  in_9,
  input  in_10,
  input  in_11,
  input  in_12,
  input  in_13,
  input  in_14,
  input  in_15,
  input  in_16,
  input  in_17,
  input  in_18,
  input  in_19,
  input  in_20,
  input  in_21,
  input  in_22,
  input  in_23,
  input  in_24,
  input  in_25,
  input  in_26,
  input  in_27,
  input  in_28
);

  wire clock_1_out;
  wire [4:0] register_5_q, register_10_q, register_11_q, spliitter_1_add_a, spliitter_1_add_b;
  wire [15:0] controlled_buffer_1_out, controlled_buffer_2_out, controlled_buffer_3_out, ram_1_dout,
       ram_2_dout, ram_4_dout, register_1_q, register_3_q, register_12_q, register_13_q, register_14_q;

  Register #(.width(16)) register_1 (
    .D(controlled_buffer_2_out), .en(in_25), .clk(clock_1_out), .Q(register_1_q));  // open: clr
  Register #(.width(16)) register_2 (
    .D(controlled_buffer_2_out), .en(in_24), .clk(clock_1_out), .Q(register_1_q));  // open: clr
  Register #(.width(16)) register_3 (
    .D(controlled_buffer_1_out), .en(in_23), .clk(clock_1_out), .Q(register_3_q));  // open: clr
  Register #(.width(16)) register_4 (
    .D(controlled_buffer_1_out), .en(in_22), .clk(clock_1_out), .Q(register_3_q));  // open: clr
  Register #(.width(5)) register_5 (.D({5{1'b0}}), .en(in_26), .clk(clock_1_out), .Q(register_5_q));  // open: clr
  Spliitter spliitter_1 (
    .Instruction(controlled_buffer_3_out), .WE(in_3), .clk(clock_1_out), .Add_B(spliitter_1_add_b),
    .Add_A(spliitter_1_add_a));  // open: opcode, flag
  Register #(.width(16)) register_6 (
    .D(controlled_buffer_2_out), .en(in_21), .clk(clock_1_out), .Q(register_1_q));  // open: clr
  Register #(.width(16)) register_7 (
    .D(controlled_buffer_2_out), .en(in_20), .clk(clock_1_out), .Q(register_1_q));  // open: clr
  Register #(.width(16)) register_8 (
    .D(controlled_buffer_1_out), .en(in_19), .clk(clock_1_out), .Q(register_3_q));  // open: clr
  Register #(.width(16)) register_9 (
    .D(controlled_buffer_1_out), .en(in_18), .clk(clock_1_out), .Q(register_3_q));  // open: clr
  Register #(.width(5)) register_10 (
    .D(spliitter_1_add_a), .en(in_27), .clk(clock_1_out), .Q(register_10_q));  // open: clr
  assign controlled_buffer_1_out = in_16 ? register_3_q : 16'bz;  // Controlled_Buffer controlled_buffer_1
  assign controlled_buffer_2_out = in_17 ? register_1_q : 16'bz;  // Controlled_Buffer controlled_buffer_2
  Register #(.width(5)) register_11 (
    .D(spliitter_1_add_b), .en(in_28), .clk(clock_1_out), .Q(register_11_q));  // open: clr
  Register #(.width(16)) register_12 (.D(ram_1_dout), .en(in_14), .clk(clock_1_out), .Q(register_12_q));  // open: clr
  Register #(.width(16)) register_13 (.D(ram_2_dout), .en(in_13), .clk(clock_1_out), .Q(register_13_q));  // open: clr
  Register #(.width(16)) register_14 (.D(ram_4_dout), .en(in_15), .clk(clock_1_out), .Q(register_14_q));  // open: clr
  Clock clock_1 (.out(clock_1_out));
  assign controlled_buffer_3_out = in_10 ? register_12_q : 16'bz;  // Controlled_Buffer controlled_buffer_3
  assign controlled_buffer_2_out = in_11 ? register_13_q : 16'bz;  // Controlled_Buffer controlled_buffer_4
  assign controlled_buffer_1_out = in_12 ? register_14_q : 16'bz;  // Controlled_Buffer controlled_buffer_5
  RAM #(.addrWidth(5), .dataWidth(16)) ram_1 (
    .addr(register_5_q), .we(in_1), .oe(in_2), .clk(clock_1_out), .din(controlled_buffer_3_out),
    .dout(ram_1_dout));
  RAM #(.addrWidth(5), .dataWidth(16)) ram_2 (
    .addr(register_10_q), .we(in_6), .oe(in_7), .clk(clock_1_out), .din(controlled_buffer_2_out),
    .dout(ram_2_dout));
  // Probe on ram_1_dout
  // Probe on ram_2_dout
  RAM #(.addrWidth(5), .dataWidth(16)) ram_3 (
    .addr(register_5_q), .we(in_8), .oe(in_9), .clk(clock_1_out), .din(controlled_buffer_3_out),
    .dout(ram_1_dout));
  RAM #(.addrWidth(5), .dataWidth(16)) ram_4 (
    .addr(register_11_q), .we(in_5), .oe(in_4), .clk(clock_1_out), .din(controlled_buffer_1_out),
    .dout(ram_4_dout));
  // Probe on ram_4_dout

  // Notes on the sheet:
  //   MAR_Zero
  //   MAR_A
  //   MAR_B
  //   MBR_A
  //   MBR_B
  //   MBR_Zero
endmodule

module mux_4by1 (
  input  input_1,
  input  input_2,
  input  input_3,
  input  input_4,
  output out_1
);

  wire and_1_out, and_2_out, and_3_out, and_4_out, not_1_out, not_2_out;

  not not_1 (not_1_out, 1'b0);
  not not_2 (not_2_out, 1'b0);
  and and_1 (and_1_out, input_1, not_1_out, not_2_out);
  and and_2 (and_2_out, input_2, not_1_out, 1'b0);
  and and_3 (and_3_out, input_3, 1'b0, not_2_out);
  and and_4 (and_4_out, input_4, 1'b0, 1'b0);
  or or_1 (out_1, and_1_out, and_2_out, and_3_out, and_4_out);
endmodule

module comparater_1bit (
  input  A,
  input  B,
  output A_Greater,
  output Equal,
  output A_lower
);

  wire nand_1_out, not_1_out, not_2_out;

  not not_1 (not_1_out, B);
  not not_2 (not_2_out, A);
  and and_1 (A_Greater, A, not_1_out);
  and and_2 (A_lower, not_2_out, B);
  nand nand_1 (nand_1_out, A_Greater, A_lower);
  LED led_1 (.in(nand_1_out));
  xnor xnor_1 (Equal, A_Greater, A_lower);
endmodule

module ram_data (
  input  RAM_A_WE,
  input  RAM_A_OE,
  input  RAM_B_OE,
  input  RAM_B_WE,
  input  Inst_RAM_OE,
  input  Inst_RAM_WE,
  input  system_RAM_OE,
  input  system_RAM_WE,
  input  MBR_B_WE,
  input  MBR_A_WE,
  input  MBR_Z_WE,
  input  inst_splitter_we,
  input  MBR_B_CB,
  input  MBR_A_CB,
  input  MBR_Z_CB,
  input  MAR_Z_WE,
  input  MAR_A_WE,
  input  MAR_B_WE,
  input  reg_8_we,
  input  reg_4_we,
  input  reg_2_we,
  input  reg_6_we,
  input  reg_7_we,
  input  reg_5_we,
  input  reg_3_we,
  input  reg_1_we,
  input  reg_a_out_cb,
  input  reg_b_out_cb,
  input  Alu_out_cb,
  input  counter_increment_by_1,
  input  counter_increment_on,
  input  counter_reset
);

  wire clock_1_out;
  wire [4:0] counter_1_q, register_5_q, register_10_q, register_11_q, spliitter_1_add_a, spliitter_1_add_b;
  wire [15:0] add_16_1_sum_out, controlled_buffer_1_out, controlled_buffer_5_out, controlled_buffer_9_out,
       ram_1_dout, ram_2_dout, ram_4_dout, register_1_q, register_2_q, register_3_q, register_4_q,
       register_6_q, register_12_q, register_13_q, register_14_q;

  Counter #(.max('h1f), .width(5)) counter_1 (
    .clr(counter_reset), .load(counter_increment_on), .up(counter_increment_by_1), .clk(clock_1_out),
    .Q(counter_1_q));  // open: count, D, carry
  // Probe on add_16_1_sum_out
  assign controlled_buffer_1_out = Alu_out_cb ? add_16_1_sum_out : 16'bz;  // Controlled_Buffer controlled_buffer_1
  add_16 add_16_1 (
    .A(controlled_buffer_5_out), .B(controlled_buffer_1_out), .Sum_out(add_16_1_sum_out));  // open: Carry_In, Carry_out
  Register #(.width(16)) register_1 (
    .D(controlled_buffer_5_out), .en(reg_1_we), .clk(clock_1_out), .Q(register_1_q));  // open: clr
  Register #(.width(16)) register_2 (
    .D(controlled_buffer_5_out), .en(reg_3_we), .clk(clock_1_out), .Q(register_2_q));  // open: clr
  Register #(.width(16)) register_3 (
    .D(controlled_buffer_1_out), .en(reg_5_we), .clk(clock_1_out), .Q(register_3_q));  // open: clr
  Register #(.width(16)) register_4 (
    .D(controlled_buffer_1_out), .en(reg_7_we), .clk(clock_1_out), .Q(register_4_q));  // open: clr
  Register #(.width(5)) register_5 (.D(counter_1_q), .en(MAR_Z_WE), .clk(clock_1_out), .Q(register_5_q));  // open: clr
  Spliitter spliitter_1 (
    .Instruction(controlled_buffer_9_out), .WE(inst_splitter_we), .clk(clock_1_out),
    .Add_B(spliitter_1_add_b), .Add_A(spliitter_1_add_a));  // open: opcode, flag
  // Probe on register_5_q
  Register #(.width(16)) register_6 (
    .D(controlled_buffer_1_out), .en(reg_6_we), .clk(clock_1_out), .Q(register_6_q));  // open: clr
  // Probe on spliitter_1_add_b
  // Probe on spliitter_1_add_a
  Controlled_Buffer #(.width(16)) controlled_buffer_2 (.in(register_1_q), .out(register_2_q));  // open: en
  Register #(.width(16)) register_7 (
    .D(controlled_buffer_5_out), .en(reg_2_we), .clk(clock_1_out), .Q(register_2_q));  // open: clr
  Register #(.width(16)) register_8 (
    .D(controlled_buffer_5_out), .en(reg_4_we), .clk(clock_1_out), .Q(register_2_q));  // open: clr
  Controlled_Buffer #(.width(16)) controlled_buffer_3 (.in(register_3_q), .out(register_4_q));  // open: en
  Register #(.width(16)) register_9 (
    .D(controlled_buffer_1_out), .en(reg_8_we), .clk(clock_1_out), .Q(register_4_q));  // open: clr
  Controlled_Buffer #(.width(16)) controlled_buffer_4 (.in(register_6_q), .out(register_4_q));  // open: en
  Register #(.width(5)) register_10 (
    .D(spliitter_1_add_a), .en(MAR_A_WE), .clk(clock_1_out), .Q(register_10_q));  // open: clr
  assign controlled_buffer_5_out = reg_a_out_cb ? register_2_q : 16'bz;  // Controlled_Buffer controlled_buffer_5
  assign controlled_buffer_1_out = reg_b_out_cb ? register_4_q : 16'bz;  // Controlled_Buffer controlled_buffer_6
  Clock clock_1 (.out(clock_1_out));
  Register #(.width(5)) register_11 (
    .D(spliitter_1_add_b), .en(MAR_B_WE), .clk(clock_1_out), .Q(register_11_q));  // open: clr
  Register #(.width(16)) register_12 (
    .D(ram_1_dout), .en(MBR_Z_WE), .clk(clock_1_out), .Q(register_12_q));  // open: clr
  Register #(.width(16)) register_13 (
    .D(ram_2_dout), .en(MBR_A_WE), .clk(clock_1_out), .Q(register_13_q));  // open: clr
  Register #(.width(16)) register_14 (
    .D(ram_4_dout), .en(MBR_B_WE), .clk(clock_1_out), .Q(register_14_q));  // open: clr
  assign controlled_buffer_5_out = MBR_A_CB ? register_13_q : 16'bz;  // Controlled_Buffer controlled_buffer_7
  assign controlled_buffer_1_out = MBR_B_CB ? register_14_q : 16'bz;  // Controlled_Buffer controlled_buffer_8
  assign controlled_buffer_9_out = MBR_Z_CB ? register_12_q : 16'bz;  // Controlled_Buffer controlled_buffer_9
  // Probe on register_5_q
  RAM #(.addrWidth(5), .dataWidth(16)) ram_1 (
    .addr(register_5_q), .we(Inst_RAM_WE), .oe(Inst_RAM_OE), .clk(clock_1_out),
    .din(controlled_buffer_9_out), .dout(ram_1_dout));
  // Probe on controlled_buffer_9_out
  RAM #(.addrWidth(5), .dataWidth(16)) ram_2 (
    .addr(register_10_q), .we(RAM_A_WE), .oe(RAM_A_OE), .clk(clock_1_out), .din(controlled_buffer_5_out),
    .dout(ram_2_dout));
  // Probe on ram_1_dout
  // Probe on ram_2_dout
  RAM #(.addrWidth(5), .dataWidth(16)) ram_3 (
    .addr(register_5_q), .we(system_RAM_WE), .oe(system_RAM_OE), .clk(clock_1_out),
    .din(controlled_buffer_9_out), .dout(ram_1_dout));
  RAM #(.addrWidth(5), .dataWidth(16)) ram_4 (
    .addr(register_11_q), .we(RAM_B_WE), .oe(RAM_B_OE), .clk(clock_1_out), .din(controlled_buffer_1_out),
    .dout(ram_4_dout));
  // Probe on ram_4_dout

  // Notes on the sheet:
  //   Reg 5
  //   Reg 7
  //   MAR_Zero
  //   Reg 1
  //   Reg 3
  //   Reg 2
  //   Reg 6
  //   MAR_A
  //   Reg 4
  //   Reg 8
  //   MAR_B
  //   MBR_B
  //   MBR_Z
  //   MBR_A
  //   RAM_A
  //   Instruction_Ram
  //   System_Ram
  //   RAM_B
endmodule

module mat_mult_rom (
  input  OE,
  input  [15:0] Register1,
  input  [15:0] Register5,
  input  [15:0] Register2,
  input  [15:0] Register7,
  input  [15:0] Register6,
  input  [15:0] Register8,
  input  [15:0] Register3,
  input  [15:0] Register4,
  output [15:0] out_10,
  output [15:0] out_11,
  output [15:0] out_12,
  output [15:0] out_13
);

  wire add_16_1_carry_out, add_16_2_carry_out, add_16_3_carry_out, add_16_4_carry_out;
  wire [7:0] bit_extender_1_out, bit_extender_2_out, bit_extender_3_out, bit_extender_4_out,
       bit_extender_5_out, bit_extender_6_out, bit_extender_7_out, bit_extender_8_out;
  wire [15:0] add_16_1_sum_out, add_16_2_sum_out, add_16_3_sum_out, add_16_4_sum_out, bit_extender_9_out,
       mult_8_1_product, mult_8_2_product, mult_8_3_product, mult_8_4_product, mult_8_5_product,
       mult_8_6_product, mult_8_7_product, mult_8_8_product;

  Bit_Extender #(.in_width(16), .out_width(8)) bit_extender_1 (.in(Register2), .out(bit_extender_1_out));
  Bit_Extender #(.in_width(16), .out_width(8)) bit_extender_2 (.in(Register7), .out(bit_extender_2_out));
  Bit_Extender #(.in_width(16), .out_width(8)) bit_extender_3 (.in(Register6), .out(bit_extender_3_out));
  Bit_Extender #(.in_width(16), .out_width(8)) bit_extender_4 (.in(Register8), .out(bit_extender_4_out));
  Bit_Extender #(.in_width(16), .out_width(8)) bit_extender_5 (.in(Register3), .out(bit_extender_5_out));
  Bit_Extender #(.in_width(16), .out_width(8)) bit_extender_6 (.in(Register4), .out(bit_extender_6_out));
  Bit_Extender #(.in_width(16), .out_width(8)) bit_extender_7 (.in(Register1), .out(bit_extender_7_out));
  Bit_Extender #(.in_width(16), .out_width(8)) bit_extender_8 (.in(Register5), .out(bit_extender_8_out));
  assign bit_extender_9_out = {{15{OE}}, OE};  // Bit_Extender bit_extender_9
  mult_8 mult_8_1 (.A(bit_extender_7_out), .B(bit_extender_8_out), .product(mult_8_1_product));  // open: carry_out
  mult_8 mult_8_2 (.A(bit_extender_1_out), .B(bit_extender_2_out), .product(mult_8_2_product));  // open: carry_out
  mult_8 mult_8_3 (.A(bit_extender_7_out), .B(bit_extender_3_out), .product(mult_8_3_product));  // open: carry_out
  mult_8 mult_8_4 (.A(bit_extender_1_out), .B(bit_extender_4_out), .product(mult_8_4_product));  // open: carry_out
  mult_8 mult_8_5 (.A(bit_extender_8_out), .B(bit_extender_5_out), .product(mult_8_5_product));  // open: carry_out
  mult_8 mult_8_6 (.A(bit_extender_2_out), .B(bit_extender_6_out), .product(mult_8_6_product));  // open: carry_out
  mult_8 mult_8_7 (.A(bit_extender_3_out), .B(bit_extender_5_out), .product(mult_8_7_product));  // open: carry_out
  mult_8 mult_8_8 (.A(bit_extender_4_out), .B(bit_extender_6_out), .product(mult_8_8_product));  // open: carry_out
  add_16 add_16_1 (
    .A(mult_8_1_product), .B(mult_8_2_product), .Sum_out(add_16_1_sum_out), .Carry_out(add_16_1_carry_out));  // open: Carry_In
  add_16 add_16_2 (
    .A(mult_8_3_product), .Carry_In(add_16_1_carry_out), .B(mult_8_4_product), .Sum_out(add_16_2_sum_out),
    .Carry_out(add_16_2_carry_out));
  add_16 add_16_3 (
    .A(mult_8_5_product), .Carry_In(add_16_2_carry_out), .B(mult_8_6_product), .Sum_out(add_16_3_sum_out),
    .Carry_out(add_16_3_carry_out));
  add_16 add_16_4 (
    .A(mult_8_7_product), .Carry_In(add_16_3_carry_out), .B(mult_8_8_product), .Sum_out(add_16_4_sum_out),
    .Carry_out(add_16_4_carry_out));
  assign out_10 = add_16_1_sum_out & bit_extender_9_out;  // AND_Gate and_1, 16 bits wide
  assign out_12 = add_16_3_sum_out & bit_extender_9_out;  // AND_Gate and_2, 16 bits wide
  assign out_13 = add_16_4_sum_out & bit_extender_9_out;  // AND_Gate and_3, 16 bits wide
  assign out_11 = add_16_2_sum_out & bit_extender_9_out;  // AND_Gate and_4, 16 bits wide
endmodule

module mux_8by1 (
  input  [2:0] control,
  input  input_1,
  input  input_2,
  input  input_3,
  input  input_4,
  input  input_5,
  input  input_6,
  input  input_7,
  input  input_8,
  output out_1
);

  wire and_1_out, and_2_out, and_3_out, and_4_out, and_5_out, and_6_out, and_7_out, and_8_out, not_1_out,
       not_2_out, not_3_out;

  not not_1 (not_1_out, control[0]);
  not not_2 (not_2_out, control[1]);
  not not_3 (not_3_out, control[2]);
  and and_1 (and_1_out, input_1, not_1_out, not_2_out, not_3_out);
  and and_2 (and_2_out, input_2, not_1_out, not_2_out, control[2]);
  and and_3 (and_3_out, input_3, not_1_out, control[1], not_3_out);
  and and_4 (and_4_out, input_4, not_1_out, control[1], control[2]);
  and and_5 (and_5_out, input_5, control[0], not_2_out, not_3_out);
  and and_6 (and_6_out, input_6, control[0], not_2_out, control[2]);
  and and_7 (and_7_out, input_7, control[0], control[1], not_3_out);
  and and_8 (and_8_out, input_8, control[0], control[1], control[2]);
  or or_1 (out_1, and_1_out, and_2_out, and_3_out, and_4_out, and_5_out, and_6_out, and_7_out, and_8_out);
endmodule

module comparater_2bits (
  input  [1:0] A,
  input  [1:0] B,
  output A_greater,
  output Equal,
  output A_lesser
);

  wire and_1_out, and_2_out, and_3_out, and_4_out, and_6_out, and_7_out, comparater_1bit_1_a_greater,
       comparater_1bit_1_a_lower, comparater_1bit_1_equal, comparater_1bit_2_a_greater,
       comparater_1bit_2_a_lower, comparater_1bit_2_equal, not_1_out, not_2_out, not_3_out, not_4_out;

  comparater_1bit comparater_1bit_1 (
    .A(A[0]), .B(B[0]), .A_Greater(comparater_1bit_1_a_greater), .Equal(comparater_1bit_1_equal),
    .A_lower(comparater_1bit_1_a_lower));
  comparater_1bit comparater_1bit_2 (
    .A(A[1]), .B(B[1]), .A_Greater(comparater_1bit_2_a_greater), .Equal(comparater_1bit_2_equal),
    .A_lower(comparater_1bit_2_a_lower));
  not not_1 (not_1_out, comparater_1bit_1_a_lower);
  not not_2 (not_2_out, comparater_1bit_1_a_greater);
  not not_3 (not_3_out, comparater_1bit_2_a_lower);
  not not_4 (not_4_out, comparater_1bit_2_a_greater);
  and and_1 (and_1_out, comparater_1bit_1_a_greater, not_1_out);
  and and_2 (and_2_out, not_2_out, comparater_1bit_1_a_lower);
  and and_3 (and_3_out, comparater_1bit_2_a_greater, not_3_out);
  and and_4 (and_4_out, not_4_out, comparater_1bit_2_a_lower);
  and and_5 (Equal, comparater_1bit_1_equal, comparater_1bit_2_equal);
  and and_6 (and_6_out, and_1_out, comparater_1bit_2_equal);
  and and_7 (and_7_out, and_2_out, comparater_1bit_2_equal);
  or or_1 (A_lesser, and_7_out, and_4_out);
  or or_2 (A_greater, and_6_out, and_3_out);
endmodule

module comparater_4bits (
  input  [3:0] A,
  input  [3:0] B,
  output A_greater,
  output Equal,
  output A_lesser
);

  wire and_1_out, and_2_out, and_3_out, and_4_out, and_6_out, and_7_out, comparater_2bits_1_a_greater,
       comparater_2bits_1_a_lesser, comparater_2bits_1_equal, comparater_2bits_2_a_greater,
       comparater_2bits_2_a_lesser, comparater_2bits_2_equal, not_1_out, not_2_out, not_3_out, not_4_out;

  comparater_2bits comparater_2bits_1 (
    .A(A[1:0]), .B(B[1:0]), .A_greater(comparater_2bits_1_a_greater), .Equal(comparater_2bits_1_equal),
    .A_lesser(comparater_2bits_1_a_lesser));
  comparater_2bits comparater_2bits_2 (
    .A(A[3:2]), .B(B[3:2]), .A_greater(comparater_2bits_2_a_greater), .Equal(comparater_2bits_2_equal),
    .A_lesser(comparater_2bits_2_a_lesser));
  not not_1 (not_1_out, comparater_2bits_1_a_lesser);
  not not_2 (not_2_out, comparater_2bits_1_a_greater);
  not not_3 (not_3_out, comparater_2bits_2_a_lesser);
  not not_4 (not_4_out, comparater_2bits_2_a_greater);
  and and_1 (and_1_out, comparater_2bits_1_a_greater, not_1_out);
  and and_2 (and_2_out, not_2_out, comparater_2bits_1_a_lesser);
  and and_3 (and_3_out, comparater_2bits_2_a_greater, not_3_out);
  and and_4 (and_4_out, not_4_out, comparater_2bits_2_a_lesser);
  and and_5 (Equal, comparater_2bits_1_equal, comparater_2bits_2_equal);
  and and_6 (and_6_out, and_1_out, comparater_2bits_2_equal);
  and and_7 (and_7_out, and_2_out, comparater_2bits_2_equal);
  or or_1 (A_lesser, and_7_out, and_4_out);
  or or_2 (A_greater, and_6_out, and_3_out);
endmodule

module comparater_8bits (
  input  [7:0] A,
  input  [7:0] B,
  output A_greater,
  output Equal,
  output A_lesser
);

  wire and_1_out, and_2_out, and_3_out, and_4_out, and_6_out, and_7_out, comparater_4bits_1_a_greater,
       comparater_4bits_1_a_lesser, comparater_4bits_1_equal, comparater_4bits_2_a_greater,
       comparater_4bits_2_a_lesser, comparater_4bits_2_equal, not_1_out, not_2_out, not_3_out, not_4_out;

  comparater_4bits comparater_4bits_1 (
    .A(A[3:0]), .B(B[3:0]), .A_greater(comparater_4bits_1_a_greater), .Equal(comparater_4bits_1_equal),
    .A_lesser(comparater_4bits_1_a_lesser));
  comparater_4bits comparater_4bits_2 (
    .A(A[7:4]), .B(B[7:4]), .A_greater(comparater_4bits_2_a_greater), .Equal(comparater_4bits_2_equal),
    .A_lesser(comparater_4bits_2_a_lesser));
  not not_1 (not_1_out, comparater_4bits_1_a_lesser);
  not not_2 (not_2_out, comparater_4bits_1_a_greater);
  not not_3 (not_3_out, comparater_4bits_2_a_lesser);
  not not_4 (not_4_out, comparater_4bits_2_a_greater);
  and and_1 (and_1_out, comparater_4bits_1_a_greater, not_1_out);
  and and_2 (and_2_out, not_2_out, comparater_4bits_1_a_lesser);
  and and_3 (and_3_out, comparater_4bits_2_a_greater, not_3_out);
  and and_4 (and_4_out, not_4_out, comparater_4bits_2_a_lesser);
  and and_5 (Equal, comparater_4bits_1_equal, comparater_4bits_2_equal);
  and and_6 (and_6_out, and_1_out, comparater_4bits_2_equal);
  and and_7 (and_7_out, and_2_out, comparater_4bits_2_equal);
  or or_1 (A_lesser, and_7_out, and_4_out);
  or or_2 (A_greater, and_6_out, and_3_out);
endmodule

module compararter_16bits (
  input  [15:0] A,
  input  [15:0] B,
  output [15:0] out_3
);

  wire and_1_out, and_2_out, and_3_out, and_4_out, and_6_out, and_7_out, comparater_8bits_1_a_greater,
       comparater_8bits_1_a_lesser, comparater_8bits_1_equal, comparater_8bits_2_a_greater,
       comparater_8bits_2_a_lesser, comparater_8bits_2_equal, not_1_out, not_2_out, not_3_out, not_4_out;

  comparater_8bits comparater_8bits_1 (
    .A(A[7:0]), .B(B[7:0]), .A_greater(comparater_8bits_1_a_greater), .Equal(comparater_8bits_1_equal),
    .A_lesser(comparater_8bits_1_a_lesser));
  comparater_8bits comparater_8bits_2 (
    .A(A[15:8]), .B(B[15:8]), .A_greater(comparater_8bits_2_a_greater), .Equal(comparater_8bits_2_equal),
    .A_lesser(comparater_8bits_2_a_lesser));
  not not_1 (not_1_out, comparater_8bits_1_a_lesser);
  not not_2 (not_2_out, comparater_8bits_1_a_greater);
  not not_3 (not_3_out, comparater_8bits_2_a_lesser);
  not not_4 (not_4_out, comparater_8bits_2_a_greater);
  and and_1 (and_1_out, comparater_8bits_1_a_greater, not_1_out);
  and and_2 (and_2_out, not_2_out, comparater_8bits_1_a_lesser);
  and and_3 (and_3_out, comparater_8bits_2_a_greater, not_3_out);
  and and_4 (and_4_out, not_4_out, comparater_8bits_2_a_lesser);
  and and_5 (out_3[1], comparater_8bits_1_equal, comparater_8bits_2_equal);
  and and_6 (and_6_out, and_1_out, comparater_8bits_2_equal);
  and and_7 (and_7_out, and_2_out, comparater_8bits_2_equal);
  or or_1 (out_3[2], and_7_out, and_4_out);
  or or_2 (out_3[0], and_6_out, and_3_out);

  assign out_3[15:3] = {13{1'b0}};

  // Notes on the sheet:
  //   a>b  = 1
  //   a=b =2
  //   a<b = 4
endmodule

module ALU (
  input  [4:0] opcode,
  input  [15:0] A,
  input  [15:0] B,
  output [15:0] result,
  output carry_out
);

  wire [7:0] bitselector_1_out, bitselector_2_out;
  wire [15:0] add_16_1_sum_out, and_1_out, compararter_16bits_1_out_3, mult_8_1_product, not_1_out,
       sub_16_1_sum_out, xor_1_out;

  // Probe on A
  // Probe on B
  BitSelector #(.group(8), .width(16)) bitselector_1 (.in(A), .out(bitselector_1_out), .sel(1'b0));
  BitSelector #(.group(8), .width(16)) bitselector_2 (.in(B), .out(bitselector_2_out), .sel(1'b0));
  assign and_1_out = A & B;  // AND_Gate and_1, 16 bits wide
  assign xor_1_out = A ^ B;  // XOR_Gate xor_1, 16 bits wide
  assign not_1_out = ~A;  // NOT_Gate not_1, 16 bits wide
  compararter_16bits compararter_16bits_1 (.A(A), .B(B), .out_3(compararter_16bits_1_out_3));
  add_16 add_16_1 (.A(A), .Carry_In(1'b0), .B(B), .Sum_out(add_16_1_sum_out), .Carry_out(carry_out));
  sub_16 sub_16_1 (.A(A), .B(B), .sum_out(sub_16_1_sum_out));
  mult_8 mult_8_1 (.A(bitselector_1_out), .B(bitselector_2_out), .product(mult_8_1_product));  // open: carry_out
  // Probe on result
  final_mux32 final_mux32_1 (
    .opcode(opcode), .add_00001(add_16_1_sum_out), .mult_00011(mult_8_1_product),
    .comp_01010(compararter_16bits_1_out_3), .and_01011(and_1_out), .xor_01100(xor_1_out),
    .not_01101(not_1_out), .sub_10001(sub_16_1_sum_out), .out_34(result));  // open: op_00000, op_00010, op_00100, op_00101, op_00110, op_00111, op_01000, op_01001, op_01110, op_01111, op_10000, op_10010, op_10011, op_10100, op_10101, op_10110, op_10111, op_11000, op_11001, op_11010, op_11011, op_11100, op_11101, op_11110, op_11111
endmodule

module attempot_uno (
  input  RAM_A_WE,
  input  RAM_A_OE,
  input  RAM_B_OE,
  input  RAM_B_WE,
  input  Inst_RAM_OE,
  input  Inst_RAM_WE,
  input  system_RAM_OE,
  input  system_RAM_WE,
  input  MBR_B_WE,
  input  MBR_A_WE,
  input  MBR_Z_WE,
  input  inst_splitter_we,
  input  MBR_B_CB,
  input  MBR_A_CB,
  input  MBR_Z_CB,
  input  MAR_Z_WE,
  input  in_17,
  input  MAR_A_WE,
  input  MAR_B_WE,
  input  reg_8_we,
  input  reg_4_we,
  input  reg_2_we,
  input  reg_6_we,
  input  reg_7_we,
  input  reg_5_we,
  input  reg_3_we,
  input  reg_1_we,
  input  reg_a_out_cb,
  input  reg_b_out_cb,
  input  Alu_out_cb,
  input  counter_increment_by_1,
  input  counter_increment_on,
  input  counter_reset,
  input  opcode_reg_we,
  input  opcode_init_cb,
  input  reg1_cb,
  input  reg5_cb,
  input  reg7_cb,
  output out_39
);

  wire clock_1_out;
  wire [4:0] controlled_buffer_1_out, counter_1_q, register_6_q, register_11_q, register_12_q,
       spliitter_1_add_a, spliitter_1_add_b;
  wire [4:4] register_1_q_2;
  wire [7:0] register_1_q;
  wire [15:0] add_16_1_sum_out, controlled_buffer_2_out, controlled_buffer_6_out, controlled_buffer_8_out,
       ram_1_dout, ram_2_dout, ram_4_dout, register_2_q, register_3_q, register_4_q, register_5_q,
       register_7_q, register_13_q, register_14_q, register_15_q;
  wire [31:0] rom_1_data, rom_2_data;

  Counter #(.max('h1f), .width(5)) counter_1 (
    .clr(rom_1_data[31]), .load(rom_1_data[30]), .up(rom_1_data[29]), .clk(clock_1_out), .Q(counter_1_q));  // open: count, D, carry
  Register #(.width(5)) register_1 (
    .D(controlled_buffer_1_out), .en(rom_2_data[0]), .clk(clock_1_out),
    .Q({register_1_q_2[4], register_1_q[3:0]}));  // open: clr
  assign controlled_buffer_1_out = rom_2_data[1] ? {5{1'b0}} : 5'bz;  // Controlled_Buffer controlled_buffer_1
  // Probe on add_16_1_sum_out
  assign controlled_buffer_2_out = rom_1_data[28] ? add_16_1_sum_out : 16'bz;  // Controlled_Buffer controlled_buffer_2
  add_16 add_16_1 (
    .A(controlled_buffer_6_out), .B(controlled_buffer_2_out), .Sum_out(add_16_1_sum_out));  // open: Carry_In, Carry_out
  Register #(.width(16)) register_2 (
    .D(controlled_buffer_6_out), .en(rom_1_data[25]), .clk(clock_1_out), .Q(register_2_q));  // open: clr
  Register #(.width(16)) register_3 (
    .D(controlled_buffer_6_out), .en(rom_1_data[24]), .clk(clock_1_out), .Q(register_3_q));  // open: clr
  Register #(.width(16)) register_4 (
    .D(controlled_buffer_2_out), .en(rom_1_data[23]), .clk(clock_1_out), .Q(register_4_q));  // open: clr
  Register #(.width(16)) register_5 (
    .D(controlled_buffer_2_out), .en(rom_1_data[22]), .clk(clock_1_out), .Q(register_5_q));  // open: clr
  Register #(.width(5)) register_6 (
    .D(counter_1_q), .en(rom_1_data[15]), .clk(clock_1_out), .Q(register_6_q));  // open: clr
  Spliitter spliitter_1 (
    .Instruction(controlled_buffer_8_out), .WE(rom_1_data[11]), .clk(clock_1_out), .Add_B(spliitter_1_add_b),
    .Add_A(spliitter_1_add_a), .opcode(controlled_buffer_1_out));  // open: flag
  // Probe on register_6_q
  // Probe on spliitter_1_add_b
  Register #(.width(16)) register_7 (
    .D(controlled_buffer_2_out), .en(rom_1_data[21]), .clk(clock_1_out), .Q(register_7_q));  // open: clr
  // Probe on spliitter_1_add_a
  assign register_3_q = rom_2_data[2] ? register_2_q : 16'bz;  // Controlled_Buffer controlled_buffer_3
  Register #(.width(16)) register_8 (
    .D(controlled_buffer_6_out), .en(rom_1_data[20]), .clk(clock_1_out), .Q(register_3_q));  // open: clr
  Register #(.width(16)) register_9 (
    .D(controlled_buffer_6_out), .en(rom_1_data[19]), .clk(clock_1_out), .Q(register_3_q));  // open: clr
  assign register_5_q = rom_2_data[3] ? register_4_q : 16'bz;  // Controlled_Buffer controlled_buffer_4
  Register #(.width(16)) register_10 (
    .D(controlled_buffer_2_out), .en(rom_1_data[18]), .clk(clock_1_out), .Q(register_5_q));  // open: clr
  Register #(.width(5)) register_11 (
    .D(spliitter_1_add_a), .en(rom_1_data[16]), .clk(clock_1_out), .Q(register_11_q));  // open: clr
  assign register_5_q = rom_2_data[4] ? register_7_q : 16'bz;  // Controlled_Buffer controlled_buffer_5
  assign controlled_buffer_6_out = rom_1_data[26] ? register_3_q : 16'bz;  // Controlled_Buffer controlled_buffer_6
  assign controlled_buffer_2_out = rom_1_data[27] ? register_5_q : 16'bz;  // Controlled_Buffer controlled_buffer_7
  Register #(.width(5)) register_12 (
    .D(spliitter_1_add_b), .en(rom_1_data[17]), .clk(clock_1_out), .Q(register_12_q));  // open: clr
  Clock clock_1 (.out(clock_1_out));
  Register #(.width(16)) register_13 (
    .D(ram_1_dout), .en(rom_1_data[10]), .clk(clock_1_out), .Q(register_13_q));  // open: clr
  Register #(.width(16)) register_14 (
    .D(ram_2_dout), .en(rom_1_data[9]), .clk(clock_1_out), .Q(register_14_q));  // open: clr
  Register #(.width(16)) register_15 (
    .D(ram_4_dout), .en(rom_1_data[8]), .clk(clock_1_out), .Q(register_15_q));  // open: clr
  assign controlled_buffer_8_out = rom_1_data[14] ? register_13_q : 16'bz;  // Controlled_Buffer controlled_buffer_8
  assign controlled_buffer_6_out = rom_1_data[13] ? register_14_q : 16'bz;  // Controlled_Buffer controlled_buffer_9
  assign controlled_buffer_2_out = rom_1_data[12] ? register_15_q : 16'bz;  // Controlled_Buffer controlled_buffer_10
  // Probe on register_6_q
  // Probe on controlled_buffer_8_out
  RAM #(.addrWidth(5), .dataWidth(16)) ram_1 (
    .addr(register_6_q), .we(rom_1_data[5]), .oe(rom_1_data[4]), .clk(clock_1_out),
    .din(controlled_buffer_8_out), .dout(ram_1_dout));
  RAM #(.addrWidth(5), .dataWidth(16)) ram_2 (
    .addr(register_11_q), .we(rom_1_data[0]), .oe(rom_1_data[1]), .clk(clock_1_out),
    .din(controlled_buffer_6_out), .dout(ram_2_dout));
  // Probe on ram_1_dout
  // Probe on ram_2_dout
  RAM #(.addrWidth(5), .dataWidth(16)) ram_3 (
    .addr(register_6_q), .we(rom_1_data[7]), .oe(rom_1_data[6]), .clk(clock_1_out),
    .din(controlled_buffer_8_out), .dout(ram_1_dout));
  RAM #(.addrWidth(5), .dataWidth(16)) ram_4 (
    .addr(register_12_q), .we(rom_1_data[3]), .oe(rom_1_data[2]), .clk(clock_1_out),
    .din(controlled_buffer_2_out), .dout(ram_4_dout));
  // Probe on ram_4_dout
  ROM #(.dataWidth(32)) rom_1 (.addr(register_1_q), .data(rom_1_data));
  ROM #(.dataWidth(32)) rom_2 (.addr(register_1_q), .data(rom_2_data));
  Counter #(.max('hf), .width(4)) counter_2 (
    .up(1'b0), .count(1'b0), .clk(clock_1_out), .Q(register_1_q[7:4]));  // open: clr, load, D, carry

  // Notes on the sheet:
  //   Reg 5
  //   Reg 7
  //   MAR_Zero
  //   Reg 1
  //   Reg 3
  //   Reg 2
  //   Reg 6
  //   MAR_A
  //   Reg 4
  //   Reg 8
  //   MAR_B
  //   MBR_A
  //   MBR_B
  //   MBR_Z
  //   RAM_A
  //   Instruction_Ram
  //   RAM_B
  //   System_Ram
  //   contents of rom_1 (hex, n*v repeats v):
  //   8210004 8230004 68f3c004 8d2c144 d2f000 60c00030 60cc0004 1c0004 c2044 15 1a
endmodule

module attempt_des (
  input  RAM_A_WE,
  input  RAM_A_OE,
  input  RAM_B_OE,
  input  RAM_B_WE,
  input  Inst_RAM_OE,
  input  Inst_RAM_WE,
  input  system_RAM_OE,
  input  system_RAM_WE,
  input  MBR_B_WE,
  input  MBR_A_WE,
  input  MBR_Z_WE,
  input  inst_splitter_we,
  input  MBR_B_CB,
  input  MBR_A_CB,
  input  MBR_Z_CB,
  input  MAR_Z_WE,
  input  MAR_A_WE,
  input  MAR_B_WE,
  input  reg_8_we,
  input  reg_4_we,
  input  reg_2_we,
  input  reg_6_we,
  input  reg_7_we,
  input  reg_5_we,
  input  reg_3_we,
  input  reg_1_we,
  input  reg_a_out_cb,
  input  reg_b_out_cb,
  input  Alu_out_cb,
  input  counter_increment_by_1,
  input  counter_increment_on,
  input  counter_reset
);

  wire clock_1_out;
  wire [4:0] counter_1_q, register_6_q, register_11_q, register_12_q, spliitter_1_add_a, spliitter_1_add_b;
  wire [4:4] register_1_q_2;
  wire [7:0] register_1_q;
  wire [15:0] add_16_1_sum_out, controlled_buffer_1_out, controlled_buffer_2_out, controlled_buffer_4_out,
       ram_1_dout, ram_2_dout, ram_4_dout, register_2_q, register_4_q, register_13_q, register_14_q,
       register_15_q;
  wire [31:0] rom_1_data;

  ALU alu_1 ();  // open: opcode, A, B, result, carry_out
  Counter #(.max('h1f), .width(5)) counter_1 (
    .clr(rom_1_data[31]), .load(rom_1_data[30]), .up(rom_1_data[29]), .clk(clock_1_out), .Q(counter_1_q));  // open: count, D, carry
  Register #(.width(5)) register_1 (.clk(clock_1_out), .Q({register_1_q_2[4], register_1_q[3:0]}));  // open: D, en, clr
  // Probe on add_16_1_sum_out
  assign controlled_buffer_1_out = rom_1_data[28] ? add_16_1_sum_out : 16'bz;  // Controlled_Buffer controlled_buffer_1
  add_16 add_16_1 (
    .A(controlled_buffer_2_out), .B(controlled_buffer_1_out), .Sum_out(add_16_1_sum_out));  // open: Carry_In, Carry_out
  Register #(.width(16)) register_2 (
    .D(controlled_buffer_2_out), .en(rom_1_data[25]), .clk(clock_1_out), .Q(register_2_q));  // open: clr
  Register #(.width(16)) register_3 (
    .D(controlled_buffer_2_out), .en(rom_1_data[24]), .clk(clock_1_out), .Q(register_2_q));  // open: clr
  Register #(.width(16)) register_4 (
    .D(controlled_buffer_1_out), .en(rom_1_data[23]), .clk(clock_1_out), .Q(register_4_q));  // open: clr
  Register #(.width(16)) register_5 (
    .D(controlled_buffer_1_out), .en(rom_1_data[22]), .clk(clock_1_out), .Q(register_4_q));  // open: clr
  Register #(.width(5)) register_6 (
    .D(counter_1_q), .en(rom_1_data[15]), .clk(clock_1_out), .Q(register_6_q));  // open: clr
  Spliitter spliitter_1 (
    .Instruction(controlled_buffer_4_out), .WE(rom_1_data[11]), .clk(clock_1_out), .Add_B(spliitter_1_add_b),
    .Add_A(spliitter_1_add_a));  // open: opcode, flag
  // Probe on register_6_q
  // Probe on spliitter_1_add_b
  Register #(.width(16)) register_7 (
    .D(controlled_buffer_1_out), .en(rom_1_data[21]), .clk(clock_1_out), .Q(register_4_q));  // open: clr
  // Probe on spliitter_1_add_a
  Register #(.width(16)) register_8 (
    .D(controlled_buffer_2_out), .en(rom_1_data[20]), .clk(clock_1_out), .Q(register_2_q));  // open: clr
  Register #(.width(16)) register_9 (
    .D(controlled_buffer_2_out), .en(rom_1_data[19]), .clk(clock_1_out), .Q(register_2_q));  // open: clr
  Register #(.width(16)) register_10 (
    .D(controlled_buffer_1_out), .en(rom_1_data[18]), .clk(clock_1_out), .Q(register_4_q));  // open: clr
  Register #(.width(5)) register_11 (
    .D(spliitter_1_add_a), .en(rom_1_data[16]), .clk(clock_1_out), .Q(register_11_q));  // open: clr
  assign controlled_buffer_2_out = rom_1_data[26] ? register_2_q : 16'bz;  // Controlled_Buffer controlled_buffer_2
  assign controlled_buffer_1_out = rom_1_data[27] ? register_4_q : 16'bz;  // Controlled_Buffer controlled_buffer_3
  Register #(.width(5)) register_12 (
    .D(spliitter_1_add_b), .en(rom_1_data[17]), .clk(clock_1_out), .Q(register_12_q));  // open: clr
  Clock clock_1 (.out(clock_1_out));
  Register #(.width(16)) register_13 (
    .D(ram_1_dout), .en(rom_1_data[10]), .clk(clock_1_out), .Q(register_13_q));  // open: clr
  Register #(.width(16)) register_14 (
    .D(ram_2_dout), .en(rom_1_data[9]), .clk(clock_1_out), .Q(register_14_q));  // open: clr
  Register #(.width(16)) register_15 (
    .D(ram_4_dout), .en(rom_1_data[8]), .clk(clock_1_out), .Q(register_15_q));  // open: clr
  assign controlled_buffer_4_out = rom_1_data[14] ? register_13_q : 16'bz;  // Controlled_Buffer controlled_buffer_4
  assign controlled_buffer_2_out = rom_1_data[13] ? register_14_q : 16'bz;  // Controlled_Buffer controlled_buffer_5
  assign controlled_buffer_1_out = rom_1_data[12] ? register_15_q : 16'bz;  // Controlled_Buffer controlled_buffer_6
  // Probe on register_6_q
  // Probe on controlled_buffer_4_out
  RAM #(.addrWidth(5), .dataWidth(16)) ram_1 (
    .addr(register_6_q), .we(rom_1_data[5]), .oe(rom_1_data[4]), .clk(clock_1_out),
    .din(controlled_buffer_4_out), .dout(ram_1_dout));
  RAM #(.addrWidth(5), .dataWidth(16)) ram_2 (
    .addr(register_11_q), .we(rom_1_data[0]), .oe(rom_1_data[1]), .clk(clock_1_out),
    .din(controlled_buffer_2_out), .dout(ram_2_dout));
  // Probe on ram_1_dout
  // Probe on ram_2_dout
  RAM #(.addrWidth(5), .dataWidth(16)) ram_3 (
    .addr(register_6_q), .we(rom_1_data[7]), .oe(rom_1_data[6]), .clk(clock_1_out),
    .din(controlled_buffer_4_out), .dout(ram_1_dout));
  RAM #(.addrWidth(5), .dataWidth(16)) ram_4 (
    .addr(register_12_q), .we(rom_1_data[3]), .oe(rom_1_data[2]), .clk(clock_1_out),
    .din(controlled_buffer_1_out), .dout(ram_4_dout));
  // Probe on ram_4_dout
  ROM #(.dataWidth(32)) rom_1 (.addr(register_1_q), .data(rom_1_data));
  Counter #(.max('hf), .width(4)) counter_2 (
    .up(1'b0), .count(1'b0), .clk(clock_1_out), .Q(register_1_q[7:4]));  // open: clr, load, D, carry

  // Notes on the sheet:
  //   Reg 5
  //   Reg 7
  //   MAR_Zero
  //   Reg 1
  //   Reg 3
  //   Reg 2
  //   Reg 6
  //   MAR_A
  //   Reg 4
  //   Reg 8
  //   MAR_B
  //   MBR_A
  //   MBR_B
  //   MBR_Z
  //   RAM_A
  //   Instruction_Ram
  //   RAM_B
  //   System_Ram
  //   contents of rom_1 (hex, n*v repeats v):
  //   8210004 8230004 68f3c004 8d2c144 d2f000 60c00030 60cc0004 1c0004 c2044 15 1a
endmodule

module attempt_tres (
  input  RAM_A_WE,
  input  RAM_A_OE,
  input  RAM_B_OE,
  input  RAM_B_WE,
  input  Inst_RAM_OE,
  input  Inst_RAM_WE,
  input  system_RAM_OE,
  input  system_RAM_WE,
  input  MBR_B_WE,
  input  MBR_A_WE,
  input  MBR_Z_WE,
  input  inst_splitter_we,
  input  MBR_B_CB,
  input  MBR_A_CB,
  input  MBR_Z_CB,
  input  MAR_Z_WE,
  input  MAR_A_WE,
  input  MAR_B_WE,
  input  reg_8_we,
  input  reg_4_we,
  input  reg_2_we,
  input  reg_6_we,
  input  reg_7_we,
  input  reg_5_we,
  input  reg_3_we,
  input  reg_1_we,
  input  reg_a_out_cb,
  input  reg_b_out_cb,
  input  Alu_out_cb,
  input  counter_increment_by_1,
  input  counter_increment_on,
  input  counter_reset,
  input  opcode_reg_we,
  input  opcode_init_cb,
  input  reg1_cb,
  input  reg5_cb,
  input  reg7_cb
);

  wire clock_1_out;
  wire [4:0] controlled_buffer_1_out, counter_1_q, register_8_q, register_13_q, register_14_q,
       spliitter_1_add_a, spliitter_1_add_b;
  wire [4:4] register_1_q_2;
  wire [7:0] register_1_q;
  wire [15:0] alu_1_result, controlled_buffer_2_out, controlled_buffer_6_out, controlled_buffer_10_out,
       ram_1_dout, ram_2_dout, ram_4_dout, register_4_q, register_5_q, register_6_q, register_7_q,
       register_9_q, register_15_q, register_16_q, register_17_q;
  wire [47:0] rom_1_data;

  Counter #(.max('h1f), .width(5)) counter_1 (
    .clr(rom_1_data[16]), .load(rom_1_data[17]), .up(rom_1_data[18]), .clk(clock_1_out), .Q(counter_1_q));  // open: count, D, carry
  Register #(.width(5)) register_1 (
    .D(controlled_buffer_1_out), .en(rom_1_data[15]), .clk(clock_1_out),
    .Q({register_1_q_2[4], register_1_q[3:0]}));  // open: clr
  Register register_2 ();  // open: D, en, clk, Q, clr
  Register register_3 ();  // open: D, en, clk, Q, clr
  assign controlled_buffer_1_out = rom_1_data[14] ? {5{1'b0}} : 5'bz;  // Controlled_Buffer controlled_buffer_1
  // Probe on alu_1_result
  assign controlled_buffer_2_out = rom_1_data[19] ? alu_1_result : 16'bz;  // Controlled_Buffer controlled_buffer_2
  ALU alu_1 (
    .A(controlled_buffer_6_out), .B(controlled_buffer_2_out), .result(alu_1_result));  // open: opcode, carry_out
  Register #(.width(16)) register_4 (
    .D(controlled_buffer_6_out), .en(rom_1_data[22]), .clk(clock_1_out), .Q(register_4_q));  // open: clr
  Register #(.width(16)) register_5 (
    .D(controlled_buffer_6_out), .en(rom_1_data[23]), .clk(clock_1_out), .Q(register_5_q));  // open: clr
  Register #(.width(16)) register_6 (
    .D(controlled_buffer_2_out), .en(rom_1_data[24]), .clk(clock_1_out), .Q(register_6_q));  // open: clr
  Register #(.width(16)) register_7 (
    .D(controlled_buffer_2_out), .en(rom_1_data[25]), .clk(clock_1_out), .Q(register_7_q));  // open: clr
  Register #(.width(5)) register_8 (
    .D(counter_1_q), .en(rom_1_data[32]), .clk(clock_1_out), .Q(register_8_q));  // open: clr
  Spliitter spliitter_1 (
    .Instruction(controlled_buffer_10_out), .WE(rom_1_data[36]), .clk(clock_1_out),
    .Add_B(spliitter_1_add_b), .Add_A(spliitter_1_add_a), .opcode(controlled_buffer_1_out));  // open: flag
  // Probe on register_8_q
  Register #(.width(16)) register_9 (
    .D(controlled_buffer_2_out), .en(rom_1_data[26]), .clk(clock_1_out), .Q(register_9_q));  // open: clr
  // Probe on spliitter_1_add_b
  // Probe on spliitter_1_add_a
  assign register_5_q = rom_1_data[13] ? register_4_q : 16'bz;  // Controlled_Buffer controlled_buffer_3
  Register #(.width(16)) register_10 (
    .D(controlled_buffer_6_out), .en(rom_1_data[27]), .clk(clock_1_out), .Q(register_5_q));  // open: clr
  Register #(.width(16)) register_11 (
    .D(controlled_buffer_6_out), .en(rom_1_data[28]), .clk(clock_1_out), .Q(register_5_q));  // open: clr
  assign register_7_q = rom_1_data[12] ? register_6_q : 16'bz;  // Controlled_Buffer controlled_buffer_4
  Register #(.width(16)) register_12 (
    .D(controlled_buffer_2_out), .en(rom_1_data[29]), .clk(clock_1_out), .Q(register_7_q));  // open: clr
  assign register_7_q = rom_1_data[11] ? register_9_q : 16'bz;  // Controlled_Buffer controlled_buffer_5
  Register #(.width(5)) register_13 (
    .D(spliitter_1_add_a), .en(rom_1_data[31]), .clk(clock_1_out), .Q(register_13_q));  // open: clr
  assign controlled_buffer_6_out = rom_1_data[21] ? register_5_q : 16'bz;  // Controlled_Buffer controlled_buffer_6
  assign controlled_buffer_2_out = rom_1_data[20] ? register_7_q : 16'bz;  // Controlled_Buffer controlled_buffer_7
  Clock clock_1 (.out(clock_1_out));
  Register #(.width(5)) register_14 (
    .D(spliitter_1_add_b), .en(rom_1_data[30]), .clk(clock_1_out), .Q(register_14_q));  // open: clr
  Register #(.width(16)) register_15 (
    .D(ram_1_dout), .en(rom_1_data[37]), .clk(clock_1_out), .Q(register_15_q));  // open: clr
  Register #(.width(16)) register_16 (
    .D(ram_2_dout), .en(rom_1_data[38]), .clk(clock_1_out), .Q(register_16_q));  // open: clr
  Register #(.width(16)) register_17 (
    .D(ram_4_dout), .en(rom_1_data[39]), .clk(clock_1_out), .Q(register_17_q));  // open: clr
  assign controlled_buffer_6_out = rom_1_data[34] ? register_16_q : 16'bz;  // Controlled_Buffer controlled_buffer_8
  assign controlled_buffer_2_out = rom_1_data[35] ? register_17_q : 16'bz;  // Controlled_Buffer controlled_buffer_9
  assign controlled_buffer_10_out = rom_1_data[33] ? register_15_q : 16'bz;  // Controlled_Buffer controlled_buffer_10
  // Probe on register_8_q
  RAM #(.addrWidth(5), .dataWidth(16)) ram_1 (
    .addr(register_8_q), .we(rom_1_data[42]), .oe(rom_1_data[43]), .clk(clock_1_out),
    .din(controlled_buffer_10_out), .dout(ram_1_dout));
  // Probe on controlled_buffer_10_out
  RAM #(.addrWidth(5), .dataWidth(16)) ram_2 (
    .addr(register_13_q), .we(rom_1_data[47]), .oe(rom_1_data[46]), .clk(clock_1_out),
    .din(controlled_buffer_6_out), .dout(ram_2_dout));
  // Probe on ram_1_dout
  // Probe on ram_2_dout
  RAM #(.addrWidth(5), .dataWidth(16)) ram_3 (
    .addr(register_8_q), .we(rom_1_data[40]), .oe(rom_1_data[41]), .clk(clock_1_out),
    .din(controlled_buffer_10_out), .dout(ram_1_dout));
  RAM #(.addrWidth(5), .dataWidth(16)) ram_4 (
    .addr(register_14_q), .we(rom_1_data[44]), .oe(rom_1_data[45]), .clk(clock_1_out),
    .din(controlled_buffer_2_out), .dout(ram_4_dout));
  // Probe on ram_4_dout
  ROM #(.dataWidth(48)) rom_1 (.addr(register_1_q), .data(rom_1_data));
  Counter #(.max('hf), .width(4)) counter_2 (
    .up(1'b1), .count(1'b1), .clk(clock_1_out), .Q(register_1_q[7:4]));  // open: clr, load, D, carry

  // Notes on the sheet:
  //   Reg 5
  //   Reg 7
  //   MAR_Zero
  //   Reg 1
  //   Reg 3
  //   Reg 2
  //   Reg 6
  //   MAR_A
  //   Reg 4
  //   Reg 8
  //   MAR_B
  //   MBR_B
  //   MBR_Z
  //   MBR_A
  //   RAM_A
  //   Instruction_Ram
  //   System_Ram
  //   RAM_B
  //   zero pehle 
  //   8400800000
  //   8000E00000
  //   600000
  //   881800000000
  //   7800000000
  //   60FF000000
  //   20400120000
endmodule

module mux_5by32 (
  input  [4:0] in_1,
  input  [15:0] in_2,
  input  [15:0] in_3,
  input  [15:0] in_4,
  input  [15:0] in_5,
  input  [15:0] in_6,
  output [15:0] out_7
);

  wire [15:0] and_1_out, and_2_out, and_3_out, and_4_out, and_5_out, and_6_out, and_7_out, and_8_out,
       and_9_out, and_10_out, and_11_out, and_12_out, and_13_out, and_14_out, and_15_out, and_16_out,
       and_17_out, and_18_out, and_19_out, and_20_out, and_21_out, and_22_out, and_23_out, and_24_out,
       and_25_out, and_26_out, and_27_out, and_28_out, and_29_out, and_30_out, and_31_out, and_32_out,
       bit_extender_1_out, bit_extender_2_out, bit_extender_3_out, bit_extender_4_out, bit_extender_5_out,
       not_1_out, not_2_out, not_3_out, not_4_out, not_5_out, undriven, undriven_2, undriven_3, undriven_4,
       undriven_5, undriven_6, undriven_7, undriven_8, undriven_9, undriven_10, undriven_11, undriven_12,
       undriven_13, undriven_14, undriven_15, undriven_16, undriven_17, undriven_18, undriven_19,
       undriven_20, undriven_21, undriven_22, undriven_23, undriven_24, undriven_25, undriven_26,
       undriven_27, undriven_28, undriven_29;

  assign bit_extender_1_out = {{15{in_1[0]}}, in_1[0]};  // Bit_Extender bit_extender_1
  assign bit_extender_2_out = {{15{in_1[1]}}, in_1[1]};  // Bit_Extender bit_extender_2
  assign bit_extender_3_out = {{15{in_1[2]}}, in_1[2]};  // Bit_Extender bit_extender_3
  assign bit_extender_4_out = {{15{in_1[3]}}, in_1[3]};  // Bit_Extender bit_extender_4
  assign bit_extender_5_out = {{15{in_1[4]}}, in_1[4]};  // Bit_Extender bit_extender_5
  assign not_1_out = ~bit_extender_1_out;  // NOT_Gate not_1, 16 bits wide
  assign not_2_out = ~bit_extender_2_out;  // NOT_Gate not_2, 16 bits wide
  assign not_3_out = ~bit_extender_3_out;  // NOT_Gate not_3, 16 bits wide
  assign not_4_out = ~bit_extender_4_out;  // NOT_Gate not_4, 16 bits wide
  assign not_5_out = ~bit_extender_5_out;  // NOT_Gate not_5, 16 bits wide
  assign and_1_out = in_2 & not_1_out & not_2_out & not_4_out & not_5_out & in_3;  // AND_Gate and_1, 16 bits wide
  assign and_2_out = in_3 & not_1_out & not_2_out & not_4_out & bit_extender_5_out & in_4;  // AND_Gate and_2, 16 bits wide
  assign and_3_out = in_4 & not_1_out & not_2_out & bit_extender_4_out & not_5_out & undriven;  // AND_Gate and_3, 16 bits wide
  assign and_4_out = undriven & not_1_out & not_2_out & bit_extender_4_out & bit_extender_5_out & undriven_2;  // AND_Gate and_4, 16 bits wide
  assign and_5_out = undriven_2 & not_1_out & not_2_out & not_4_out & not_5_out & undriven_3;  // AND_Gate and_5, 16 bits wide
  assign and_6_out = undriven_3 & not_1_out & not_2_out & not_4_out & bit_extender_5_out & undriven_4;  // AND_Gate and_6, 16 bits wide
  assign and_7_out = undriven_4 & not_1_out & not_2_out & bit_extender_4_out & not_5_out & undriven_5;  // AND_Gate and_7, 16 bits wide
  assign and_8_out = undriven_5 & not_1_out & not_2_out & bit_extender_4_out & bit_extender_5_out & undriven_6;  // AND_Gate and_8, 16 bits wide
  assign and_9_out = undriven_6 & not_1_out & bit_extender_2_out & not_4_out & not_5_out & undriven_7;  // AND_Gate and_9, 16 bits wide
  assign and_10_out = undriven_7 & not_1_out & bit_extender_2_out & not_4_out & bit_extender_5_out & undriven_8;  // AND_Gate and_10, 16 bits wide
  assign and_11_out = undriven_8 & not_1_out & bit_extender_2_out & bit_extender_4_out & not_5_out & undriven_9;  // AND_Gate and_11, 16 bits wide
  assign and_12_out = undriven_9 & not_1_out & bit_extender_2_out & bit_extender_4_out & bit_extender_5_out & undriven_10;  // AND_Gate and_12, 16 bits wide
  assign and_13_out = undriven_10 & not_1_out & bit_extender_2_out & not_4_out & not_5_out & undriven_11;  // AND_Gate and_13, 16 bits wide
  assign and_14_out = undriven_11 & not_1_out & bit_extender_2_out & not_4_out & bit_extender_5_out & undriven_12;  // AND_Gate and_14, 16 bits wide
  assign and_15_out = undriven_12 & not_1_out & bit_extender_2_out & bit_extender_4_out & not_5_out & undriven_13;  // AND_Gate and_15, 16 bits wide
  assign and_16_out = undriven_13 & not_1_out & bit_extender_2_out & bit_extender_4_out & bit_extender_5_out & undriven_14;  // AND_Gate and_16, 16 bits wide
  assign and_17_out = undriven_14 & bit_extender_1_out & not_2_out & not_4_out & not_5_out & undriven_15;  // AND_Gate and_17, 16 bits wide
  assign and_18_out = undriven_15 & bit_extender_1_out & not_2_out & not_4_out & bit_extender_5_out & undriven_16;  // AND_Gate and_18, 16 bits wide
  assign and_19_out = undriven_16 & bit_extender_1_out & not_2_out & bit_extender_4_out & not_5_out & undriven_17;  // AND_Gate and_19, 16 bits wide
  assign and_20_out = undriven_17 & bit_extender_1_out & not_2_out & bit_extender_4_out & bit_extender_5_out & undriven_18;  // AND_Gate and_20, 16 bits wide
  assign and_21_out = undriven_18 & bit_extender_1_out & not_2_out & not_4_out & not_5_out & undriven_19;  // AND_Gate and_21, 16 bits wide
  assign and_22_out = undriven_19 & bit_extender_1_out & not_2_out & not_4_out & bit_extender_5_out & undriven_20;  // AND_Gate and_22, 16 bits wide
  assign and_23_out = undriven_20 & bit_extender_1_out & not_2_out & bit_extender_4_out & not_5_out & undriven_21;  // AND_Gate and_23, 16 bits wide
  assign and_24_out = undriven_21 & bit_extender_1_out & not_2_out & bit_extender_4_out & bit_extender_5_out & undriven_22;  // AND_Gate and_24, 16 bits wide
  assign and_25_out = undriven_22 & bit_extender_1_out & bit_extender_2_out & not_4_out & not_5_out & undriven_23;  // AND_Gate and_25, 16 bits wide
  assign and_26_out = undriven_23 & bit_extender_1_out & bit_extender_2_out & not_4_out & bit_extender_5_out & undriven_24;  // AND_Gate and_26, 16 bits wide
  assign and_27_out = undriven_24 & bit_extender_1_out & bit_extender_2_out & bit_extender_4_out & not_5_out & undriven_25;  // AND_Gate and_27, 16 bits wide
  assign and_28_out = undriven_25 & bit_extender_1_out & bit_extender_2_out & bit_extender_4_out & bit_extender_5_out & undriven_26;  // AND_Gate and_28, 16 bits wide
  assign and_29_out = undriven_26 & bit_extender_1_out & bit_extender_2_out & not_4_out & not_5_out & undriven_27;  // AND_Gate and_29, 16 bits wide
  assign and_30_out = undriven_27 & bit_extender_1_out & bit_extender_2_out & not_4_out & bit_extender_5_out & undriven_28;  // AND_Gate and_30, 16 bits wide
  assign and_31_out = undriven_28 & bit_extender_1_out & bit_extender_2_out & bit_extender_4_out & not_5_out & undriven_29;  // AND_Gate and_31, 16 bits wide
  assign and_32_out = undriven_29 & bit_extender_1_out & bit_extender_2_out & bit_extender_4_out & bit_extender_5_out;  // AND_Gate and_32, 16 bits wide
  assign out_7 = and_1_out | and_2_out | and_3_out | and_4_out | and_5_out | and_6_out | and_7_out | and_8_out | and_9_out | and_10_out | and_11_out | and_12_out | and_13_out | and_14_out | and_15_out | and_16_out | and_17_out | and_18_out | and_19_out | and_20_out | and_21_out | and_22_out | and_23_out | and_24_out | and_25_out | and_26_out | and_27_out | and_28_out | and_29_out | and_30_out | and_31_out | and_32_out;  // OR_Gate or_1, 16 bits wide
endmodule

module mux_32 (
  input  [4:0] in_1
);

  wire [15:0] bit_extender_1_out, bit_extender_2_out, bit_extender_3_out, bit_extender_4_out,
       bit_extender_5_out, not_1_out, not_2_out, not_3_out, not_4_out, not_5_out;

  assign bit_extender_1_out = {{15{in_1[0]}}, in_1[0]};  // Bit_Extender bit_extender_1
  assign bit_extender_2_out = {{15{in_1[1]}}, in_1[1]};  // Bit_Extender bit_extender_2
  assign bit_extender_3_out = {{15{in_1[2]}}, in_1[2]};  // Bit_Extender bit_extender_3
  assign bit_extender_4_out = {{15{in_1[3]}}, in_1[3]};  // Bit_Extender bit_extender_4
  assign bit_extender_5_out = {{15{in_1[4]}}, in_1[4]};  // Bit_Extender bit_extender_5
  assign not_1_out = ~bit_extender_1_out;  // NOT_Gate not_1, 16 bits wide
  assign not_2_out = ~bit_extender_2_out;  // NOT_Gate not_2, 16 bits wide
  assign not_3_out = ~bit_extender_3_out;  // NOT_Gate not_3, 16 bits wide
  assign not_4_out = ~bit_extender_4_out;  // NOT_Gate not_4, 16 bits wide
  assign not_5_out = ~bit_extender_5_out;  // NOT_Gate not_5, 16 bits wide
  // AND_Gate and_1 has open pins: in1=not_1_out, in2=not_2_out, in3=not_4_out, in4=not_5_out, out=open
  // AND_Gate and_2 has open pins: in1=not_1_out, in2=not_2_out, in3=not_4_out, in4=bit_extender_5_out, out=open
  // AND_Gate and_3 has open pins: in1=not_1_out, in2=not_2_out, in3=bit_extender_4_out, in4=not_5_out, out=open
  // AND_Gate and_4 has open pins: in1=not_1_out, in2=not_2_out, in3=bit_extender_4_out, in4=bit_extender_5_out, out=open
  // AND_Gate and_5 has open pins: in1=not_1_out, in2=not_2_out, in3=not_4_out, in4=not_5_out, out=open
  // AND_Gate and_6 has open pins: in1=not_1_out, in2=not_2_out, in3=not_4_out, in4=bit_extender_5_out, out=open
  // AND_Gate and_7 has open pins: in1=not_1_out, in2=not_2_out, in3=bit_extender_4_out, in4=not_5_out, out=open
  // AND_Gate and_8 has open pins: in1=not_1_out, in2=not_2_out, in3=bit_extender_4_out, in4=bit_extender_5_out, out=open
  // AND_Gate and_9 has open pins: in1=not_1_out, in2=bit_extender_2_out, in3=not_4_out, in4=not_5_out, out=open
  // AND_Gate and_10 has open pins: in1=not_1_out, in2=bit_extender_2_out, in3=not_4_out, in4=bit_extender_5_out, out=open
  // AND_Gate and_11 has open pins: in1=not_1_out, in2=bit_extender_2_out, in3=bit_extender_4_out, in4=not_5_out, out=open
  // AND_Gate and_12 has open pins: in1=not_1_out, in2=bit_extender_2_out, in3=bit_extender_4_out, in4=bit_extender_5_out, out=open
  // AND_Gate and_13 has open pins: in1=not_1_out, in2=bit_extender_2_out, in3=not_4_out, in4=not_5_out, out=open
  // AND_Gate and_14 has open pins: in1=not_1_out, in2=bit_extender_2_out, in3=not_4_out, in4=bit_extender_5_out, out=open
  // AND_Gate and_15 has open pins: in1=not_1_out, in2=bit_extender_2_out, in3=bit_extender_4_out, in4=not_5_out, out=open
  // AND_Gate and_16 has open pins: in1=not_1_out, in2=bit_extender_2_out, in3=bit_extender_4_out, in4=bit_extender_5_out, out=open
  // AND_Gate and_17 has open pins: in1=bit_extender_1_out, in2=not_2_out, in3=not_4_out, in4=not_5_out, out=open
  // AND_Gate and_18 has open pins: in1=bit_extender_1_out, in2=not_2_out, in3=not_4_out, in4=bit_extender_5_out, out=open
  // AND_Gate and_19 has open pins: in1=bit_extender_1_out, in2=not_2_out, in3=bit_extender_4_out, in4=not_5_out, out=open
  // AND_Gate and_20 has open pins: in1=bit_extender_1_out, in2=not_2_out, in3=bit_extender_4_out, in4=bit_extender_5_out, out=open
  // AND_Gate and_21 has open pins: in1=bit_extender_1_out, in2=not_2_out, in3=not_4_out, in4=not_5_out, out=open
  // AND_Gate and_22 has open pins: in1=bit_extender_1_out, in2=not_2_out, in3=not_4_out, in4=bit_extender_5_out, out=open
  // AND_Gate and_23 has open pins: in1=bit_extender_1_out, in2=not_2_out, in3=bit_extender_4_out, in4=not_5_out, out=open
  // AND_Gate and_24 has open pins: in1=bit_extender_1_out, in2=not_2_out, in3=bit_extender_4_out, in4=bit_extender_5_out, out=open
  // AND_Gate and_25 has open pins: in1=bit_extender_1_out, in2=bit_extender_2_out, in3=not_4_out, in4=not_5_out, out=open
  // AND_Gate and_26 has open pins: in1=bit_extender_1_out, in2=bit_extender_2_out, in3=not_4_out, in4=bit_extender_5_out, out=open
  // AND_Gate and_27 has open pins: in1=bit_extender_1_out, in2=bit_extender_2_out, in3=bit_extender_4_out, in4=not_5_out, out=open
  // AND_Gate and_28 has open pins: in1=bit_extender_1_out, in2=bit_extender_2_out, in3=bit_extender_4_out, in4=bit_extender_5_out, out=open
  // AND_Gate and_29 has open pins: in1=bit_extender_1_out, in2=bit_extender_2_out, in3=not_4_out, in4=not_5_out, out=open
  // AND_Gate and_30 has open pins: in1=bit_extender_1_out, in2=bit_extender_2_out, in3=not_4_out, in4=bit_extender_5_out, out=open
  // AND_Gate and_31 has open pins: in1=bit_extender_1_out, in2=bit_extender_2_out, in3=bit_extender_4_out, in4=not_5_out, out=open
  // AND_Gate and_32 has open pins: in1=bit_extender_1_out, in2=bit_extender_2_out, in3=bit_extender_4_out, in4=bit_extender_5_out, out=open
endmodule

module final_mux32 (
  input  [4:0] opcode,
  input  [15:0] op_00000,
  input  [15:0] add_00001,
  input  [15:0] op_00010,
  input  [15:0] mult_00011,
  input  [15:0] op_00100,
  input  [15:0] op_00101,
  input  [15:0] op_00110,
  input  [15:0] op_00111,
  input  [15:0] op_01000,
  input  [15:0] op_01001,
  input  [15:0] comp_01010,
  input  [15:0] and_01011,
  input  [15:0] xor_01100,
  input  [15:0] not_01101,
  input  [15:0] op_01110,
  input  [15:0] op_01111,
  input  [15:0] op_10000,
  input  [15:0] sub_10001,
  input  [15:0] op_10010,
  input  [15:0] op_10011,
  input  [15:0] op_10100,
  input  [15:0] op_10101,
  input  [15:0] op_10110,
  input  [15:0] op_10111,
  input  [15:0] op_11000,
  input  [15:0] op_11001,
  input  [15:0] op_11010,
  input  [15:0] op_11011,
  input  [15:0] op_11100,
  input  [15:0] op_11101,
  input  [15:0] op_11110,
  input  [15:0] op_11111,
  output [15:0] out_34
);

  wire [15:0] and_1_out, and_2_out, and_3_out, and_4_out, and_5_out, and_6_out, and_7_out, and_8_out,
       and_9_out, and_10_out, and_11_out, and_12_out, and_13_out, and_14_out, and_15_out, and_16_out,
       and_17_out, and_18_out, and_19_out, and_20_out, and_21_out, and_22_out, and_23_out, and_24_out,
       and_25_out, and_26_out, and_27_out, and_28_out, and_29_out, and_30_out, and_31_out, and_32_out,
       bit_extender_1_out, bit_extender_2_out, bit_extender_3_out, bit_extender_4_out, bit_extender_5_out,
       not_1_out, not_2_out, not_3_out, not_4_out, not_5_out;

  assign bit_extender_1_out = {{15{opcode[4]}}, opcode[4]};  // Bit_Extender bit_extender_1
  assign bit_extender_2_out = {{15{opcode[3]}}, opcode[3]};  // Bit_Extender bit_extender_2
  assign bit_extender_3_out = {{15{opcode[2]}}, opcode[2]};  // Bit_Extender bit_extender_3
  assign bit_extender_4_out = {{15{opcode[1]}}, opcode[1]};  // Bit_Extender bit_extender_4
  assign bit_extender_5_out = {{15{opcode[0]}}, opcode[0]};  // Bit_Extender bit_extender_5
  assign not_1_out = ~bit_extender_1_out;  // NOT_Gate not_1, 16 bits wide
  assign not_2_out = ~bit_extender_2_out;  // NOT_Gate not_2, 16 bits wide
  assign not_3_out = ~bit_extender_3_out;  // NOT_Gate not_3, 16 bits wide
  assign not_4_out = ~bit_extender_4_out;  // NOT_Gate not_4, 16 bits wide
  assign not_5_out = ~bit_extender_5_out;  // NOT_Gate not_5, 16 bits wide
  assign and_1_out = not_1_out & not_2_out & not_3_out & not_4_out & not_5_out & op_00000;  // AND_Gate and_1, 16 bits wide
  assign and_2_out = not_1_out & not_2_out & not_3_out & not_4_out & bit_extender_5_out & add_00001;  // AND_Gate and_2, 16 bits wide
  assign and_3_out = not_1_out & not_2_out & not_3_out & bit_extender_4_out & not_5_out & op_00010;  // AND_Gate and_3, 16 bits wide
  assign and_4_out = not_1_out & not_2_out & not_3_out & bit_extender_4_out & bit_extender_5_out & mult_00011;  // AND_Gate and_4, 16 bits wide
  assign and_5_out = not_1_out & not_2_out & bit_extender_3_out & not_4_out & not_5_out & op_00100;  // AND_Gate and_5, 16 bits wide
  assign and_6_out = not_1_out & not_2_out & bit_extender_3_out & not_4_out & bit_extender_5_out & op_00101;  // AND_Gate and_6, 16 bits wide
  assign and_7_out = not_1_out & not_2_out & bit_extender_3_out & bit_extender_4_out & not_5_out & op_00110;  // AND_Gate and_7, 16 bits wide
  assign and_8_out = not_1_out & not_2_out & bit_extender_3_out & bit_extender_4_out & bit_extender_5_out & op_00111;  // AND_Gate and_8, 16 bits wide
  assign and_9_out = not_1_out & bit_extender_2_out & not_3_out & not_4_out & not_5_out & op_01000;  // AND_Gate and_9, 16 bits wide
  assign and_10_out = not_1_out & bit_extender_2_out & not_3_out & not_4_out & bit_extender_5_out & op_01001;  // AND_Gate and_10, 16 bits wide
  assign and_11_out = not_1_out & bit_extender_2_out & not_3_out & bit_extender_4_out & not_5_out & comp_01010;  // AND_Gate and_11, 16 bits wide
  assign and_12_out = not_1_out & bit_extender_2_out & not_3_out & bit_extender_4_out & bit_extender_5_out & and_01011;  // AND_Gate and_12, 16 bits wide
  assign and_13_out = not_1_out & bit_extender_2_out & bit_extender_3_out & not_4_out & not_5_out & xor_01100;  // AND_Gate and_13, 16 bits wide
  assign and_14_out = not_1_out & bit_extender_2_out & bit_extender_3_out & not_4_out & bit_extender_5_out & not_01101;  // AND_Gate and_14, 16 bits wide
  assign and_15_out = not_1_out & bit_extender_2_out & bit_extender_3_out & bit_extender_4_out & not_5_out & op_01110;  // AND_Gate and_15, 16 bits wide
  assign and_16_out = not_1_out & bit_extender_2_out & bit_extender_3_out & bit_extender_4_out & bit_extender_5_out & op_01111;  // AND_Gate and_16, 16 bits wide
  assign and_17_out = bit_extender_1_out & not_2_out & not_3_out & not_4_out & not_5_out & op_10000;  // AND_Gate and_17, 16 bits wide
  assign and_18_out = bit_extender_1_out & not_2_out & not_3_out & not_4_out & bit_extender_5_out & sub_10001;  // AND_Gate and_18, 16 bits wide
  assign and_19_out = bit_extender_1_out & not_2_out & not_3_out & bit_extender_4_out & not_5_out & op_10010;  // AND_Gate and_19, 16 bits wide
  assign and_20_out = bit_extender_1_out & not_2_out & not_3_out & bit_extender_4_out & bit_extender_5_out & op_10011;  // AND_Gate and_20, 16 bits wide
  assign and_21_out = bit_extender_1_out & not_2_out & bit_extender_3_out & not_4_out & not_5_out & op_10100;  // AND_Gate and_21, 16 bits wide
  assign and_22_out = bit_extender_1_out & not_2_out & bit_extender_3_out & not_4_out & bit_extender_5_out & op_10101;  // AND_Gate and_22, 16 bits wide
  assign and_23_out = bit_extender_1_out & not_2_out & bit_extender_3_out & bit_extender_4_out & not_5_out & op_10110;  // AND_Gate and_23, 16 bits wide
  assign and_24_out = bit_extender_1_out & not_2_out & bit_extender_3_out & bit_extender_4_out & bit_extender_5_out & op_10111;  // AND_Gate and_24, 16 bits wide
  assign and_25_out = bit_extender_1_out & bit_extender_2_out & not_3_out & not_4_out & not_5_out & op_11000;  // AND_Gate and_25, 16 bits wide
  assign and_26_out = bit_extender_1_out & bit_extender_2_out & not_3_out & not_4_out & bit_extender_5_out & op_11001;  // AND_Gate and_26, 16 bits wide
  assign and_27_out = bit_extender_1_out & bit_extender_2_out & not_3_out & bit_extender_4_out & not_5_out & op_11010;  // AND_Gate and_27, 16 bits wide
  assign and_28_out = bit_extender_1_out & bit_extender_2_out & not_3_out & bit_extender_4_out & bit_extender_5_out & op_11011;  // AND_Gate and_28, 16 bits wide
  assign and_29_out = bit_extender_1_out & bit_extender_2_out & bit_extender_3_out & not_4_out & not_5_out & op_11100;  // AND_Gate and_29, 16 bits wide
  assign and_30_out = bit_extender_1_out & bit_extender_2_out & bit_extender_3_out & not_4_out & bit_extender_5_out & op_11101;  // AND_Gate and_30, 16 bits wide
  assign and_31_out = bit_extender_1_out & bit_extender_2_out & bit_extender_3_out & bit_extender_4_out & not_5_out & op_11110;  // AND_Gate and_31, 16 bits wide
  assign and_32_out = bit_extender_1_out & bit_extender_2_out & bit_extender_3_out & bit_extender_4_out & bit_extender_5_out & op_11111;  // AND_Gate and_32, 16 bits wide
  assign out_34 = and_1_out | and_2_out | and_3_out | and_4_out | and_5_out | and_6_out | and_7_out | and_8_out | and_9_out | and_10_out | and_11_out | and_12_out | and_13_out | and_14_out | and_15_out | and_16_out | and_17_out | and_18_out | and_19_out | and_20_out | and_21_out | and_22_out | and_23_out | and_24_out | and_25_out | and_26_out | and_27_out | and_28_out | and_29_out | and_30_out | and_31_out | and_32_out;  // OR_Gate or_1, 16 bits wide
endmodule

module sharah_e_faisal (
  input  OE,
  input  bit1,
  input  bit2,
  input  [15:0] data_In,
  output [15:0] Ram_system,
  output [15:0] Ram_A,
  output [15:0] Ram_B
);

  wire [15:0] and_1_out, and_2_out, and_3_out, and_4_out, and_5_out, bit_extender_1_out, bit_extender_2_out,
       bit_extender_3_out, not_1_out, not_2_out;

  assign bit_extender_1_out = {{15{OE}}, OE};  // Bit_Extender bit_extender_1
  assign bit_extender_2_out = {{15{bit1}}, bit1};  // Bit_Extender bit_extender_2
  assign bit_extender_3_out = {{15{bit2}}, bit2};  // Bit_Extender bit_extender_3
  assign not_1_out = ~bit_extender_2_out;  // NOT_Gate not_1, 16 bits wide
  assign not_2_out = ~bit_extender_3_out;  // NOT_Gate not_2, 16 bits wide
  assign and_1_out = not_1_out & data_In & not_2_out;  // AND_Gate and_1, 16 bits wide
  assign and_2_out = not_1_out & data_In & bit_extender_3_out;  // AND_Gate and_2, 16 bits wide
  assign and_3_out = bit_extender_2_out & data_In & not_2_out;  // AND_Gate and_3, 16 bits wide
  assign and_4_out = bit_extender_2_out & data_In & bit_extender_3_out;  // AND_Gate and_4, 16 bits wide
  assign and_5_out = and_1_out & bit_extender_1_out;  // AND_Gate and_5, 16 bits wide
  assign Ram_system = and_2_out & bit_extender_1_out;  // AND_Gate and_6, 16 bits wide
  assign Ram_A = and_3_out & bit_extender_1_out;  // AND_Gate and_7, 16 bits wide
  assign Ram_B = and_4_out & bit_extender_1_out;  // AND_Gate and_8, 16 bits wide
endmodule

module attempt_quadra (
  input  RAM_A_WE,
  input  RAM_A_OE,
  input  RAM_B_OE,
  input  RAM_B_WE,
  input  Inst_RAM_OE,
  input  Inst_RAM_WE,
  input  system_RAM_OE,
  input  system_RAM_WE,
  input  MBR_B_WE,
  input  MBR_A_WE,
  input  MBR_Z_WE,
  input  inst_splitter_we,
  input  MBR_B_CB,
  input  MBR_A_CB,
  input  MBR_Z_CB,
  input  MAR_Z_WE,
  input  MAR_A_WE,
  input  MAR_B_WE,
  input  reg_8_we,
  input  reg_4_we,
  input  reg_2_we,
  input  reg_6_we,
  input  reg_7_we,
  input  reg_5_we,
  input  reg_3_we,
  input  reg_1_we,
  input  reg_a_out_cb,
  input  reg_b_out_cb,
  input  Alu_out_cb,
  input  counter_increment_by_1,
  input  counter_increment_on,
  input  counter_reset,
  input  opcode_reg_we,
  input  opcode_init_cb,
  input  reg1_cb,
  input  reg5_cb,
  input  reg7_cb,
  input  Alu_register_we,
  input  overflow_reg_we,
  input  bus_select_oe,
  input  bus_select_bit1,
  input  bus_select_bit2,
  input  system_cb,
  input  reset_shit
);

  wire alu_1_carry_out, clock_1_out;
  wire [4:0] controlled_buffer_1_out, counter_1_q, register_8_q, register_13_q, register_14_q,
       spliitter_1_add_a, spliitter_1_add_b;
  wire [4:4] controlled_buffer_1_out_2, register_1_q;
  wire [7:0] register_1_q_2;
  wire [15:0] alu_1_result, controlled_buffer_5_out, controlled_buffer_6_out, controlled_buffer_8_out,
       ram_1_dout, ram_2_dout, ram_4_dout, register_2_q, register_4_q, register_5_q, register_6_q,
       register_7_q, register_9_q, register_15_q, register_16_q, register_17_q, undriven;
  wire [61:0] rom_1_data;

  Counter #(.max('h1f), .width(5)) counter_1 (
    .clr(rom_1_data[31]), .up(1'b1), .count(rom_1_data[29]), .clk(clock_1_out), .Q(counter_1_q));  // open: load, D, carry
  Register #(.width(5)) register_1 (
    .D({controlled_buffer_1_out_2[4], controlled_buffer_1_out[3:0]}), .en(rom_1_data[32]), .clk(clock_1_out),
    .Q({register_1_q[4], register_1_q_2[7:4]}), .clr(rom_1_data[43]));
  Register #(.width(16)) register_2 (
    .D(alu_1_result), .en(rom_1_data[37]), .clk(clock_1_out), .Q(register_2_q));  // open: clr
  Register #(.width(1)) register_3 (.D(alu_1_carry_out), .en(rom_1_data[38]), .clk(clock_1_out));  // open: Q, clr
  assign {controlled_buffer_1_out_2[4], controlled_buffer_1_out[3:0]} = rom_1_data[33] ? {5{1'b0}} : 5'bz;  // Controlled_Buffer controlled_buffer_1
  // Probe on alu_1_result
  ALU alu_1 (
    .opcode(controlled_buffer_1_out), .A(controlled_buffer_5_out), .B(controlled_buffer_6_out),
    .result(alu_1_result), .carry_out(alu_1_carry_out));
  sharah_e_faisal sharah_e_faisal_1 ();  // open: OE, bit1, bit2, data_In, Ram_system, Ram_A, Ram_B
  Register #(.width(16)) register_4 (
    .D(controlled_buffer_5_out), .en(rom_1_data[25]), .clk(clock_1_out), .Q(register_4_q));  // open: clr
  Register #(.width(16)) register_5 (
    .D(controlled_buffer_5_out), .en(rom_1_data[24]), .clk(clock_1_out), .Q(register_5_q));  // open: clr
  Register #(.width(16)) register_6 (
    .D(undriven), .en(rom_1_data[23]), .clk(clock_1_out), .Q(register_6_q));  // open: clr
  Register #(.width(16)) register_7 (
    .D(undriven), .en(rom_1_data[22]), .clk(clock_1_out), .Q(register_7_q));  // open: clr
  Register #(.width(5)) register_8 (
    .D(counter_1_q), .en(rom_1_data[15]), .clk(clock_1_out), .Q(register_8_q));  // open: clr
  // Probe on register_8_q
  Spliitter spliitter_1 (
    .Instruction(controlled_buffer_8_out), .WE(rom_1_data[11]), .clk(clock_1_out), .Add_B(spliitter_1_add_b),
    .Add_A(spliitter_1_add_a), .opcode({controlled_buffer_1_out_2[4], controlled_buffer_1_out[3:0]}),
    .flag(controlled_buffer_1_out[4]));
  Register #(.width(16)) register_9 (
    .D(undriven), .en(rom_1_data[21]), .clk(clock_1_out), .Q(register_9_q));  // open: clr
  // Probe on spliitter_1_add_b
  // Probe on spliitter_1_add_a
  assign register_5_q = rom_1_data[34] ? register_4_q : 16'bz;  // Controlled_Buffer controlled_buffer_2
  Register #(.width(16)) register_10 (
    .D(controlled_buffer_5_out), .en(rom_1_data[20]), .clk(clock_1_out), .Q(register_5_q));  // open: clr
  Register #(.width(16)) register_11 (
    .D(controlled_buffer_5_out), .en(rom_1_data[19]), .clk(clock_1_out), .Q(register_5_q));  // open: clr
  assign register_7_q = rom_1_data[35] ? register_6_q : 16'bz;  // Controlled_Buffer controlled_buffer_3
  Register #(.width(16)) register_12 (
    .D(undriven), .en(rom_1_data[18]), .clk(clock_1_out), .Q(register_7_q));  // open: clr
  assign register_7_q = rom_1_data[36] ? register_9_q : 16'bz;  // Controlled_Buffer controlled_buffer_4
  Register #(.width(5)) register_13 (
    .D(spliitter_1_add_a), .en(rom_1_data[16]), .clk(clock_1_out), .Q(register_13_q));  // open: clr
  // Probe on {controlled_buffer_1_out_2[4], controlled_buffer_1_out[3:0]}
  assign controlled_buffer_5_out = rom_1_data[26] ? register_5_q : 16'bz;  // Controlled_Buffer controlled_buffer_5
  assign controlled_buffer_6_out = rom_1_data[27] ? register_7_q : 16'bz;  // Controlled_Buffer controlled_buffer_6
  Clock clock_1 (.out(clock_1_out));
  Register #(.width(5)) register_14 (
    .D(spliitter_1_add_b), .en(rom_1_data[17]), .clk(clock_1_out), .Q(register_14_q));  // open: clr
  Counter #(.max('h1f), .width(5)) counter_2 ();  // open: clr, load, up, count, clk, D, carry, Q
  // mat_mult_rom mat_mult_rom_1: pin names not known; wires that end beside it: register_4_q, register_9_q, register_5_q, register_7_q, register_6_q, register_7_q, register_5_q, register_5_q
  Register #(.width(16)) register_15 (
    .D(ram_1_dout), .en(rom_1_data[10]), .clk(clock_1_out), .Q(register_15_q));  // open: clr
  Register #(.width(16)) register_16 (
    .D(ram_2_dout), .en(rom_1_data[9]), .clk(clock_1_out), .Q(register_16_q));  // open: clr
  Register #(.width(16)) register_17 (
    .D(ram_4_dout), .en(rom_1_data[8]), .clk(clock_1_out), .Q(register_17_q));  // open: clr
  assign controlled_buffer_6_out = rom_1_data[12] ? register_17_q : 16'bz;  // Controlled_Buffer controlled_buffer_7
  assign controlled_buffer_8_out = rom_1_data[14] ? register_15_q : 16'bz;  // Controlled_Buffer controlled_buffer_8
  assign controlled_buffer_5_out = rom_1_data[13] ? register_16_q : 16'bz;  // Controlled_Buffer controlled_buffer_9
  // Probe on register_8_q
  RAM #(.addrWidth(5), .dataWidth(16)) ram_1 (
    .addr(register_8_q), .we(rom_1_data[5]), .oe(rom_1_data[4]), .clk(clock_1_out),
    .din(controlled_buffer_8_out), .dout(ram_1_dout));
  // Probe on controlled_buffer_8_out
  RAM #(.addrWidth(5), .dataWidth(16)) ram_2 (
    .addr(register_13_q), .we(rom_1_data[0]), .oe(rom_1_data[1]), .clk(clock_1_out),
    .din(controlled_buffer_5_out), .dout(ram_2_dout));
  // Probe on ram_1_dout
  // Probe on ram_2_dout
  assign controlled_buffer_8_out = rom_1_data[42] ? register_2_q : 16'bz;  // Controlled_Buffer controlled_buffer_10
  RAM #(.addrWidth(5), .dataWidth(16)) ram_3 (
    .addr(register_8_q), .we(rom_1_data[7]), .oe(rom_1_data[6]), .clk(clock_1_out),
    .din(controlled_buffer_8_out), .dout(ram_1_dout));
  RAM #(.addrWidth(5), .dataWidth(16)) ram_4 (
    .addr(register_14_q), .we(rom_1_data[3]), .oe(rom_1_data[2]), .clk(clock_1_out),
    .din(controlled_buffer_6_out), .dout(ram_4_dout));
  Register #(.width(16)) register_18 ();  // open: D, en, clk, Q, clr
  // Probe on ram_4_dout
  ROM #(.addrWidth(9), .dataWidth(62)) rom_1 (.addr({controlled_buffer_1_out[4], register_1_q_2}), .data(rom_1_data));
  Counter #(.max('hf), .width(4)) counter_3 (
    .clr(rom_1_data[43]), .up(1'b1), .count(1'b1), .clk(clock_1_out), .Q(register_1_q_2[3:0]));  // open: load, D, carry
  Counter #(.max('h1f), .width(5)) counter_4 ();  // open: clr, load, up, count, clk, D, carry, Q

  // Notes on the sheet:
  //   opcode
  //   alu register
  //   overflow
  //   Reg 5
  //   MAR_Zero
  //   Reg 1
  //   Reg 3
  //   Reg 7
  //   Reg 2
  //   Reg 6
  //   Reg 4
  //   Reg 8
  //   MAR_A
  //   MAR_B
  //   0fff mult
  //   MBR_B
  //   38
  //   MBR_Z
  //   MBR_A
  //   and
  //   xor
  //   07ff
  //   2bff
  //   2fff
  //   18
  //   comp
  //   b8
  //   c8
  //   33ff
  //   add
  //   a8
  //   RAM_A
  //   Instruction_Ram
  //   System_Ram
  //   RAM_B
  //   8
  //   4
  //   2
  //   1
  //   8
  //   4
  //   2
  //   1
  //   8
  //   4
  //   2
  //   1
  //   8
  //   4
  //   2
  //   1
  //   4
  //   2
  //   8
  //   4
  //   2
  //   1
  //   8
  //   8
  //   1
  //   4
  //   2
  //   1
  //   8
  //   4
  //   2
  //   1
  //   8
  //   4
  //   2
  //   1
  //   8
  //   4
  //   2
  //   1
  //   8
  //   4
  //   2
  //   1
  //   8
  //   4
  //   2
  //   1
  //   contents of rom_1 (hex, n*v repeats v):
  //   0 82000000000 82000000000 1200000000 c0000000 60c000000000 60c000000000 8000 16*0 c00080400 40000
  //   100000000 10000000020 10 27*0 c00080400 40000 100000000 10000000020 10 107*0 c00080400 40000
  //   100000000 10000000020 10 11*0 c00080400 40000 100000000 10000000020 10 11*0 c00080400 40000
  //   100000000 10000000020 10
  //   8000E00000
  //   zero pehle 
  //   881800000000
  //   7800000000
  //   60FF000000
  //   20400120000
  //   8400800000
  //   600000
  //   b8
  //   c8
endmodule

module attempt_poncho (
  input  RAM_A_WE,
  input  RAM_A_OE,
  input  RAM_B_OE,
  input  RAM_B_WE,
  input  Inst_RAM_OE,
  input  Inst_RAM_WE,
  input  system_RAM_OE,
  input  system_RAM_WE,
  input  MBR_B_WE,
  input  MBR_A_WE,
  input  MBR_Z_WE,
  input  inst_splitter_we,
  input  MBR_B_CB,
  input  MBR_A_CB,
  input  MBR_Z_CB,
  input  MAR_Z_WE,
  input  MAR_A_WE,
  input  MAR_B_WE,
  input  reg_8_we,
  input  reg_4_we,
  input  reg_2_we,
  input  reg_6_we,
  input  reg_7_we,
  input  reg_5_we,
  input  reg_3_we,
  input  reg_1_we,
  input  reg_a_out_cb,
  input  reg_b_out_cb,
  input  Alu_out_cb,
  input  counter_increment_by_1,
  input  counter_increment_on,
  input  counter_reset,
  input  opcode_reg_we,
  input  opcode_init_cb,
  input  reg1_cb,
  input  reg5_cb,
  input  reg7_cb,
  input  Alu_register_we,
  input  overflow_reg_we,
  input  bus_select_oe,
  input  bus_select_bit1,
  input  bus_select_bit2,
  input  system_cb,
  input  reset_shit
);

  wire clock_1_out;
  wire [4:0] controlled_buffer_3_out, counter_1_q, counter_2_q, register_8_q, register_13_q, register_16_q,
       spliitter_1_add_a, spliitter_1_add_b;
  wire [4:4] controlled_buffer_3_out_2, register_1_q;
  wire [7:0] register_1_q_2;
  wire [15:0] alu_1_carry_out, alu_1_result, controlled_buffer_1_out, controlled_buffer_7_out,
       controlled_buffer_8_out, controlled_buffer_15_out, mat_mult_rom_1_out_10, mat_mult_rom_1_out_11,
       mat_mult_rom_1_out_12, mat_mult_rom_1_out_13, ram_1_dout, ram_2_dout, ram_4_dout, register_2_q,
       register_3_q, register_4_q, register_5_q, register_6_q, register_7_q, register_9_q, register_14_q,
       register_15_q, register_17_q, register_18_q, register_19_q, register_20_q, register_21_q, undriven,
       undriven_2;
  wire [61:0] rom_1_data;

  Controlled_Buffer #(.width(16)) controlled_buffer_1 (.in(register_2_q), .out(controlled_buffer_1_out));  // open: en
  Controlled_Buffer #(.width(16)) controlled_buffer_2 (.in(register_3_q), .out(controlled_buffer_1_out));  // open: en
  sharah_e_faisal sharah_e_faisal_1 (
    .OE(rom_1_data[39]), .bit1(rom_1_data[40]), .bit2(rom_1_data[41]), .data_In(controlled_buffer_1_out));  // open: Ram_system, Ram_A, Ram_B
  Counter #(.max('h1f), .width(5)) counter_1 (
    .clr(rom_1_data[31]), .up(1'b1), .count(rom_1_data[29]), .clk(clock_1_out), .Q(counter_1_q));  // open: load, D, carry
  Register #(.width(5)) register_1 (
    .D({controlled_buffer_3_out_2[4], controlled_buffer_3_out[3:0]}), .en(rom_1_data[32]), .clk(clock_1_out),
    .Q({register_1_q[4], register_1_q_2[7:4]}), .clr(rom_1_data[43]));
  Register #(.width(16)) register_2 (
    .D(alu_1_result), .en(rom_1_data[37]), .clk(clock_1_out), .Q(register_2_q));  // open: clr
  Register #(.width(16)) register_3 (
    .D(alu_1_carry_out), .en(rom_1_data[38]), .clk(clock_1_out), .Q(register_3_q));  // open: clr
  assign {controlled_buffer_3_out_2[4], controlled_buffer_3_out[3:0]} = rom_1_data[33] ? {5{1'b0}} : 5'bz;  // Controlled_Buffer controlled_buffer_3
  // Probe on alu_1_result
  ALU alu_1 (
    .opcode(controlled_buffer_3_out), .A(controlled_buffer_7_out), .B(controlled_buffer_8_out),
    .result(alu_1_result), .carry_out(alu_1_carry_out[0]));
  Register #(.width(16)) register_4 (
    .D(controlled_buffer_7_out), .en(rom_1_data[25]), .clk(clock_1_out), .Q(register_4_q));  // open: clr
  Register #(.width(16)) register_5 (
    .D(controlled_buffer_7_out), .en(rom_1_data[24]), .clk(clock_1_out), .Q(register_5_q));  // open: clr
  Register #(.width(16)) register_6 (
    .D(undriven), .en(rom_1_data[23]), .clk(clock_1_out), .Q(register_6_q));  // open: clr
  Register #(.width(16)) register_7 (
    .D(undriven), .en(rom_1_data[22]), .clk(clock_1_out), .Q(register_7_q));  // open: clr
  Register #(.width(5)) register_8 (
    .D(counter_1_q), .en(rom_1_data[15]), .clk(clock_1_out), .Q(register_8_q));  // open: clr
  Spliitter spliitter_1 (
    .Instruction(controlled_buffer_15_out), .WE(rom_1_data[11]), .clk(clock_1_out),
    .Add_B(spliitter_1_add_b), .Add_A(spliitter_1_add_a),
    .opcode({controlled_buffer_3_out_2[4], controlled_buffer_3_out[3:0]}), .flag(controlled_buffer_3_out[4]));
  // Probe on register_8_q
  Register #(.width(16)) register_9 (
    .D(undriven), .en(rom_1_data[21]), .clk(clock_1_out), .Q(register_9_q));  // open: clr
  // Probe on spliitter_1_add_b
  // Probe on spliitter_1_add_a
  assign register_5_q = rom_1_data[34] ? register_4_q : 16'bz;  // Controlled_Buffer controlled_buffer_4
  Register #(.width(16)) register_10 (
    .D(controlled_buffer_7_out), .en(rom_1_data[20]), .clk(clock_1_out), .Q(register_5_q));  // open: clr
  Register #(.width(16)) register_11 (
    .D(controlled_buffer_7_out), .en(rom_1_data[19]), .clk(clock_1_out), .Q(register_5_q));  // open: clr
  assign register_7_q = rom_1_data[35] ? register_6_q : 16'bz;  // Controlled_Buffer controlled_buffer_5
  Register #(.width(16)) register_12 (
    .D(undriven), .en(rom_1_data[18]), .clk(clock_1_out), .Q(register_7_q));  // open: clr
  assign register_7_q = rom_1_data[36] ? register_9_q : 16'bz;  // Controlled_Buffer controlled_buffer_6
  Register #(.width(5)) register_13 (
    .D(spliitter_1_add_a), .en(rom_1_data[16]), .clk(clock_1_out), .Q(register_13_q));  // open: clr
  // Probe on {controlled_buffer_3_out_2[4], controlled_buffer_3_out[3:0]}
  assign controlled_buffer_7_out = rom_1_data[26] ? register_5_q : 16'bz;  // Controlled_Buffer controlled_buffer_7
  assign controlled_buffer_8_out = rom_1_data[27] ? register_7_q : 16'bz;  // Controlled_Buffer controlled_buffer_8
  Register #(.width(16)) register_14 (.D(mat_mult_rom_1_out_10), .Q(register_14_q));  // open: en, clk, clr
  Register #(.width(16)) register_15 (.D(mat_mult_rom_1_out_12), .Q(register_15_q));  // open: en, clk, clr
  Clock clock_1 (.out(clock_1_out));
  Register #(.width(5)) register_16 (
    .D(spliitter_1_add_b), .en(rom_1_data[17]), .clk(clock_1_out), .Q(register_16_q));  // open: clr
  Controlled_Buffer #(.width(16)) controlled_buffer_9 (.in(register_14_q), .out(controlled_buffer_1_out));  // open: en
  Controlled_Buffer #(.width(16)) controlled_buffer_10 (.in(register_15_q), .out(controlled_buffer_1_out));  // open: en
  Counter #(.max('h1f), .width(5)) counter_2 (
    .up(1'b0), .clk(clock_1_out), .Q(counter_2_q));  // open: clr, load, count, D, carry
  mat_mult_rom mat_mult_rom_1 (
    .Register1(register_9_q), .Register5(register_5_q), .Register2(register_7_q), .Register7(register_6_q),
    .Register6(register_7_q), .Register8(register_5_q), .Register3(register_5_q),
    .out_10(mat_mult_rom_1_out_10), .out_11(mat_mult_rom_1_out_11), .out_12(mat_mult_rom_1_out_12),
    .out_13(mat_mult_rom_1_out_13));  // open: OE, Register4
  Register #(.width(16)) register_17 (.D(mat_mult_rom_1_out_11), .Q(register_17_q));  // open: en, clk, clr
  Register #(.width(16)) register_18 (.D(mat_mult_rom_1_out_13), .Q(register_18_q));  // open: en, clk, clr
  sharah_e_faisal sharah_e_faisal_2 ();  // open: OE, bit1, bit2, data_In, Ram_system, Ram_A, Ram_B
  Controlled_Buffer #(.width(16)) controlled_buffer_11 (.in(register_17_q), .out(controlled_buffer_1_out));  // open: en
  Controlled_Buffer #(.width(16)) controlled_buffer_12 (.in(register_18_q), .out(controlled_buffer_1_out));  // open: en
  Register #(.width(16)) register_19 (
    .D(ram_1_dout), .en(rom_1_data[10]), .clk(clock_1_out), .Q(register_19_q));  // open: clr
  Register #(.width(16)) register_20 (
    .D(ram_2_dout), .en(rom_1_data[9]), .clk(clock_1_out), .Q(register_20_q));  // open: clr
  Register #(.width(16)) register_21 (
    .D(ram_4_dout), .en(rom_1_data[8]), .clk(clock_1_out), .Q(register_21_q));  // open: clr
  assign controlled_buffer_7_out = rom_1_data[13] ? register_20_q : 16'bz;  // Controlled_Buffer controlled_buffer_13
  assign controlled_buffer_8_out = rom_1_data[12] ? register_21_q : 16'bz;  // Controlled_Buffer controlled_buffer_14
  assign controlled_buffer_15_out = rom_1_data[14] ? register_19_q : 16'bz;  // Controlled_Buffer controlled_buffer_15
  Controlled_Buffer #(.width(16)) controlled_buffer_16 (
    .in(controlled_buffer_8_out), .out(controlled_buffer_7_out));  // open: en
  // add_4 add_4_1: pin names not known; wires that end beside it: counter_2_q
  Controlled_Buffer #(.width(16)) controlled_buffer_17 (.in(ram_1_dout), .out(controlled_buffer_7_out));  // open: en
  Register #(.width(16)) register_22 (.D(controlled_buffer_7_out), .Q(controlled_buffer_1_out));  // open: en, clk, clr
  // Probe on register_8_q
  RAM #(.addrWidth(5), .dataWidth(16)) ram_1 (
    .addr(register_8_q), .we(rom_1_data[5]), .oe(rom_1_data[4]), .clk(clock_1_out),
    .din(controlled_buffer_15_out), .dout(ram_1_dout));
  // Probe on controlled_buffer_15_out
  RAM #(.addrWidth(5), .dataWidth(16)) ram_2 (
    .addr(register_13_q), .we(rom_1_data[0]), .oe(rom_1_data[1]), .clk(clock_1_out),
    .din(controlled_buffer_7_out), .dout(ram_2_dout));
  // Probe on ram_1_dout
  // Probe on ram_2_dout
  assign controlled_buffer_15_out = rom_1_data[42] ? undriven_2 : 16'bz;  // Controlled_Buffer controlled_buffer_18
  RAM #(.addrWidth(5), .dataWidth(16)) ram_3 (
    .addr(register_8_q), .we(rom_1_data[7]), .oe(rom_1_data[6]), .clk(clock_1_out),
    .din(controlled_buffer_15_out), .dout(ram_1_dout));
  RAM #(.addrWidth(5), .dataWidth(16)) ram_4 (
    .addr(register_16_q), .we(rom_1_data[3]), .oe(rom_1_data[2]), .clk(clock_1_out),
    .din(controlled_buffer_8_out), .dout(ram_4_dout));
  Register #(.width(16)) register_23 ();  // open: D, en, clk, Q, clr
  // Probe on ram_4_dout
  ROM #(.addrWidth(9), .dataWidth(62)) rom_1 (.addr({controlled_buffer_3_out[4], register_1_q_2}), .data(rom_1_data));
  Counter #(.max('hf), .width(4)) counter_3 (
    .clr(rom_1_data[43]), .up(1'b1), .count(1'b1), .clk(clock_1_out), .Q(register_1_q_2[3:0]));  // open: load, D, carry
  Counter #(.max('h1f), .width(5)) counter_4 ();  // open: clr, load, up, count, clk, D, carry, Q
  // Pins of 1 and 16 bits meet at alu_1_carry_out

  // Notes on the sheet:
  //   opcode
  //   alu register
  //   overflow
  //   Reg 5
  //   Reg 7
  //   MAR_Zero
  //   Reg 1
  //   Reg 3
  //   Reg 2
  //   Reg 6
  //   MAR_A
  //   Reg 4
  //   Reg 8
  //   MAR_B
  //   0fff mult
  //   MBR_B
  //   38
  //   MBR_Z
  //   MBR_A
  //   and
  //   xor
  //   07ff
  //   2bff
  //   2fff
  //   33ff
  //   18
  //   comp
  //   b8
  //   c8
  //   system reg
  //   add
  //   a8
  //   RAM_A
  //   Instruction_Ram
  //   System_Ram
  //   RAM_B
  //   8
  //   4
  //   2
  //   1
  //   8
  //   4
  //   2
  //   1
  //   8
  //   4
  //   2
  //   1
  //   8
  //   4
  //   2
  //   1
  //   8
  //   4
  //   2
  //   1
  //   8
  //   4
  //   2
  //   1
  //   8
  //   4
  //   2
  //   1
  //   8
  //   4
  //   2
  //   1
  //   8
  //   4
  //   2
  //   1
  //   8
  //   2
  //   1
  //   8
  //   4
  //   2
  //   1
  //   8
  //   4
  //   2
  //   1
  //   4
  //   contents of rom_1 (hex, n*v repeats v):
  //   0 82000000000 82000000000 1200000000 c0000000 60c000000000 60c000000000 8000 16*0 c00080400 40000
  //   100000000 10000000020 10 27*0 c00080400 40000 100000000 10000000020 10 107*0 c00080400 40000
  //   100000000 10000000020 10 11*0 c00080400 40000 100000000 10000000020 10 11*0 c00080400 40000
  //   100000000 10000000020 10
  //   zero pehle 
  //   8400800000
  //   8000E00000
  //   600000
  //   881800000000
  //   7800000000
  //   60FF000000
  //   20400120000
  //   b8
  //   c8
endmodule
module attempt_sixno (
  input  RAM_A_WE,
  input  RAM_A_OE,
  input  RAM_B_OE,
  input  RAM_B_WE,
  input  Inst_RAM_OE,
  input  Inst_RAM_WE,
  input  system_RAM_OE,
  input  system_RAM_WE,
  input  MBR_B_WE,
  input  MBR_A_WE,
  input  MBR_Z_WE,
  input  inst_splitter_we,
  input  MBR_B_CB,
  input  MBR_A_CB,
  input  MBR_Z_CB,
  input  MAR_Z_WE,
  input  MAR_A_WE,
  input  MAR_B_WE,
  input  reg_8_we,
  input  reg_4_we,
  input  reg_2_we,
  input  reg_6_we,
  input  reg_7_we,
  input  reg_5_we,
  input  reg_3_we,
  input  reg_1_we,
  input  reg_a_out_cb,
  input  reg_b_out_cb,
  input  Alu_out_cb,
  input  counter_increment_by_1,
  input  counter_increment_on,
  input  counter_reset,
  input  opcode_reg_we,
  input  opcode_init_cb,
  input  reg1_cb,
  input  reg5_cb,
  input  reg7_cb,
  input  Alu_register_we,
  input  overflow_reg_we,
  input  bus_select_oe,
  input  bus_select_bit1,
  input  bus_select_bit2,
  input  system_cb,
  input  reset_shit
);

  wire alu_1_carry_out, clock_1_out, not_1_out, undriven, undriven_2, undriven_3, undriven_4, undriven_5,
       undriven_6;
  wire [3:0] counter_3_q;
  wire [4:0] controlled_buffer_1_out, controlled_buffer_2_out, controlled_buffer_11_out, counter_1_q,
       counter_2_q, register_8_q, register_13_q, register_14_q, spliitter_1_add_a, spliitter_1_add_b;
  wire [4:4] controlled_buffer_1_out_2, controlled_buffer_1_out_3;
  wire [5:0] register_1_q;
  wire [15:0] alu_1_result, controlled_buffer_8_out, controlled_buffer_9_out, controlled_buffer_14_out,
       controlled_buffer_16_out, controlled_buffer_24_out, mat_mult_rom_1_out_10, mat_mult_rom_1_out_11,
       mat_mult_rom_1_out_12, mat_mult_rom_1_out_13, mux_for_mult_1_cout, ram_1_dout, ram_2_dout, ram_4_dout,
       register_2_q, register_4_q, register_5_q, register_6_q, register_7_q, register_9_q, register_15_q,
       register_16_q, register_17_q, register_18_q, register_19_q, sharah_e_faisal_1_ram_a,
       sharah_e_faisal_1_ram_b, sharah_e_faisal_1_ram_system;
  wire [63:0] rom_1_data;

  Counter #(.max('h1f), .width(5)) counter_1 (
    .clr(rom_1_data[31]), .up(1'b1), .count(rom_1_data[29]), .clk(clock_1_out), .Q(counter_1_q));  // open: load, D, carry
  Register #(.width(6)) register_1 (
    .D({controlled_buffer_1_out_2[4], controlled_buffer_1_out_3[4], controlled_buffer_1_out[3:0]}),
    .en(rom_1_data[32]), .clk(clock_1_out), .Q(register_1_q), .clr(rom_1_data[43]));
  Register #(.width(16)) register_2 (
    .D(alu_1_result), .en(rom_1_data[37]), .clk(clock_1_out), .Q(register_2_q));  // open: clr
  Register #(.width(1)) register_3 (.D(alu_1_carry_out), .en(rom_1_data[38]), .clk(clock_1_out));  // open: Q, clr
  assign {controlled_buffer_1_out_2[4], controlled_buffer_1_out_3[4], controlled_buffer_1_out[3:0]} = rom_1_data[33] ? {6{1'b0}} : 6'bz;  // Controlled_Buffer controlled_buffer_1
  assign controlled_buffer_2_out = undriven ? counter_1_q : 5'bz;  // Controlled_Buffer controlled_buffer_2
  // Probe on alu_1_result
  ALU alu_1 (
    .opcode({controlled_buffer_1_out_2[4], controlled_buffer_1_out[3:0]}), .A(controlled_buffer_8_out),
    .B(controlled_buffer_9_out), .result(alu_1_result), .carry_out(alu_1_carry_out));
  Register #(.width(16)) register_4 (
    .D(controlled_buffer_8_out), .en(rom_1_data[25]), .clk(clock_1_out), .Q(register_4_q));  // open: clr
  Register #(.width(16)) register_5 (
    .D(controlled_buffer_8_out), .en(rom_1_data[24]), .clk(clock_1_out), .Q(register_5_q));  // open: clr
  Register #(.width(16)) register_6 (
    .D(controlled_buffer_9_out), .en(rom_1_data[23]), .clk(clock_1_out), .Q(register_6_q));  // open: clr
  Register #(.width(16)) register_7 (
    .D(controlled_buffer_9_out), .en(rom_1_data[22]), .clk(clock_1_out), .Q(register_7_q));  // open: clr
  Controlled_Buffer #(.width(5)) controlled_buffer_3 (.in(register_14_q), .out(controlled_buffer_2_out));  // open: en
  Register #(.width(5)) register_8 (
    .D(controlled_buffer_2_out), .en(rom_1_data[15]), .clk(clock_1_out), .Q(register_8_q));  // open: clr
  Spliitter spliitter_1 (
    .Instruction(controlled_buffer_16_out), .WE(rom_1_data[11]), .clk(clock_1_out),
    .Add_B(spliitter_1_add_b), .Add_A(spliitter_1_add_a), .opcode(controlled_buffer_1_out),
    .flag(controlled_buffer_1_out_2[4]));
  // Probe on register_8_q
  // Probe on spliitter_1_add_b
  Register #(.width(16)) register_9 (
    .D(controlled_buffer_9_out), .en(rom_1_data[21]), .clk(clock_1_out), .Q(register_9_q));  // open: clr
  Counter #(.max('h1f), .width(5)) counter_2 (
    .clr(undriven_2), .up(1'b0), .count(undriven_3), .clk(clock_1_out), .Q(counter_2_q));  // open: load, D, carry
  // Probe on spliitter_1_add_a
  assign register_5_q = rom_1_data[34] ? register_4_q : 16'bz;  // Controlled_Buffer controlled_buffer_4
  Register #(.width(16)) register_10 (
    .D(controlled_buffer_8_out), .en(rom_1_data[20]), .clk(clock_1_out), .Q(register_5_q));  // open: clr
  Register #(.width(16)) register_11 (
    .D(controlled_buffer_8_out), .en(rom_1_data[19]), .clk(clock_1_out), .Q(register_5_q));  // open: clr
  assign register_7_q = rom_1_data[35] ? register_6_q : 16'bz;  // Controlled_Buffer controlled_buffer_5
  Register #(.width(16)) register_12 (
    .D(controlled_buffer_9_out), .en(rom_1_data[18]), .clk(clock_1_out), .Q(register_7_q));  // open: clr
  Register #(.width(5)) register_13 (
    .D(controlled_buffer_2_out), .en(rom_1_data[16]), .clk(clock_1_out), .Q(register_13_q));  // open: clr
  Controlled_Buffer #(.width(5)) controlled_buffer_6 (
    .in(spliitter_1_add_a), .out(controlled_buffer_2_out));  // open: en
  assign register_7_q = rom_1_data[36] ? register_9_q : 16'bz;  // Controlled_Buffer controlled_buffer_7
  assign controlled_buffer_8_out = rom_1_data[26] ? register_5_q : 16'bz;  // Controlled_Buffer controlled_buffer_8
  assign controlled_buffer_9_out = rom_1_data[27] ? register_7_q : 16'bz;  // Controlled_Buffer controlled_buffer_9
  Controlled_Buffer #(.width(5)) controlled_buffer_10 (.in(counter_2_q), .out(controlled_buffer_2_out));  // open: en
  Controlled_Buffer #(.width(5)) controlled_buffer_11 (
    .in(controlled_buffer_2_out), .out(controlled_buffer_11_out));  // open: en
  Register #(.width(5)) register_14 (
    .D(controlled_buffer_11_out), .en(rom_1_data[17]), .clk(clock_1_out), .Q(register_14_q));  // open: clr
  Controlled_Buffer #(.width(5)) controlled_buffer_12 (
    .in(spliitter_1_add_b), .out(controlled_buffer_11_out));  // open: en
  Clock clock_1 (.out(clock_1_out));
  mat_mult_rom mat_mult_rom_1 (
    .Register1(register_4_q), .Register5(register_6_q), .Register2(register_5_q), .Register7(register_7_q),
    .Register6(register_9_q), .Register8(register_7_q), .Register3(register_5_q), .Register4(register_5_q),
    .out_10(mat_mult_rom_1_out_10), .out_11(mat_mult_rom_1_out_11), .out_12(mat_mult_rom_1_out_12),
    .out_13(mat_mult_rom_1_out_13));  // open: OE
  mux_for_mult mux_for_mult_1 (
    .A(mat_mult_rom_1_out_10), .B(mat_mult_rom_1_out_11), .C(mat_mult_rom_1_out_12),
    .D(mat_mult_rom_1_out_13), .cout(mux_for_mult_1_cout));  // open: cb_1, cb_2
  sharah_e_faisal sharah_e_faisal_1 (
    .OE(rom_1_data[39]), .bit1(rom_1_data[40]), .bit2(rom_1_data[41]), .data_In(register_2_q),
    .Ram_system(sharah_e_faisal_1_ram_system), .Ram_A(sharah_e_faisal_1_ram_a),
    .Ram_B(sharah_e_faisal_1_ram_b));
  Controlled_Buffer #(.width(16)) controlled_buffer_13 (.in(mux_for_mult_1_cout), .out(register_2_q));  // open: en
  Controlled_Buffer #(.width(16)) controlled_buffer_14 (
    .in(sharah_e_faisal_1_ram_a), .out(controlled_buffer_14_out));  // open: en
  Controlled_Buffer #(.width(16)) controlled_buffer_15 (
    .in(sharah_e_faisal_1_ram_b), .out(controlled_buffer_14_out));  // open: en
  Register #(.width(16)) register_15 (
    .D(controlled_buffer_24_out), .en(rom_1_data[10]), .clk(clock_1_out), .Q(register_15_q));  // open: clr
  Register #(.width(16)) register_16 (
    .D(ram_2_dout), .en(rom_1_data[9]), .clk(clock_1_out), .Q(register_16_q));  // open: clr
  Register #(.width(16)) register_17 (
    .D(ram_4_dout), .en(rom_1_data[8]), .clk(clock_1_out), .Q(register_17_q));  // open: clr
  assign controlled_buffer_16_out = rom_1_data[14] ? register_15_q : 16'bz;  // Controlled_Buffer controlled_buffer_16
  assign controlled_buffer_8_out = rom_1_data[13] ? register_16_q : 16'bz;  // Controlled_Buffer controlled_buffer_17
  assign controlled_buffer_9_out = rom_1_data[12] ? register_17_q : 16'bz;  // Controlled_Buffer controlled_buffer_18
  Register #(.width(16)) register_18 (.D(controlled_buffer_14_out), .Q(register_18_q));  // open: en, clk, clr
  assign controlled_buffer_8_out = undriven_4 ? register_18_q : 16'bz;  // Controlled_Buffer controlled_buffer_19
  Controlled_Buffer #(.width(5)) controlled_buffer_20 (.out(register_8_q), .en(undriven));  // open: in
  // Probe on register_8_q
  // Probe on controlled_buffer_16_out
  RAM #(.addrWidth(5), .dataWidth(16)) ram_1 (
    .addr(register_8_q), .we(rom_1_data[5]), .oe(rom_1_data[4]), .clk(clock_1_out),
    .din(controlled_buffer_16_out), .dout(ram_1_dout));
  RAM #(.addrWidth(5), .dataWidth(16)) ram_2 (
    .addr(register_13_q), .we(rom_1_data[0]), .oe(rom_1_data[1]), .clk(clock_1_out),
    .din(controlled_buffer_8_out), .dout(ram_2_dout));
  Controlled_Buffer #(.width(16)) controlled_buffer_21 (
    .in(controlled_buffer_8_out), .out(controlled_buffer_9_out));  // open: en
  assign register_2_q = undriven_5 ? register_17_q : 16'bz;  // Controlled_Buffer controlled_buffer_22
  assign register_2_q = undriven_6 ? register_16_q : 16'bz;  // Controlled_Buffer controlled_buffer_23
  // Probe on ram_1_dout
  Controlled_Buffer #(.width(16)) controlled_buffer_24 (.in(ram_1_dout), .out(controlled_buffer_24_out));  // open: en
  // Probe on ram_2_dout
  RAM #(.addrWidth(5), .dataWidth(16)) ram_3 (
    .addr(register_8_q), .we(rom_1_data[7]), .oe(rom_1_data[6]), .clk(clock_1_out), .din(register_19_q),
    .dout(controlled_buffer_24_out));
  RAM #(.addrWidth(5), .dataWidth(16)) ram_4 (
    .addr(register_14_q), .we(rom_1_data[3]), .oe(rom_1_data[2]), .clk(clock_1_out),
    .din(controlled_buffer_9_out), .dout(ram_4_dout));
  Controlled_Buffer #(.width(16)) controlled_buffer_25 (
    .in(controlled_buffer_16_out), .out(controlled_buffer_8_out));  // open: en
  Register #(.width(16)) register_19 (
    .D(sharah_e_faisal_1_ram_system), .clk(clock_1_out), .Q(register_19_q));  // open: en, clr
  // Probe on ram_4_dout
  ROM #(.addrWidth(9), .dataWidth(64)) rom_1 (
    .addr({register_1_q[5], register_1_q[3:0], counter_3_q}), .data(rom_1_data));
  not not_1 (not_1_out, rom_1_data[63]);
  assign clock_1_out = rom_1_data[63] ? not_1_out : 1'bz;  // Controlled_Buffer controlled_buffer_26
  Counter #(.max('hf), .width(4)) counter_3 (
    .clr(rom_1_data[43]), .up(1'b1), .count(1'b1), .clk(clock_1_out), .Q(counter_3_q));  // open: load, D, carry
  // also tied to GND on the sheet: {controlled_buffer_1_out_3[4], register_1_q[4]}

  // Notes on the sheet:
  //   opcode
  //   alu register
  //   overflow
  //   Reg 5
  //   Reg 7
  //   MAR_Zero
  //   Reg 1
  //   Reg 3
  //   Reg 2
  //   Reg 6
  //   MAR_A
  //   Reg 4
  //   Reg 8
  //   MAR_B
  //   0fff mult
  //   MBR_A
  //   MBR_B
  //   38
  //   MBR_Z
  //   and
  //   xor
  //   07ff
  //   2bff
  //   2fff
  //   33ff
  //   add
  //   18
  //   comp
  //   b8
  //   c8
  //   a8
  //   RAM_A
  //   Instruction_Ram
  //   RAM_B
  //   System_Ram
  //   8
  //   4
  //   2
  //   1
  //   8
  //   4
  //   2
  //   1
  //   8
  //   4
  //   system
  //   8
  //   4
  //   2
  //   1
  //   8
  //   4
  //   2
  //   1
  //   8
  //   4
  //   2
  //   1
  //   2
  //   1
  //   8
  //   4
  //   2
  //   1
  //   8
  //   4
  //   2
  //   2
  //   1
  //   8
  //   4
  //   2
  //   1
  //   8
  //   4
  //   2
  //   1
  //   8
  //   4
  //   2
  //   1
  //   8
  //   4
  //   1
  //   contents of rom_1 (hex, n*v repeats v):
  //   0 82000000000 82000000000 1200000000 c0000000 60c000000000 60c000000000 8000 16*0 c00080400 40000
  //   100000000 10000000020 10
  //   zero pehle 
  //   20400120000
  //   8400800000
  //   8000E00000
  //   600000
  //   881800000000
  //   7800000000
  //   60FF000000
  //   b8
  //   c8
endmodule

module mux_for_mult (
  input  [15:0] A,
  input  [15:0] B,
  input  [15:0] C,
  input  [15:0] D,
  input  cb_1,
  input  cb_2,
  output [15:0] cout
);

  wire [15:0] and_1_out, and_2_out, and_3_out, and_4_out, bit_extender_1_out, bit_extender_2_out, not_1_out,
       not_2_out;

  assign bit_extender_1_out = {{15{cb_1}}, cb_1};  // Bit_Extender bit_extender_1
  assign bit_extender_2_out = {{15{cb_2}}, cb_2};  // Bit_Extender bit_extender_2
  assign not_1_out = ~bit_extender_2_out;  // NOT_Gate not_1, 16 bits wide
  assign not_2_out = ~bit_extender_1_out;  // NOT_Gate not_2, 16 bits wide
  assign and_1_out = not_1_out & not_2_out & A;  // AND_Gate and_1, 16 bits wide
  assign and_2_out = not_1_out & bit_extender_1_out & B;  // AND_Gate and_2, 16 bits wide
  assign and_3_out = bit_extender_2_out & not_2_out & C;  // AND_Gate and_3, 16 bits wide
  assign and_4_out = bit_extender_2_out & bit_extender_1_out & D;  // AND_Gate and_4, 16 bits wide
  assign cout = and_1_out | and_2_out | and_3_out | and_4_out;  // OR_Gate or_1, 16 bits wide
endmodule

module terminus_uno (
  input  temp_reg_cb,
  input  [15:0] mbr_a,
  input  [15:0] mbr_b,
  output [15:0] temp_reg_out
);

  wire [15:0] and_1_out, and_2_out, bit_extender_1_out, not_1_out;

  assign bit_extender_1_out = {{15{temp_reg_cb}}, temp_reg_cb};  // Bit_Extender bit_extender_1
  assign not_1_out = ~bit_extender_1_out;  // NOT_Gate not_1, 16 bits wide
  assign and_1_out = mbr_a & not_1_out;  // AND_Gate and_1, 16 bits wide
  assign and_2_out = mbr_b & bit_extender_1_out;  // AND_Gate and_2, 16 bits wide
  assign temp_reg_out = and_1_out | and_2_out;  // OR_Gate or_1, 16 bits wide
endmodule

module terminus_des (
  input  temp_reg_cb,
  input  [15:0] mbr_z,
  output [15:0] ram_a,
  output [15:0] ram_b
);

  wire [15:0] bit_extender_1_out, not_1_out;

  assign bit_extender_1_out = {{15{temp_reg_cb}}, temp_reg_cb};  // Bit_Extender bit_extender_1
  assign not_1_out = ~bit_extender_1_out;  // NOT_Gate not_1, 16 bits wide
  assign ram_a = mbr_z & not_1_out;  // AND_Gate and_1, 16 bits wide
  assign ram_b = mbr_z & bit_extender_1_out;  // AND_Gate and_2, 16 bits wide
endmodule

module J_16_Core (
  input  RAM_A_WE,
  input  RAM_A_OE,
  input  RAM_B_OE,
  input  RAM_B_WE,
  input  Inst_RAM_OE,
  input  Inst_RAM_WE,
  input  system_RAM_OE,
  input  system_RAM_WE,
  input  MBR_B_WE,
  input  MBR_A_WE,
  input  MBR_Z_WE,
  input  inst_splitter_we,
  input  MBR_B_CB,
  input  MBR_A_CB,
  input  MBR_Z_CB,
  input  MAR_Z_WE,
  input  MAR_A_WE,
  input  MAR_B_WE,
  input  reg_8_we,
  input  reg_4_we,
  input  reg_2_we,
  input  reg_6_we,
  input  reg_7_we,
  input  reg_5_we,
  input  reg_3_we,
  input  reg_1_we,
  input  reg_a_out_cb,
  input  halt_maybe,
  input  reg_b_out_cb,
  input  Alu_out_cb,
  input  counter_increment_by_1,
  input  counter_increment_on,
  input  decode_cb_ramb,
  input  counter_reset,
  input  opcode_reg_we,
  input  opcode_init_cb,
  input  reg1_cb,
  input  reg5_cb,
  input  reg7_cb,
  input  Alu_register_we,
  input  overflow_reg_we,
  input  bus_select_oe,
  input  bus_select_bit1,
  input  bus_select_bit2,
  input  inst_ram_cb,
  input  reset_shit,
  input  decode_cb_rama,
  input  decode_control,
  input  temp_reg_confl,
  input  temp_reg_cb_mux,
  input  mux_control,
  input  temp_reg_we,
  input  program_counter_cb,
  input  ram_increment,
  input  ram_increment_Cb,
  input  system_reg_we,
  input  mar_a_cb,
  input  mar_b_cb,
  input  mar_b_conf_cb,
  input  mat_mult_oe,
  input  matrix_mux_cb,
  input  ramb_bustrm_cb,
  input  rama_bustrm_cb,
  input  mat_mux_cb_2,
  input  mat_mux_cb_1,
  input  mar_b_conf_2
);

  wire alu_1_carry_out, clock_1_out, not_1_out;
  wire [3:0] counter_3_q;
  wire [4:0] controlled_buffer_1_out, controlled_buffer_2_out, controlled_buffer_12_out, counter_1_q,
       counter_2_q, register_8_q, register_13_q, register_14_q, spliitter_1_add_a, spliitter_1_add_b;
  wire [4:4] controlled_buffer_1_out_2, controlled_buffer_1_out_3;
  wire [5:0] register_1_q;
  wire [15:0] alu_1_result, controlled_buffer_3_out, controlled_buffer_9_out, controlled_buffer_10_out,
       controlled_buffer_15_out, controlled_buffer_17_out, controlled_buffer_24_out,
       controlled_buffer_25_out, mat_mult_fix_1_out_10, mat_mult_fix_1_out_11, mat_mult_fix_1_out_12,
       mat_mult_fix_1_out_13, mem_swap_temp_reg_out, mux_for_mult_1_cout, ram_1_dout, ram_2_dout, ram_4_dout,
       register_2_q, register_4_q, register_5_q, register_6_q, register_7_q, register_9_q, register_15_q,
       register_16_q, register_17_q, register_18_q, sharah_e_faisal_1_ram_a, sharah_e_faisal_1_ram_b,
       sharah_e_faisal_1_ram_system, Temp_reg_q, terminus_des_1_ram_a, terminus_des_1_ram_b;
  wire [63:0] rom_1_data;

  Counter #(.max('h1f), .width(5)) counter_1 (
    .up(1'b1), .count(rom_1_data[34]), .clk(clock_1_out), .Q(counter_1_q));  // open: clr, load, D, carry
  Register #(.width(6)) register_1 (
    .D({controlled_buffer_1_out_2[4], controlled_buffer_1_out_3[4], controlled_buffer_1_out[3:0]}),
    .en(rom_1_data[31]), .clk(clock_1_out), .Q(register_1_q), .clr(rom_1_data[20]));
  Register #(.width(16)) register_2 (
    .D(controlled_buffer_3_out), .en(rom_1_data[26]), .clk(clock_1_out), .Q(register_2_q));  // open: clr
  Register #(.width(1)) register_3 (.D(alu_1_carry_out), .en(rom_1_data[25]), .clk(clock_1_out));  // open: Q, clr
  assign {controlled_buffer_1_out_2[4], controlled_buffer_1_out_3[4], controlled_buffer_1_out[3:0]} = rom_1_data[30] ? {6{1'b0}} : 6'bz;  // Controlled_Buffer controlled_buffer_1
  assign controlled_buffer_2_out = rom_1_data[13] ? counter_1_q : 5'bz;  // Controlled_Buffer controlled_buffer_2
  // Probe on alu_1_result
  assign controlled_buffer_3_out = rom_1_data[35] ? alu_1_result : 16'bz;  // Controlled_Buffer controlled_buffer_3
  ALU alu_1 (
    .opcode({controlled_buffer_1_out_2[4], controlled_buffer_1_out[3:0]}), .A(controlled_buffer_9_out),
    .B(controlled_buffer_10_out), .result(alu_1_result), .carry_out(alu_1_carry_out));
  Register #(.width(16)) register_4 (
    .D(controlled_buffer_9_out), .en(rom_1_data[38]), .clk(clock_1_out), .Q(register_4_q));  // open: clr
  Register #(.width(16)) register_5 (
    .D(controlled_buffer_9_out), .en(rom_1_data[39]), .clk(clock_1_out), .Q(register_5_q));  // open: clr
  Register #(.width(16)) register_6 (
    .D(controlled_buffer_10_out), .en(rom_1_data[40]), .clk(clock_1_out), .Q(register_6_q));  // open: clr
  Register #(.width(16)) register_7 (
    .D(controlled_buffer_10_out), .en(rom_1_data[41]), .clk(clock_1_out), .Q(register_7_q));  // open: clr
  assign controlled_buffer_2_out = rom_1_data[0] ? register_14_q : 5'bz;  // Controlled_Buffer controlled_buffer_4
  Register #(.width(5)) register_8 (
    .D(controlled_buffer_2_out), .en(rom_1_data[48]), .clk(clock_1_out), .Q(register_8_q));  // open: clr
  Spliitter spliitter_1 (
    .Instruction(controlled_buffer_17_out), .WE(rom_1_data[52]), .clk(clock_1_out),
    .Add_B(spliitter_1_add_b), .Add_A(spliitter_1_add_a), .opcode(controlled_buffer_1_out),
    .flag(controlled_buffer_1_out_2[4]));
  // Probe on register_8_q
  // Probe on spliitter_1_add_b
  // Probe on controlled_buffer_1_out
  Register #(.width(16)) register_9 (
    .D(controlled_buffer_10_out), .en(rom_1_data[42]), .clk(clock_1_out), .Q(register_9_q));  // open: clr
  Counter #(.max('h1f), .width(5)) counter_2 (
    .clr(rom_1_data[32]), .up(1'b0), .count(rom_1_data[12]), .clk(clock_1_out), .Q(counter_2_q));  // open: load, D, carry
  // Probe on spliitter_1_add_a
  assign register_5_q = rom_1_data[29] ? register_4_q : 16'bz;  // Controlled_Buffer controlled_buffer_5
  Register #(.width(16)) register_10 (
    .D(controlled_buffer_9_out), .en(rom_1_data[43]), .clk(clock_1_out), .Q(register_5_q));  // open: clr
  Register #(.width(16)) register_11 (
    .D(controlled_buffer_9_out), .en(rom_1_data[44]), .clk(clock_1_out), .Q(register_5_q));  // open: clr
  assign register_7_q = rom_1_data[28] ? register_6_q : 16'bz;  // Controlled_Buffer controlled_buffer_6
  Register #(.width(16)) register_12 (
    .D(controlled_buffer_10_out), .en(rom_1_data[45]), .clk(clock_1_out), .Q(register_7_q));  // open: clr
  Register #(.width(5)) register_13 (
    .D(controlled_buffer_2_out), .en(rom_1_data[47]), .clk(clock_1_out), .Q(register_13_q));  // open: clr
  assign controlled_buffer_2_out = rom_1_data[9] ? spliitter_1_add_a : 5'bz;  // Controlled_Buffer controlled_buffer_7
  assign register_7_q = rom_1_data[27] ? register_9_q : 16'bz;  // Controlled_Buffer controlled_buffer_8
  // Probe on register_2_q
  Controlled_Buffer #(.width(16)) controlled_buffer_9 (.in(register_5_q), .out(controlled_buffer_9_out));  // open: en
  assign controlled_buffer_10_out = rom_1_data[36] ? register_7_q : 16'bz;  // Controlled_Buffer controlled_buffer_10
  assign controlled_buffer_2_out = rom_1_data[11] ? counter_2_q : 5'bz;  // Controlled_Buffer controlled_buffer_11
  assign controlled_buffer_12_out = rom_1_data[7] ? controlled_buffer_2_out : 5'bz;  // Controlled_Buffer controlled_buffer_12
  Register #(.width(5)) register_14 (
    .D(controlled_buffer_12_out), .en(rom_1_data[46]), .clk(clock_1_out), .Q(register_14_q));  // open: clr
  assign controlled_buffer_12_out = rom_1_data[8] ? spliitter_1_add_b : 5'bz;  // Controlled_Buffer controlled_buffer_13
  Clock clock_1 (.out(clock_1_out));
  mat_mult_fix mat_mult_fix_1 (
    .OE(rom_1_data[6]), .reg_1(register_4_q), .reg_5(register_6_q), .reg_2(register_5_q),
    .reg_7(register_7_q), .reg_6(register_9_q), .reg_8(register_7_q), .reg_3(register_5_q),
    .reg_4(register_5_q), .out_10(mat_mult_fix_1_out_10), .out_11(mat_mult_fix_1_out_11),
    .out_12(mat_mult_fix_1_out_12), .out_13(mat_mult_fix_1_out_13));
  mux_for_mult mux_for_mult_1 (
    .A(mat_mult_fix_1_out_10), .B(mat_mult_fix_1_out_11), .C(mat_mult_fix_1_out_12),
    .D(mat_mult_fix_1_out_13), .cb_1(rom_1_data[1]), .cb_2(rom_1_data[2]), .cout(mux_for_mult_1_cout));
  sharah_e_faisal sharah_e_faisal_1 (
    .OE(rom_1_data[24]), .bit1(rom_1_data[23]), .bit2(rom_1_data[22]), .data_In(register_2_q),
    .Ram_system(sharah_e_faisal_1_ram_system), .Ram_A(sharah_e_faisal_1_ram_a),
    .Ram_B(sharah_e_faisal_1_ram_b));
  assign register_2_q = rom_1_data[5] ? mux_for_mult_1_cout : 16'bz;  // Controlled_Buffer controlled_buffer_14
  assign controlled_buffer_15_out = rom_1_data[3] ? sharah_e_faisal_1_ram_a : 16'bz;  // Controlled_Buffer controlled_buffer_15
  assign controlled_buffer_15_out = rom_1_data[4] ? sharah_e_faisal_1_ram_b : 16'bz;  // Controlled_Buffer controlled_buffer_16
  Register #(.width(16)) register_15 (
    .D(controlled_buffer_24_out), .en(rom_1_data[53]), .clk(clock_1_out), .Q(register_15_q));  // open: clr
  Register #(.width(16)) register_16 (
    .D(ram_2_dout), .en(rom_1_data[54]), .clk(clock_1_out), .Q(register_16_q));  // open: clr
  Register #(.width(16)) register_17 (
    .D(ram_4_dout), .en(rom_1_data[55]), .clk(clock_1_out), .Q(register_17_q));  // open: clr
  // Probe on mux_for_mult_1_cout
  assign controlled_buffer_17_out = rom_1_data[49] ? register_15_q : 16'bz;  // Controlled_Buffer controlled_buffer_17
  assign controlled_buffer_9_out = rom_1_data[50] ? register_16_q : 16'bz;  // Controlled_Buffer controlled_buffer_18
  assign controlled_buffer_10_out = rom_1_data[51] ? register_17_q : 16'bz;  // Controlled_Buffer controlled_buffer_19
  Register #(.width(16)) Temp_reg (
    .D(controlled_buffer_15_out), .en(rom_1_data[14]), .clk(clock_1_out), .Q(Temp_reg_q));  // open: clr
  assign controlled_buffer_9_out = rom_1_data[16] ? Temp_reg_q : 16'bz;  // Controlled_Buffer controlled_buffer_20
  Controlled_Buffer #(.width(5)) controlled_buffer_21 (.out(register_8_q), .en(rom_1_data[13]));  // open: in
  // Probe on register_8_q
  // Probe on controlled_buffer_17_out
  RAM #(.addrWidth(5), .dataWidth(16), .\type ("nonvolatile")) ram_1 (
    .addr(register_8_q), .we(rom_1_data[58]), .oe(rom_1_data[59]), .clk(clock_1_out),
    .din(controlled_buffer_17_out), .dout(ram_1_dout));
  RAM #(.addrWidth(5), .dataWidth(16), .\type ("nonvolatile")) ram_2 (
    .addr(register_13_q), .we(rom_1_data[63]), .oe(rom_1_data[62]), .clk(clock_1_out),
    .din(controlled_buffer_9_out), .dout(ram_2_dout));
  assign controlled_buffer_10_out = rom_1_data[17] ? controlled_buffer_9_out : 16'bz;  // Controlled_Buffer controlled_buffer_22
  // Probe on Temp_reg_q
  terminus_uno mem_swap (
    .temp_reg_cb(rom_1_data[15]), .mbr_a(register_16_q), .mbr_b(register_17_q),
    .temp_reg_out(mem_swap_temp_reg_out));
  assign register_2_q = rom_1_data[16] ? mem_swap_temp_reg_out : 16'bz;  // Controlled_Buffer controlled_buffer_23
  // Probe on ram_1_dout
  assign controlled_buffer_24_out = rom_1_data[21] ? ram_1_dout : 16'bz;  // Controlled_Buffer controlled_buffer_24
  // Probe on ram_2_dout
  assign controlled_buffer_25_out = rom_1_data[33] ? terminus_des_1_ram_b : 16'bz;  // Controlled_Buffer controlled_buffer_25
  RAM #(.addrWidth(5), .dataWidth(16)) ram_3 (
    .addr(register_8_q), .we(rom_1_data[56]), .oe(rom_1_data[57]), .clk(clock_1_out), .din(register_18_q),
    .dout(controlled_buffer_24_out));
  // Probe on register_18_q
  RAM #(.addrWidth(5), .dataWidth(16), .\type ("nonvolatile")) ram_4 (
    .addr(register_14_q), .we(rom_1_data[60]), .oe(rom_1_data[61]), .clk(clock_1_out),
    .din(controlled_buffer_10_out), .dout(ram_4_dout));
  terminus_des terminus_des_1 (
    .temp_reg_cb(rom_1_data[18]), .mbr_z(controlled_buffer_17_out), .ram_a(terminus_des_1_ram_a),
    .ram_b(terminus_des_1_ram_b));
  assign controlled_buffer_9_out = rom_1_data[19] ? terminus_des_1_ram_a : 16'bz;  // Controlled_Buffer controlled_buffer_26
  Register #(.width(16)) register_18 (
    .D(sharah_e_faisal_1_ram_system), .en(rom_1_data[10]), .clk(clock_1_out), .Q(register_18_q));  // open: clr
  // Probe on ram_4_dout
  ROM #(.addrWidth(9), .dataWidth(64)) rom_1 (
    .addr({register_1_q[5], register_1_q[3:0], counter_3_q}), .data(rom_1_data));
  not not_1 (not_1_out, rom_1_data[37]);
  assign clock_1_out = rom_1_data[37] ? not_1_out : 1'bz;  // Controlled_Buffer controlled_buffer_27
  Counter #(.max('hf), .width(4)) counter_3 (
    .clr(rom_1_data[20]), .up(1'b1), .count(1'b1), .clk(clock_1_out), .Q(counter_3_q));  // open: load, D, carry
  // also tied to GND on the sheet: {controlled_buffer_1_out_3[4], register_1_q[4]}

  // Notes on the sheet:
  //   program counter for instruction ram
  //   opcode
  //   alu register
  //   overflow
  //   couldn't complete 
  //   as of yet
  //   Reg 5
  //   Reg 7
  //   MAR_Zero
  //   Reg 1
  //   Reg 3
  //   Reg 2
  //   RAM counter for the system ram
  //   Reg 6
  //   MAR_A
  //   Reg 4
  //   Reg 8
  //   MAR_B
  //   depending on the output
  //   turn on the control bits
  //   of the mux
  //   00 for A
  //   10 for B
  //   01 for C
  //   11 for D
  //   bit 2 system
  //   bit 1 ram a
  //   bit 1 and 2 ram b
  //   MBR_A
  //   MBR_B
  //   MBR_Z
  //   waste of time
  //   Instruction_Ram
  //   RAM_A
  //   move
  //   System_Ram
  //   0
  //   0
  //   0
  //   0
  //   0
  //   0
  //   0
  //   RAM_B
  //   8
  //   4
  //   2
  //   1
  //   8
  //   4
  //   2
  //   1
  //   8
  //   4
  //   system
  //   8
  //   4
  //   2
  //   1
  //   8
  //   4
  //   2
  //   1
  //   8
  //   4
  //   2
  //   1
  //   2
  //   1
  //   8
  //   4
  //   2
  //   1
  //   8
  //   4
  //   2
  //   2
  //   1
  //   8
  //   4
  //   2
  //   move system ram to ram a
  //   mem swap ram_a to ram_b
  //   1
  //   8
  //   4
  //   2
  //   1
  //   8
  //   4
  //   2
  //   1
  //   8
  //   4
  //   1
  //   8
  //   4
  //   2
  //   1
  //   8
  //   4
  //   2
  //   1
  //   8
  //   4
  //   2
  //   1
  //   8
  //   4
  //   halt_but_no_sucess
  //   contents of rom_1 (hex, n*v repeats v):
  //   0 820000000200000 820000000200000 12000000000000 c00000000300 60c0000000000300 60c0000000000300
  //   80000000 16*0 c000806000000 400002000 1000000002000 100000 28*0 c000806000000 400002000
  //   1000000002000 100000 12*0 1000800400200 801400400 100000800002000 1000400002000 1000000002000 100000
  //   10*0 1c14010 1000000000030000 181c008 8000000000010000 400002000 1000000002000 100000 25*0
  //   cc14000001880 c00000000880 60c0c00000000880 60c0c00000000880 ccc0000001880 c00000000880
  //   60c0c00000000880 60c0c00000000880 cc28000001880 c00000000880 60c0c00000000880 60c0c00000000880
  //   cf00000001880 400002000 1000000002000 100000 1400460 100000001401862 1000001400c62 100000001401864
  //   1000001400c64 100000001401866 1000001400c66 100000400002000 1000000002000 100000 6*0 400002040
  //   1000000002040 100040 13*0 c000806000000 400002000 1000000002000 100000 12*0 c000806000000 400002000
  //   1000000002000 100000 12*0 c000806000000 400002000 1000000002000 100000 12*0 c000806000000 400002000
  //   1000000002000 100000 28*0 1000000000001 220000000000000 220000000000000 8002000000080000 400002000
  //   1000000002000 100000 25*0 c000806000000 400002000 1000000002000 100000 204*0 2000000000 15*0
  //   1000000000080 220000000000000 220000000000000 10080000000c0000 100000
  //   zero pehle 
  //   20400120000
  //   8400800000
  //   8000E00000
  //   600000
  //   881800000000
  //   7800000000
  //   60FF000000
  //   00001 add
  //   00011 mult
  //   01010 comp
  //   01011 and
  //   01100 xor
  //   01101 not
  //   10001 sub
  //   01001 mat mult
  //   00111 block load
  //   01000 block store
  //   00101 mem swap
  //   01111 move w/o flag
  //   00100 store
  //   01110 nop
  //   18
  //   38
  //   a8
  //   b8
  //   c8
  //   d8
  //   118
  //   98
  //   78
  //   88
  //   58
  //   48
  //   1e8
  //   11110 halt
  //   0e8
  //   f8
  //   rom incrementer
endmodule

module bus_ke_maslay (
  input  OE,
  input  bit1,
  input  bit2,
  input  data_In,
  output Ram_system,
  output Ram_A,
  output Ram_B
);

  wire and_1_out, and_2_out, and_3_out, and_4_out, and_5_out, not_1_out, not_2_out;

  not not_1 (not_1_out, bit1);
  not not_2 (not_2_out, bit2);
  and and_1 (and_1_out, not_1_out, data_In, not_2_out);
  and and_2 (and_2_out, not_1_out, data_In, bit2);
  and and_3 (and_3_out, bit1, data_In, not_2_out);
  and and_4 (and_4_out, bit1, data_In, bit2);
  and and_5 (and_5_out, and_1_out, OE);
  and and_6 (Ram_system, and_2_out, OE);
  and and_7 (Ram_A, and_3_out, OE);
  and and_8 (Ram_B, and_4_out, OE);

  // Notes on the sheet:
  //   bit 2 for system
  //   bit 1 for ram a
  //   both on ram b
endmodule

module matrix_ke_maslay (
  input  A,
  input  B,
  input  C,
  input  D,
  input  cb_1,
  input  cb_2,
  output cout
);

  wire and_1_out, and_2_out, and_3_out, and_4_out, not_1_out, not_2_out;

  not not_1 (not_1_out, cb_2);
  not not_2 (not_2_out, cb_1);
  and and_1 (and_1_out, not_1_out, not_2_out, A);
  and and_2 (and_2_out, not_1_out, cb_1, B);
  and and_3 (and_3_out, cb_2, not_2_out, C);
  and and_4 (and_4_out, cb_2, cb_1, D);
  or or_1 (cout, and_1_out, and_2_out, and_3_out, and_4_out);
endmodule

module mat_mult_fix (
  input  OE,
  input  [15:0] reg_1,
  input  [15:0] reg_5,
  input  [15:0] reg_2,
  input  [15:0] reg_7,
  input  [15:0] reg_6,
  input  [15:0] reg_8,
  input  [15:0] reg_3,
  input  [15:0] reg_4,
  output [15:0] out_10,
  output [15:0] out_11,
  output [15:0] out_12,
  output [15:0] out_13
);

  wire [7:0] bit_extender_2_out, bit_extender_3_out, bit_extender_4_out, bit_extender_5_out,
       bit_extender_6_out, bit_extender_7_out, bit_extender_8_out, bit_extender_9_out;
  wire [15:0] add_16_1_sum_out, add_16_2_sum_out, add_16_3_sum_out, add_16_4_sum_out, bit_extender_1_out,
       mult_8_1_product, mult_8_2_product, mult_8_3_product, mult_8_4_product, mult_8_5_product,
       mult_8_6_product, mult_8_7_product, mult_8_8_product;

  assign bit_extender_1_out = {{15{OE}}, OE};  // Bit_Extender bit_extender_1
  Bit_Extender #(.in_width(16), .out_width(8)) bit_extender_2 (.in(reg_1), .out(bit_extender_2_out));
  Bit_Extender #(.in_width(16), .out_width(8)) bit_extender_3 (.in(reg_5), .out(bit_extender_3_out));
  Bit_Extender #(.in_width(16), .out_width(8)) bit_extender_4 (.in(reg_2), .out(bit_extender_4_out));
  Bit_Extender #(.in_width(16), .out_width(8)) bit_extender_5 (.in(reg_7), .out(bit_extender_5_out));
  Bit_Extender #(.in_width(16), .out_width(8)) bit_extender_6 (.in(reg_6), .out(bit_extender_6_out));
  Bit_Extender #(.in_width(16), .out_width(8)) bit_extender_7 (.in(reg_8), .out(bit_extender_7_out));
  Bit_Extender #(.in_width(16), .out_width(8)) bit_extender_8 (.in(reg_3), .out(bit_extender_8_out));
  Bit_Extender #(.in_width(16), .out_width(8)) bit_extender_9 (.in(reg_4), .out(bit_extender_9_out));
  mult_8 mult_8_1 (.A(bit_extender_2_out), .B(bit_extender_3_out), .product(mult_8_1_product));  // open: carry_out
  mult_8 mult_8_2 (.A(bit_extender_4_out), .B(bit_extender_5_out), .product(mult_8_2_product));  // open: carry_out
  mult_8 mult_8_3 (.A(bit_extender_2_out), .B(bit_extender_6_out), .product(mult_8_3_product));  // open: carry_out
  mult_8 mult_8_4 (.A(bit_extender_4_out), .B(bit_extender_7_out), .product(mult_8_4_product));  // open: carry_out
  mult_8 mult_8_5 (.A(bit_extender_3_out), .B(bit_extender_8_out), .product(mult_8_5_product));  // open: carry_out
  mult_8 mult_8_6 (.A(bit_extender_5_out), .B(bit_extender_9_out), .product(mult_8_6_product));  // open: carry_out
  mult_8 mult_8_7 (.A(bit_extender_6_out), .B(bit_extender_8_out), .product(mult_8_7_product));  // open: carry_out
  mult_8 mult_8_8 (.A(bit_extender_7_out), .B(bit_extender_9_out), .product(mult_8_8_product));  // open: carry_out
  add_16 add_16_1 (
    .A(mult_8_1_product), .B(mult_8_2_product), .Sum_out(add_16_1_sum_out));  // open: Carry_In, Carry_out
  add_16 add_16_2 (
    .A(mult_8_3_product), .B(mult_8_4_product), .Sum_out(add_16_2_sum_out));  // open: Carry_In, Carry_out
  add_16 add_16_3 (
    .A(mult_8_5_product), .B(mult_8_6_product), .Sum_out(add_16_3_sum_out));  // open: Carry_In, Carry_out
  add_16 add_16_4 (
    .A(mult_8_7_product), .B(mult_8_8_product), .Sum_out(add_16_4_sum_out));  // open: Carry_In, Carry_out
  assign out_10 = add_16_1_sum_out & bit_extender_1_out;  // AND_Gate and_1, 16 bits wide
  assign out_11 = add_16_2_sum_out & bit_extender_1_out;  // AND_Gate and_2, 16 bits wide
  assign out_12 = add_16_3_sum_out & bit_extender_1_out;  // AND_Gate and_3, 16 bits wide
  assign out_13 = add_16_4_sum_out & bit_extender_1_out;  // AND_Gate and_4, 16 bits wide

  // Notes on the sheet:
  //   r1*r5 + r2*r7
  //   r3*r5 +r4*r7
  //   r1*r6 + r2*r8
  //   r3*r6 + r4*r8
endmodule

module J_16_Core_final_move (
  input  RAM_A_WE,
  input  RAM_A_OE,
  input  RAM_B_OE,
  input  RAM_B_WE,
  input  Inst_RAM_OE,
  input  Inst_RAM_WE,
  input  system_RAM_OE,
  input  system_RAM_WE,
  input  MBR_B_WE,
  input  MBR_A_WE,
  input  MBR_Z_WE,
  input  inst_splitter_we,
  input  MBR_B_CB,
  input  MBR_A_CB,
  input  MBR_Z_CB,
  input  MAR_Z_WE,
  input  MAR_A_WE,
  input  MAR_B_WE,
  input  reg_8_we,
  input  reg_4_we,
  input  reg_2_we,
  input  reg_6_we,
  input  reg_7_we,
  input  reg_5_we,
  input  reg_3_we,
  input  reg_1_we,
  input  reg_a_out_cb,
  input  halt_maybe,
  input  reg_b_out_cb,
  input  Alu_out_cb,
  input  counter_increment_by_1,
  input  counter_increment_on,
  input  decode_cb_ramb,
  input  counter_reset,
  input  opcode_reg_we,
  input  opcode_init_cb,
  input  reg1_cb,
  input  reg5_cb,
  input  reg7_cb,
  input  Alu_register_we,
  input  overflow_reg_we,
  input  bus_select_oe,
  input  bus_select_bit1,
  input  bus_select_bit2,
  input  inst_ram_cb,
  input  reset_shit,
  input  decode_cb_rama,
  input  decode_control,
  input  temp_reg_confl,
  input  temp_reg_cb_mux,
  input  mux_control,
  input  temp_reg_we,
  input  program_counter_cb,
  input  ram_increment,
  input  ram_increment_Cb,
  input  system_reg_we,
  input  mar_a_cb,
  input  mar_b_cb,
  input  mar_b_conf_cb,
  input  mat_mult_oe,
  input  matrix_mux_cb,
  input  ramb_bustrm_cb,
  input  rama_bustrm_cb,
  input  mat_mux_cb_2,
  input  mat_mux_cb_1,
  input  mar_b_conf_2
);

  wire alu_1_carry_out, clock_1_out, not_1_out;
  wire [3:0] counter_3_q;
  wire [4:0] controlled_buffer_1_out, controlled_buffer_2_out, controlled_buffer_12_out, counter_1_q,
       counter_2_q, register_8_q, register_13_q, register_14_q, spliitter_1_add_a, spliitter_1_add_b;
  wire [4:4] controlled_buffer_1_out_2, controlled_buffer_1_out_3;
  wire [5:0] register_1_q;
  wire [15:0] alu_1_result, controlled_buffer_3_out, controlled_buffer_9_out, controlled_buffer_10_out,
       controlled_buffer_15_out, controlled_buffer_17_out, controlled_buffer_25_out, mat_mult_fix_1_out_10,
       mat_mult_fix_1_out_11, mat_mult_fix_1_out_12, mat_mult_fix_1_out_13, mem_swap_temp_reg_out,
       mux_for_mult_1_cout, ram_1_dout, ram_2_dout, ram_4_dout, register_2_q, register_4_q, register_5_q,
       register_6_q, register_7_q, register_9_q, register_15_q, register_16_q, register_17_q, register_18_q,
       sharah_e_faisal_1_ram_a, sharah_e_faisal_1_ram_b, sharah_e_faisal_1_ram_system, Temp_reg_q,
       terminus_des_1_ram_a, terminus_des_1_ram_b;
  wire [63:0] rom_1_data;

  Counter #(.max('h1f), .width(5)) counter_1 (
    .up(1'b1), .count(rom_1_data[34]), .clk(clock_1_out), .Q(counter_1_q));  // open: clr, load, D, carry
  Register #(.width(6)) register_1 (
    .D({controlled_buffer_1_out_2[4], controlled_buffer_1_out_3[4], controlled_buffer_1_out[3:0]}),
    .en(rom_1_data[31]), .clk(clock_1_out), .Q(register_1_q), .clr(rom_1_data[20]));
  Register #(.width(16)) register_2 (
    .D(controlled_buffer_3_out), .en(rom_1_data[26]), .clk(clock_1_out), .Q(register_2_q));  // open: clr
  Register #(.width(1)) register_3 (.D(alu_1_carry_out), .en(rom_1_data[25]), .clk(clock_1_out));  // open: Q, clr
  assign {controlled_buffer_1_out_2[4], controlled_buffer_1_out_3[4], controlled_buffer_1_out[3:0]} = rom_1_data[30] ? {6{1'b0}} : 6'bz;  // Controlled_Buffer controlled_buffer_1
  assign controlled_buffer_2_out = rom_1_data[13] ? counter_1_q : 5'bz;  // Controlled_Buffer controlled_buffer_2
  // Probe on alu_1_result
  assign controlled_buffer_3_out = rom_1_data[35] ? alu_1_result : 16'bz;  // Controlled_Buffer controlled_buffer_3
  ALU alu_1 (
    .opcode({controlled_buffer_1_out_2[4], controlled_buffer_1_out[3:0]}), .A(controlled_buffer_9_out),
    .B(controlled_buffer_10_out), .result(alu_1_result), .carry_out(alu_1_carry_out));
  Register #(.width(16)) register_4 (
    .D(controlled_buffer_9_out), .en(rom_1_data[38]), .clk(clock_1_out), .Q(register_4_q));  // open: clr
  Register #(.width(16)) register_5 (
    .D(controlled_buffer_9_out), .en(rom_1_data[39]), .clk(clock_1_out), .Q(register_5_q));  // open: clr
  Register #(.width(16)) register_6 (
    .D(controlled_buffer_10_out), .en(rom_1_data[40]), .clk(clock_1_out), .Q(register_6_q));  // open: clr
  Register #(.width(16)) register_7 (
    .D(controlled_buffer_10_out), .en(rom_1_data[41]), .clk(clock_1_out), .Q(register_7_q));  // open: clr
  assign controlled_buffer_2_out = rom_1_data[0] ? register_14_q : 5'bz;  // Controlled_Buffer controlled_buffer_4
  Register #(.width(5)) register_8 (
    .D(controlled_buffer_2_out), .en(rom_1_data[48]), .clk(clock_1_out), .Q(register_8_q));  // open: clr
  Spliitter spliitter_1 (
    .Instruction(controlled_buffer_17_out), .WE(rom_1_data[52]), .clk(clock_1_out),
    .Add_B(spliitter_1_add_b), .Add_A(spliitter_1_add_a), .opcode(controlled_buffer_1_out),
    .flag(controlled_buffer_1_out_2[4]));
  // Probe on register_8_q
  // Probe on spliitter_1_add_b
  // Probe on controlled_buffer_1_out
  Register #(.width(16)) register_9 (
    .D(controlled_buffer_10_out), .en(rom_1_data[42]), .clk(clock_1_out), .Q(register_9_q));  // open: clr
  Counter #(.max('h1f), .width(5)) counter_2 (
    .clr(rom_1_data[32]), .up(1'b0), .count(rom_1_data[12]), .clk(clock_1_out), .Q(counter_2_q));  // open: load, D, carry
  // Probe on spliitter_1_add_a
  assign register_5_q = rom_1_data[29] ? register_4_q : 16'bz;  // Controlled_Buffer controlled_buffer_5
  Register #(.width(16)) register_10 (
    .D(controlled_buffer_9_out), .en(rom_1_data[43]), .clk(clock_1_out), .Q(register_5_q));  // open: clr
  Register #(.width(16)) register_11 (
    .D(controlled_buffer_9_out), .en(rom_1_data[44]), .clk(clock_1_out), .Q(register_5_q));  // open: clr
  assign register_7_q = rom_1_data[28] ? register_6_q : 16'bz;  // Controlled_Buffer controlled_buffer_6
  Register #(.width(16)) register_12 (
    .D(controlled_buffer_10_out), .en(rom_1_data[45]), .clk(clock_1_out), .Q(register_7_q));  // open: clr
  Register #(.width(5)) register_13 (
    .D(controlled_buffer_2_out), .en(rom_1_data[47]), .clk(clock_1_out), .Q(register_13_q));  // open: clr
  assign controlled_buffer_2_out = rom_1_data[9] ? spliitter_1_add_a : 5'bz;  // Controlled_Buffer controlled_buffer_7
  assign register_7_q = rom_1_data[27] ? register_9_q : 16'bz;  // Controlled_Buffer controlled_buffer_8
  // Probe on register_2_q
  Controlled_Buffer #(.width(16)) controlled_buffer_9 (.in(register_5_q), .out(controlled_buffer_9_out));  // open: en
  assign controlled_buffer_10_out = rom_1_data[36] ? register_7_q : 16'bz;  // Controlled_Buffer controlled_buffer_10
  assign controlled_buffer_2_out = rom_1_data[11] ? counter_2_q : 5'bz;  // Controlled_Buffer controlled_buffer_11
  assign controlled_buffer_12_out = rom_1_data[7] ? controlled_buffer_2_out : 5'bz;  // Controlled_Buffer controlled_buffer_12
  Register #(.width(5)) register_14 (
    .D(controlled_buffer_12_out), .en(rom_1_data[46]), .clk(clock_1_out), .Q(register_14_q));  // open: clr
  assign controlled_buffer_12_out = rom_1_data[8] ? spliitter_1_add_b : 5'bz;  // Controlled_Buffer controlled_buffer_13
  Clock clock_1 (.out(clock_1_out));
  mat_mult_fix mat_mult_fix_1 (
    .OE(rom_1_data[6]), .reg_1(register_4_q), .reg_5(register_6_q), .reg_2(register_5_q),
    .reg_7(register_7_q), .reg_6(register_9_q), .reg_8(register_7_q), .reg_3(register_5_q),
    .reg_4(register_5_q), .out_10(mat_mult_fix_1_out_10), .out_11(mat_mult_fix_1_out_11),
    .out_12(mat_mult_fix_1_out_12), .out_13(mat_mult_fix_1_out_13));
  mux_for_mult mux_for_mult_1 (
    .A(mat_mult_fix_1_out_10), .B(mat_mult_fix_1_out_11), .C(mat_mult_fix_1_out_12),
    .D(mat_mult_fix_1_out_13), .cb_1(rom_1_data[1]), .cb_2(rom_1_data[2]), .cout(mux_for_mult_1_cout));
  sharah_e_faisal sharah_e_faisal_1 (
    .OE(rom_1_data[24]), .bit1(rom_1_data[23]), .bit2(rom_1_data[22]), .data_In(register_2_q),
    .Ram_system(sharah_e_faisal_1_ram_system), .Ram_A(sharah_e_faisal_1_ram_a),
    .Ram_B(sharah_e_faisal_1_ram_b));
  assign register_2_q = rom_1_data[5] ? mux_for_mult_1_cout : 16'bz;  // Controlled_Buffer controlled_buffer_14
  assign controlled_buffer_15_out = rom_1_data[3] ? sharah_e_faisal_1_ram_a : 16'bz;  // Controlled_Buffer controlled_buffer_15
  assign controlled_buffer_15_out = rom_1_data[4] ? sharah_e_faisal_1_ram_b : 16'bz;  // Controlled_Buffer controlled_buffer_16
  Register #(.width(16)) register_15 (
    .D(controlled_buffer_25_out), .en(rom_1_data[53]), .clk(clock_1_out), .Q(register_15_q));  // open: clr
  Register #(.width(16)) register_16 (
    .D(ram_2_dout), .en(rom_1_data[54]), .clk(clock_1_out), .Q(register_16_q));  // open: clr
  Register #(.width(16)) register_17 (
    .D(ram_4_dout), .en(rom_1_data[55]), .clk(clock_1_out), .Q(register_17_q));  // open: clr
  // Probe on mux_for_mult_1_cout
  assign controlled_buffer_17_out = rom_1_data[49] ? register_15_q : 16'bz;  // Controlled_Buffer controlled_buffer_17
  assign controlled_buffer_9_out = rom_1_data[50] ? register_16_q : 16'bz;  // Controlled_Buffer controlled_buffer_18
  assign controlled_buffer_10_out = rom_1_data[51] ? register_17_q : 16'bz;  // Controlled_Buffer controlled_buffer_19
  Register #(.width(16)) Temp_reg (
    .D(controlled_buffer_15_out), .en(rom_1_data[14]), .clk(clock_1_out), .Q(Temp_reg_q));  // open: clr
  assign controlled_buffer_9_out = rom_1_data[16] ? Temp_reg_q : 16'bz;  // Controlled_Buffer controlled_buffer_20
  Controlled_Buffer #(.width(5)) controlled_buffer_21 (.out(register_8_q), .en(rom_1_data[13]));  // open: in
  // Probe on register_8_q
  // Probe on controlled_buffer_17_out
  RAM #(.addrWidth(5), .dataWidth(16), .\type ("nonvolatile")) ram_1 (
    .addr(register_8_q), .we(rom_1_data[58]), .oe(rom_1_data[59]), .clk(clock_1_out),
    .din(controlled_buffer_17_out), .dout(ram_1_dout));
  RAM #(.addrWidth(5), .dataWidth(16), .\type ("nonvolatile")) ram_2 (
    .addr(register_13_q), .we(rom_1_data[63]), .oe(rom_1_data[62]), .clk(clock_1_out),
    .din(controlled_buffer_9_out), .dout(ram_2_dout));
  assign controlled_buffer_10_out = rom_1_data[17] ? controlled_buffer_9_out : 16'bz;  // Controlled_Buffer controlled_buffer_22
  // Probe on Temp_reg_q
  assign register_14_q = rom_1_data[18] ? register_13_q : 5'bz;  // Controlled_Buffer controlled_buffer_23
  terminus_uno mem_swap (
    .temp_reg_cb(rom_1_data[15]), .mbr_a(register_16_q), .mbr_b(register_17_q),
    .temp_reg_out(mem_swap_temp_reg_out));
  assign register_2_q = rom_1_data[16] ? mem_swap_temp_reg_out : 16'bz;  // Controlled_Buffer controlled_buffer_24
  // Probe on ram_1_dout
  assign controlled_buffer_25_out = rom_1_data[21] ? ram_1_dout : 16'bz;  // Controlled_Buffer controlled_buffer_25
  // Probe on ram_2_dout
  assign controlled_buffer_10_out = rom_1_data[18] ? terminus_des_1_ram_b : 16'bz;  // Controlled_Buffer controlled_buffer_26
  RAM #(.addrWidth(5), .dataWidth(16)) ram_3 (
    .addr(register_8_q), .we(rom_1_data[56]), .oe(rom_1_data[57]), .clk(clock_1_out), .din(register_18_q),
    .dout(controlled_buffer_25_out));
  // Probe on register_18_q
  RAM #(.addrWidth(5), .dataWidth(16), .\type ("nonvolatile")) ram_4 (
    .addr(register_14_q), .we(rom_1_data[60]), .oe(rom_1_data[61]), .clk(clock_1_out),
    .din(controlled_buffer_10_out), .dout(ram_4_dout));
  terminus_des terminus_des_1 (
    .temp_reg_cb(rom_1_data[18]), .mbr_z(controlled_buffer_17_out), .ram_a(terminus_des_1_ram_a),
    .ram_b(terminus_des_1_ram_b));
  assign controlled_buffer_9_out = rom_1_data[19] ? terminus_des_1_ram_a : 16'bz;  // Controlled_Buffer controlled_buffer_27
  Controlled_Buffer #(.width(16)) controlled_buffer_28 (
    .in(terminus_des_1_ram_a), .out(controlled_buffer_10_out));  // open: en
  Register #(.width(16)) register_18 (
    .D(sharah_e_faisal_1_ram_system), .en(rom_1_data[10]), .clk(clock_1_out), .Q(register_18_q));  // open: clr
  // Probe on ram_4_dout
  ROM #(.addrWidth(9), .dataWidth(64)) rom_1 (
    .addr({register_1_q[5], register_1_q[3:0], counter_3_q}), .data(rom_1_data));
  not not_1 (not_1_out, rom_1_data[37]);
  assign clock_1_out = rom_1_data[37] ? not_1_out : 1'bz;  // Controlled_Buffer controlled_buffer_29
  Counter #(.max('hf), .width(4)) counter_3 (
    .clr(rom_1_data[20]), .up(1'b1), .count(1'b1), .clk(clock_1_out), .Q(counter_3_q));  // open: load, D, carry
  // also tied to GND on the sheet: {controlled_buffer_1_out_3[4], register_1_q[4]}

  // Notes on the sheet:
  //   program counter for instruction ram
  //   opcode
  //   alu register
  //   overflow
  //   couldn't complete 
  //   as of yet
  //   Reg 5
  //   Reg 7
  //   MAR_Zero
  //   Reg 1
  //   Reg 3
  //   Reg 2
  //   RAM counter for the system ram
  //   Reg 6
  //   MAR_A
  //   Reg 4
  //   Reg 8
  //   MAR_B
  //   depending on the output
  //   turn on the control bits
  //   of the mux
  //   00 for A
  //   10 for B
  //   01 for C
  //   11 for D
  //   bit 2 system
  //   bit 1 ram a
  //   bit 1 and 2 ram b
  //   MBR_A
  //   MBR_B
  //   MBR_Z
  //   waste of time
  //   Instruction_Ram
  //   RAM_A
  //   move
  //   System_Ram
  //   0
  //   0
  //   0
  //   0
  //   0
  //   0
  //   0
  //   RAM_B
  //   8
  //   4
  //   2
  //   1
  //   8
  //   4
  //   2
  //   1
  //   8
  //   4
  //   system
  //   8
  //   4
  //   2
  //   1
  //   8
  //   4
  //   2
  //   1
  //   8
  //   4
  //   2
  //   1
  //   2
  //   1
  //   8
  //   4
  //   2
  //   1
  //   8
  //   4
  //   2
  //   2
  //   1
  //   8
  //   4
  //   2
  //   move system ram to ram a
  //   mem swap ram_a to ram_b
  //   1
  //   8
  //   4
  //   2
  //   1
  //   8
  //   4
  //   2
  //   1
  //   8
  //   4
  //   1
  //   8
  //   4
  //   2
  //   1
  //   8
  //   4
  //   2
  //   1
  //   8
  //   4
  //   2
  //   1
  //   8
  //   4
  //   halt_but_no_sucess
  //   contents of rom_1 (hex, n*v repeats v):
  //   0 820000000200000 820000000200000 12000000000000 c00000000300 60c0000000000300 60c0000000000300
  //   80000000 16*0 c000806000000 400002000 1000000002000 100000 28*0 c000806000000 400002000
  //   1000000002000 100000 12*0 1000800400200 801400400 100000800002000 1000400002000 1000000002000 100000
  //   10*0 1c14010 1000000000030000 181c008 8000000000010000 400002000 1000000002000 100000 25*0
  //   cc14000001880 c00000000880 60c0c00000000880 60c0c00000000880 ccc0000001880 c00000000880
  //   60c0c00000000880 60c0c00000000880 cc28000001880 c00000000880 60c0c00000000880 60c0c00000000880
  //   cf00000001880 400002000 1000000002000 100000 1400460 100000001401862 1000001400c62 100000001401864
  //   1000001400c64 100000001401866 1000001400c66 100000400002000 1000000002000 100000 6*0 400002040
  //   1000000002040 100040 13*0 c000806000000 400002000 1000000002000 100000 12*0 c000806000000 400002000
  //   1000000002000 100000 12*0 c000806000000 400002000 1000000002000 100000 12*0 c000806000000 400002000
  //   1000000002000 100000 28*0 1000000000001 220000000000000 220000000000000 8002000000080000 400002000
  //   1000000002000 100000 25*0 c000806000000 400002000 1000000002000 100000 204*0 2000000000 15*0
  //   1000000000080 220000000000000 220000000000000 10000000000c0000 400002000 1000000002000 100000
  //   zero pehle 
  //   20400120000
  //   8400800000
  //   8000E00000
  //   600000
  //   881800000000
  //   7800000000
  //   60FF000000
  //   00001 add
  //   00011 mult
  //   01010 comp
  //   01011 and
  //   01100 xor
  //   01101 not
  //   10001 sub
  //   01001 mat mult
  //   00111 block load
  //   01000 block store
  //   00101 mem swap
  //   01111 move w/o flag
  //   00100 store
  //   01110 nop
  //   18
  //   38
  //   a8
  //   b8
  //   c8
  //   d8
  //   118
  //   98
  //   78
  //   88
  //   58
  //   48
  //   1e8
  //   11110 halt
  //   0e8
  //   f8
  //   rom incrementer
endmodule

module J_16_Core_improvisation (
  input  RAM_A_WE,
  input  RAM_A_OE,
  input  RAM_B_OE,
  input  RAM_B_WE,
  input  Inst_RAM_OE,
  input  Inst_RAM_WE,
  input  system_RAM_OE,
  input  system_RAM_WE,
  input  MBR_B_WE,
  input  MBR_A_WE,
  input  MBR_Z_WE,
  input  inst_splitter_we,
  input  MBR_B_CB,
  input  MBR_A_CB,
  input  MBR_Z_CB,
  input  MAR_Z_WE,
  input  MAR_A_WE,
  input  MAR_B_WE,
  input  reg_8_we,
  input  reg_4_we,
  input  reg_2_we,
  input  reg_6_we,
  input  reg_7_we,
  input  reg_5_we,
  input  reg_3_we,
  input  reg_1_we,
  input  reg_a_out_cb,
  input  halt_maybe,
  input  reg_b_out_cb,
  input  Alu_out_cb,
  input  counter_increment_by_1,
  input  counter_increment_on,
  input  decode_cb_ramb,
  input  counter_reset,
  input  opcode_reg_we,
  input  opcode_init_cb,
  input  reg1_cb,
  input  reg5_cb,
  input  reg7_cb,
  input  Alu_register_we,
  input  overflow_reg_we,
  input  bus_select_oe,
  input  bus_select_bit1,
  input  bus_select_bit2,
  input  inst_ram_cb,
  input  reset_shit,
  input  decode_cb_rama,
  input  decode_control,
  input  temp_reg_confl,
  input  temp_reg_cb_mux,
  input  mux_control,
  input  temp_reg_we,
  input  program_counter_cb,
  input  ram_increment,
  input  ram_increment_Cb,
  input  system_reg_we,
  input  mar_a_cb,
  input  mar_b_cb,
  input  mar_b_conf_cb,
  input  mat_mult_oe,
  input  matrix_mux_cb,
  input  ramb_bustrm_cb,
  input  rama_bustrm_cb,
  input  mat_mux_cb_2,
  input  mat_mux_cb_1,
  input  mar_b_conf_2
);

  wire alu_1_carry_out, clock_1_out, not_1_out;
  wire [3:0] counter_3_q;
  wire [4:0] controlled_buffer_1_out, controlled_buffer_2_out, controlled_buffer_15_out, counter_1_q,
       counter_2_q, register_8_q, register_13_q, register_14_q, spliitter_1_add_a, spliitter_1_add_b;
  wire [4:4] controlled_buffer_1_out_2, controlled_buffer_1_out_3;
  wire [5:0] register_1_q;
  wire [15:0] alu_1_result, controlled_buffer_3_out, controlled_buffer_5_out, controlled_buffer_7_out,
       controlled_buffer_12_out, controlled_buffer_13_out, controlled_buffer_18_out,
       controlled_buffer_20_out, controlled_buffer_28_out, mat_mult_fix_1_out_10, mat_mult_fix_1_out_11,
       mat_mult_fix_1_out_12, mat_mult_fix_1_out_13, mem_swap_temp_reg_out, mux_for_mult_1_cout, ram_1_dout,
       ram_2_dout, ram_4_dout, register_2_q, register_4_q, register_5_q, register_6_q, register_7_q,
       register_9_q, register_10_q, register_15_q, register_16_q, register_17_q, register_18_q,
       sharah_e_faisal_1_ram_a, sharah_e_faisal_1_ram_b, sharah_e_faisal_1_ram_system, Temp_reg_q,
       terminus_des_1_ram_a, terminus_des_1_ram_b;
  wire [63:0] rom_1_data;

  Counter #(.max('h1f), .width(5)) counter_1 (
    .up(1'b1), .count(rom_1_data[34]), .clk(clock_1_out), .Q(counter_1_q));  // open: clr, load, D, carry
  Register #(.width(6)) register_1 (
    .D({controlled_buffer_1_out_2[4], controlled_buffer_1_out_3[4], controlled_buffer_1_out[3:0]}),
    .en(rom_1_data[31]), .clk(clock_1_out), .Q(register_1_q), .clr(rom_1_data[20]));
  Register #(.width(16)) register_2 (
    .D(controlled_buffer_3_out), .en(rom_1_data[26]), .clk(clock_1_out), .Q(register_2_q));  // open: clr
  Register #(.width(1)) register_3 (.D(alu_1_carry_out), .en(rom_1_data[25]), .clk(clock_1_out));  // open: Q, clr
  assign {controlled_buffer_1_out_2[4], controlled_buffer_1_out_3[4], controlled_buffer_1_out[3:0]} = rom_1_data[30] ? {6{1'b0}} : 6'bz;  // Controlled_Buffer controlled_buffer_1
  assign controlled_buffer_2_out = rom_1_data[13] ? counter_1_q : 5'bz;  // Controlled_Buffer controlled_buffer_2
  // Probe on alu_1_result
  assign controlled_buffer_3_out = rom_1_data[35] ? alu_1_result : 16'bz;  // Controlled_Buffer controlled_buffer_3
  ALU alu_1 (
    .opcode({controlled_buffer_1_out_2[4], controlled_buffer_1_out[3:0]}), .A(controlled_buffer_12_out),
    .B(controlled_buffer_13_out), .result(alu_1_result), .carry_out(alu_1_carry_out));
  Register #(.width(16)) register_4 (
    .D(controlled_buffer_12_out), .en(rom_1_data[38]), .clk(clock_1_out), .Q(register_4_q));  // open: clr
  Register #(.width(16)) register_5 (
    .D(controlled_buffer_12_out), .en(rom_1_data[39]), .clk(clock_1_out), .Q(register_5_q));  // open: clr
  Register #(.width(16)) register_6 (
    .D(controlled_buffer_13_out), .en(rom_1_data[40]), .clk(clock_1_out), .Q(register_6_q));  // open: clr
  Register #(.width(16)) register_7 (
    .D(controlled_buffer_13_out), .en(rom_1_data[41]), .clk(clock_1_out), .Q(register_7_q));  // open: clr
  assign controlled_buffer_2_out = rom_1_data[0] ? register_14_q : 5'bz;  // Controlled_Buffer controlled_buffer_4
  Register #(.width(5)) register_8 (
    .D(controlled_buffer_2_out), .en(rom_1_data[48]), .clk(clock_1_out), .Q(register_8_q));  // open: clr
  Spliitter spliitter_1 (
    .Instruction(controlled_buffer_20_out), .WE(rom_1_data[52]), .clk(clock_1_out),
    .Add_B(spliitter_1_add_b), .Add_A(spliitter_1_add_a), .opcode(controlled_buffer_1_out),
    .flag(controlled_buffer_1_out_2[4]));
  // Probe on register_8_q
  // Probe on spliitter_1_add_b
  // Probe on controlled_buffer_1_out
  Register #(.width(16)) register_9 (
    .D(controlled_buffer_12_out), .en(rom_1_data[43]), .clk(clock_1_out), .Q(register_9_q));  // open: clr
  Register #(.width(16)) register_10 (
    .D(controlled_buffer_13_out), .en(rom_1_data[42]), .clk(clock_1_out), .Q(register_10_q));  // open: clr
  Counter #(.max('h1f), .width(5)) counter_2 (
    .clr(rom_1_data[32]), .up(1'b0), .count(rom_1_data[12]), .clk(clock_1_out), .Q(counter_2_q));  // open: load, D, carry
  // Probe on spliitter_1_add_a
  assign controlled_buffer_5_out = rom_1_data[29] ? register_4_q : 16'bz;  // Controlled_Buffer controlled_buffer_5
  Controlled_Buffer #(.width(16)) controlled_buffer_6 (.in(register_5_q), .out(controlled_buffer_5_out));  // open: en
  Register #(.width(16)) register_11 (
    .D(controlled_buffer_12_out), .en(rom_1_data[44]), .clk(clock_1_out), .Q(controlled_buffer_5_out));  // open: clr
  assign controlled_buffer_7_out = rom_1_data[28] ? register_6_q : 16'bz;  // Controlled_Buffer controlled_buffer_7
  Controlled_Buffer #(.width(16)) controlled_buffer_8 (.in(register_7_q), .out(controlled_buffer_7_out));  // open: en
  Register #(.width(16)) register_12 (
    .D(controlled_buffer_13_out), .en(rom_1_data[45]), .clk(clock_1_out), .Q(controlled_buffer_7_out));  // open: clr
  Register #(.width(5)) register_13 (
    .D(controlled_buffer_2_out), .en(rom_1_data[47]), .clk(clock_1_out), .Q(register_13_q));  // open: clr
  assign controlled_buffer_2_out = rom_1_data[9] ? spliitter_1_add_a : 5'bz;  // Controlled_Buffer controlled_buffer_9
  Controlled_Buffer #(.width(16)) controlled_buffer_10 (.in(register_9_q), .out(controlled_buffer_5_out));  // open: en
  assign controlled_buffer_7_out = rom_1_data[27] ? register_10_q : 16'bz;  // Controlled_Buffer controlled_buffer_11
  // Probe on register_2_q
  Controlled_Buffer #(.width(16)) controlled_buffer_12 (
    .in(controlled_buffer_5_out), .out(controlled_buffer_12_out));  // open: en
  assign controlled_buffer_13_out = rom_1_data[36] ? controlled_buffer_7_out : 16'bz;  // Controlled_Buffer controlled_buffer_13
  assign controlled_buffer_2_out = rom_1_data[11] ? counter_2_q : 5'bz;  // Controlled_Buffer controlled_buffer_14
  assign controlled_buffer_15_out = rom_1_data[7] ? controlled_buffer_2_out : 5'bz;  // Controlled_Buffer controlled_buffer_15
  Register #(.width(5)) register_14 (
    .D(controlled_buffer_15_out), .en(rom_1_data[46]), .clk(clock_1_out), .Q(register_14_q));  // open: clr
  assign controlled_buffer_15_out = rom_1_data[8] ? spliitter_1_add_b : 5'bz;  // Controlled_Buffer controlled_buffer_16
  Clock clock_1 (.out(clock_1_out));
  mat_mult_fix mat_mult_fix_1 (
    .OE(rom_1_data[6]), .reg_1(register_4_q), .reg_5(register_6_q), .reg_2(register_9_q),
    .reg_7(register_7_q), .reg_6(register_10_q), .reg_8(controlled_buffer_7_out), .reg_3(register_5_q),
    .reg_4(controlled_buffer_5_out), .out_10(mat_mult_fix_1_out_10), .out_11(mat_mult_fix_1_out_11),
    .out_12(mat_mult_fix_1_out_12), .out_13(mat_mult_fix_1_out_13));
  mux_for_mult mux_for_mult_1 (
    .A(mat_mult_fix_1_out_10), .B(mat_mult_fix_1_out_11), .C(mat_mult_fix_1_out_12),
    .D(mat_mult_fix_1_out_13), .cb_1(rom_1_data[1]), .cb_2(rom_1_data[2]), .cout(mux_for_mult_1_cout));
  sharah_e_faisal sharah_e_faisal_1 (
    .OE(rom_1_data[24]), .bit1(rom_1_data[23]), .bit2(rom_1_data[22]), .data_In(register_2_q),
    .Ram_system(sharah_e_faisal_1_ram_system), .Ram_A(sharah_e_faisal_1_ram_a),
    .Ram_B(sharah_e_faisal_1_ram_b));
  assign register_2_q = rom_1_data[5] ? mux_for_mult_1_cout : 16'bz;  // Controlled_Buffer controlled_buffer_17
  assign controlled_buffer_18_out = rom_1_data[3] ? sharah_e_faisal_1_ram_a : 16'bz;  // Controlled_Buffer controlled_buffer_18
  assign controlled_buffer_18_out = rom_1_data[4] ? sharah_e_faisal_1_ram_b : 16'bz;  // Controlled_Buffer controlled_buffer_19
  Register #(.width(16)) register_15 (
    .D(controlled_buffer_28_out), .en(rom_1_data[53]), .clk(clock_1_out), .Q(register_15_q));  // open: clr
  Register #(.width(16)) register_16 (
    .D(ram_2_dout), .en(rom_1_data[54]), .clk(clock_1_out), .Q(register_16_q));  // open: clr
  Register #(.width(16)) register_17 (
    .D(ram_4_dout), .en(rom_1_data[55]), .clk(clock_1_out), .Q(register_17_q));  // open: clr
  // Probe on mat_mult_fix_1_out_10
  // Probe on mat_mult_fix_1_out_11
  // Probe on mat_mult_fix_1_out_12
  // Probe on mat_mult_fix_1_out_13
  // Probe on mux_for_mult_1_cout
  assign controlled_buffer_20_out = rom_1_data[49] ? register_15_q : 16'bz;  // Controlled_Buffer controlled_buffer_20
  assign controlled_buffer_12_out = rom_1_data[50] ? register_16_q : 16'bz;  // Controlled_Buffer controlled_buffer_21
  assign controlled_buffer_13_out = rom_1_data[51] ? register_17_q : 16'bz;  // Controlled_Buffer controlled_buffer_22
  Register #(.width(16)) Temp_reg (
    .D(controlled_buffer_18_out), .en(rom_1_data[14]), .clk(clock_1_out), .Q(Temp_reg_q));  // open: clr
  assign controlled_buffer_12_out = rom_1_data[16] ? Temp_reg_q : 16'bz;  // Controlled_Buffer controlled_buffer_23
  Controlled_Buffer #(.width(5)) controlled_buffer_24 (.out(register_8_q), .en(rom_1_data[13]));  // open: in
  // Probe on register_8_q
  // Probe on controlled_buffer_20_out
  // Probe on register_16_q
  RAM #(.addrWidth(5), .dataWidth(16), .\type ("nonvolatile")) ram_1 (
    .addr(register_8_q), .we(rom_1_data[58]), .oe(rom_1_data[59]), .clk(clock_1_out),
    .din(controlled_buffer_20_out), .dout(ram_1_dout));
  RAM #(.addrWidth(5), .dataWidth(16), .\type ("nonvolatile")) ram_2 (
    .addr(register_13_q), .we(rom_1_data[63]), .oe(rom_1_data[62]), .clk(clock_1_out),
    .din(controlled_buffer_12_out), .dout(ram_2_dout));
  assign controlled_buffer_13_out = rom_1_data[17] ? controlled_buffer_12_out : 16'bz;  // Controlled_Buffer controlled_buffer_25
  // Probe on register_17_q
  // Probe on Temp_reg_q
  assign register_14_q = rom_1_data[18] ? register_13_q : 5'bz;  // Controlled_Buffer controlled_buffer_26
  terminus_uno mem_swap (
    .temp_reg_cb(rom_1_data[15]), .mbr_a(register_16_q), .mbr_b(register_17_q),
    .temp_reg_out(mem_swap_temp_reg_out));
  assign register_2_q = rom_1_data[16] ? mem_swap_temp_reg_out : 16'bz;  // Controlled_Buffer controlled_buffer_27
  // Probe on mem_swap_temp_reg_out
  // Probe on ram_1_dout
  assign controlled_buffer_28_out = rom_1_data[21] ? ram_1_dout : 16'bz;  // Controlled_Buffer controlled_buffer_28
  // Probe on ram_2_dout
  assign controlled_buffer_13_out = rom_1_data[18] ? terminus_des_1_ram_b : 16'bz;  // Controlled_Buffer controlled_buffer_29
  RAM #(.addrWidth(5), .dataWidth(16)) ram_3 (
    .addr(register_8_q), .we(rom_1_data[56]), .oe(rom_1_data[57]), .clk(clock_1_out), .din(register_18_q),
    .dout(controlled_buffer_28_out));
  // Probe on register_18_q
  RAM #(.addrWidth(5), .dataWidth(16), .\type ("nonvolatile")) ram_4 (
    .addr(register_14_q), .we(rom_1_data[60]), .oe(rom_1_data[61]), .clk(clock_1_out),
    .din(controlled_buffer_13_out), .dout(ram_4_dout));
  terminus_des terminus_des_1 (
    .temp_reg_cb(rom_1_data[18]), .mbr_z(controlled_buffer_20_out), .ram_a(terminus_des_1_ram_a),
    .ram_b(terminus_des_1_ram_b));
  assign controlled_buffer_12_out = rom_1_data[19] ? terminus_des_1_ram_a : 16'bz;  // Controlled_Buffer controlled_buffer_30
  Controlled_Buffer #(.width(16)) controlled_buffer_31 (
    .in(terminus_des_1_ram_a), .out(controlled_buffer_13_out));  // open: en
  Register #(.width(16)) register_18 (
    .D(sharah_e_faisal_1_ram_system), .en(rom_1_data[10]), .clk(clock_1_out), .Q(register_18_q));  // open: clr
  // Probe on ram_4_dout
  ROM #(.addrWidth(9), .dataWidth(64)) rom_1 (
    .addr({register_1_q[5], register_1_q[3:0], counter_3_q}), .data(rom_1_data));
  not not_1 (not_1_out, rom_1_data[37]);
  assign clock_1_out = rom_1_data[37] ? not_1_out : 1'bz;  // Controlled_Buffer controlled_buffer_32
  Counter #(.max('hf), .width(4)) counter_3 (
    .clr(rom_1_data[20]), .up(1'b1), .count(1'b1), .clk(clock_1_out), .Q(counter_3_q));  // open: load, D, carry
  // also tied to GND on the sheet: {controlled_buffer_1_out_3[4], register_1_q[4]}

  // Notes on the sheet:
  //   program counter for instruction ram
  //   opcode
  //   alu register
  //   overflow
  //   couldn't complete 
  //   as of yet
  //   Reg 5
  //   Reg 7
  //   MAR_Zero
  //   Reg 1
  //   Reg 3
  //   Reg 2
  //   RAM counter for the system ram
  //   Reg 6
  //   MAR_A
  //   Reg 4
  //   Reg 8
  //   MAR_B
  //   depending on the output
  //   turn on the control bits
  //   of the mux
  //   00 for A
  //   10 for B
  //   01 for C
  //   11 for D
  //   bit 2 system
  //   bit 1 ram a
  //   bit 1 and 2 ram b
  //   MBR_A
  //   MBR_B
  //   MBR_Z
  //   waste of time
  //   Instruction_Ram
  //   RAM_A
  //   move
  //   System_Ram
  //   0
  //   0
  //   0
  //   0
  //   0
  //   0
  //   RAM_B
  //   8
  //   4
  //   2
  //   1
  //   8
  //   4
  //   2
  //   1
  //   8
  //   4
  //   system
  //   no connection needed
  //   8
  //   4
  //   2
  //   1
  //   8
  //   4
  //   2
  //   1
  //   8
  //   4
  //   2
  //   1
  //   2
  //   1
  //   8
  //   4
  //   2
  //   1
  //   8
  //   4
  //   2
  //   2
  //   1
  //   8
  //   4
  //   2
  //   move system ram to ram a
  //   mem swap ram_a to ram_b
  //   1
  //   8
  //   4
  //   2
  //   1
  //   8
  //   4
  //   2
  //   1
  //   8
  //   4
  //   1
  //   8
  //   4
  //   2
  //   1
  //   8
  //   4
  //   2
  //   1
  //   8
  //   4
  //   2
  //   1
  //   8
  //   4
  //   halt_but_no_sucess
  //   contents of rom_1 (hex, n*v repeats v):
  //   0 820000000200000 820000000200000 12000000000000 c00000000300 60c0000000000300 60c0000000000300
  //   80000000 16*0 c000806000000 400002000 1000000002000 100000 28*0 c000806000000 400002000
  //   1000000002000 100000 12*0 1000800400200 801400400 100000800002000 1000400002000 1000000002000 100000
  //   10*0 1c14010 1000000000030000 181c008 8000000000010000 400002000 1000000002000 100000 17*0
  //   cc28000001880 c00000000880 60c0c00000000880 60c0c00000000880 cf00000001880 400002000 1000000002000
  //   100000 cc14000001880 c00000000880 60c0c00000000880 60c0c00000000880 ccc0000001880 c00000000880
  //   60c0c00000000880 60c0c00000000880 1000000002000 100000 6*0 1400460 100000001401862 1000001400c62
  //   100000001401864 1000001400c64 100000001401866 1000001400c66 100000400002000 1000000002000 100000 6*0
  //   400002040 1000000002040 100040 13*0 c000806000000 400002000 1000000002000 100000 12*0 c000806000000
  //   400002000 1000000002000 100000 12*0 c000806000000 400002000 1000000002000 100000 12*0 c000806000000
  //   400002000 1000000002000 100000 12*0 400002000 1000000002000 100000 13*0 1000000000001
  //   220000000000000 220000000000000 8002000000080000 400002000 1000000002000 100000 25*0 c000806000000
  //   400002000 1000000002000 100000 204*0 2000000000 15*0 1000000000080 220000000000000 220000000000000
  //   10000000000c0000 400002000 1000000002000 100000
  //   zero pehle 
  //   20400120000
  //   8400800000
  //   8000E00000
  //   600000
  //   881800000000
  //   7800000000
  //   60FF000000
  //   00001 add
  //   00011 mult
  //   01010 comp
  //   01011 and
  //   01100 xor
  //   01101 not
  //   10001 sub
  //   01001 mat mult
  //   00111 block load
  //   01000 block store
  //   00101 mem swap
  //   01111 move w/o flag
  //   11111 move flag 
  //   00100 store
  //   11110 halt
  //   01110 nop
  //   18
  //   checked
  //   38
  //   checked
  //   a8
  //   b8
  //   c8
  //   d8
  //   118
  //   98
  //   78
  //   88
  //   58
  //   48
  //   1e8
  //   0e8
  //   checked
  //   checked
  //   checked
  //   checked
  //   checked
  //   checked
  //   checked
  //   f8
  //   checked
  //   1f8
  //   checked
  //   checked
  //   checked
  //   rom incrementer
  //   checked
endmodule

module opcode_reader (
  input  [15:0] Instruction,
  input  WE,
  input  clk,
  output [4:0] Add_B,
  output [4:0] Add_A,
  output [4:0] opcode,
  output flag
);

  Register #(.width(16)) register_1 (
    .D(Instruction), .en(WE), .clk(clk), .Q({flag, opcode, Add_A, Add_B}));  // open: clr
endmodule

module J_16_Core_Final (
  input  RAM_A_WE,
  input  RAM_A_OE,
  input  RAM_B_OE,
  input  RAM_B_WE,
  input  Inst_RAM_OE,
  input  Inst_RAM_WE,
  input  system_RAM_OE,
  input  system_RAM_WE,
  input  MBR_B_WE,
  input  MBR_A_WE,
  input  MBR_Z_WE,
  input  inst_splitter_we,
  input  MBR_B_CB,
  input  MBR_A_CB,
  input  MBR_Z_CB,
  input  MAR_Z_WE,
  input  MAR_A_WE,
  input  MAR_B_WE,
  input  reg_8_we,
  input  reg_4_we,
  input  reg_2_we,
  input  reg_6_we,
  input  reg_7_we,
  input  reg_5_we,
  input  reg_3_we,
  input  reg_1_we,
  input  reg_a_out_cb,
  input  halt_maybe,
  input  reg_b_out_cb,
  input  Alu_reg_cb,
  input  Alu_out_cb,
  input  counter_increment_by_1,
  input  counter_increment_on,
  input  decode_cb_ramb,
  input  counter_reset,
  input  opcode_reg_we,
  input  opcode_init_cb,
  input  reg1_cb,
  input  reg5_cb,
  input  reg7_cb,
  input  Alu_register_we,
  input  overflow_reg_we,
  input  bus_select_oe,
  input  bus_select_bit1,
  input  bus_select_bit2,
  input  inst_ram_cb,
  input  reset_shit,
  input  decode_cb_rama,
  input  decode_control,
  input  temp_reg_confl,
  input  temp_reg_cb_mux,
  input  mux_control,
  input  temp_reg_we,
  input  program_counter_cb,
  input  ram_increment,
  input  ram_increment_Cb,
  input  system_reg_we,
  input  mar_a_cb,
  input  mar_b_cb,
  input  mar_b_conf_cb,
  input  mat_mult_oe,
  input  matrix_mux_cb,
  input  ramb_bustrm_cb,
  input  rama_bustrm_cb,
  input  mat_mux_cb_2,
  input  mat_mux_cb_1,
  input  mar_b_conf_2
);

  wire alu_1_carry_out, clock_1_out, not_1_out, not_2_out;
  wire [3:0] counter_3_q;
  wire [4:0] controlled_buffer_1_out, controlled_buffer_2_out, controlled_buffer_16_out, counter_1_q,
       counter_2_q, register_8_q, register_13_q, register_14_q, spliitter_1_add_a, spliitter_1_add_b;
  wire [4:4] controlled_buffer_1_out_2, controlled_buffer_1_out_3;
  wire [5:0] register_1_q;
  wire [15:0] alu_1_result, controlled_buffer_3_out, controlled_buffer_4_out, controlled_buffer_6_out,
       controlled_buffer_8_out, controlled_buffer_13_out, controlled_buffer_14_out, controlled_buffer_19_out,
       controlled_buffer_21_out, controlled_buffer_29_out, mat_mult_fix_1_out_10, mat_mult_fix_1_out_11,
       mat_mult_fix_1_out_12, mat_mult_fix_1_out_13, mem_swap_temp_reg_out, mux_for_mult_1_cout, ram_1_dout,
       ram_2_dout, ram_3_dout, ram_4_dout, register_2_q, register_4_q, register_5_q, register_6_q,
       register_7_q, register_9_q, register_10_q, register_15_q, register_16_q, register_17_q, register_18_q,
       sharah_e_faisal_1_ram_a, sharah_e_faisal_1_ram_b, sharah_e_faisal_1_ram_system, Temp_reg_q,
       terminus_des_1_ram_a, terminus_des_1_ram_b;
  wire [63:0] rom_1_data;

  Counter #(.max('h1f), .width(5)) counter_1 (
    .up(1'b1), .count(rom_1_data[34]), .clk(clock_1_out), .Q(counter_1_q));  // open: clr, load, D, carry
  Register #(.width(6)) register_1 (
    .D({controlled_buffer_1_out_2[4], controlled_buffer_1_out_3[4], controlled_buffer_1_out[3:0]}),
    .en(rom_1_data[31]), .clk(clock_1_out), .Q(register_1_q), .clr(rom_1_data[20]));
  Register #(.width(16)) register_2 (
    .D(controlled_buffer_3_out), .en(rom_1_data[26]), .clk(clock_1_out), .Q(register_2_q));  // open: clr
  Register #(.width(1)) register_3 (.D(alu_1_carry_out), .en(rom_1_data[25]), .clk(clock_1_out));  // open: Q, clr
  assign {controlled_buffer_1_out_2[4], controlled_buffer_1_out_3[4], controlled_buffer_1_out[3:0]} = rom_1_data[30] ? {6{1'b0}} : 6'bz;  // Controlled_Buffer controlled_buffer_1
  assign controlled_buffer_2_out = rom_1_data[13] ? counter_1_q : 5'bz;  // Controlled_Buffer controlled_buffer_2
  // Probe on alu_1_result
  assign controlled_buffer_3_out = rom_1_data[35] ? alu_1_result : 16'bz;  // Controlled_Buffer controlled_buffer_3
  ALU alu_1 (
    .opcode({controlled_buffer_1_out_2[4], controlled_buffer_1_out[3:0]}), .A(controlled_buffer_13_out),
    .B(controlled_buffer_14_out), .result(alu_1_result), .carry_out(alu_1_carry_out));
  assign controlled_buffer_4_out = rom_1_data[36] ? register_2_q : 16'bz;  // Controlled_Buffer controlled_buffer_4
  Register #(.width(16)) register_4 (
    .D(controlled_buffer_13_out), .en(rom_1_data[38]), .clk(clock_1_out), .Q(register_4_q));  // open: clr
  Register #(.width(16)) register_5 (
    .D(controlled_buffer_13_out), .en(rom_1_data[39]), .clk(clock_1_out), .Q(register_5_q));  // open: clr
  Register #(.width(16)) register_6 (
    .D(controlled_buffer_14_out), .en(rom_1_data[40]), .clk(clock_1_out), .Q(register_6_q));  // open: clr
  Register #(.width(16)) register_7 (
    .D(controlled_buffer_14_out), .en(rom_1_data[41]), .clk(clock_1_out), .Q(register_7_q));  // open: clr
  assign controlled_buffer_2_out = rom_1_data[0] ? register_14_q : 5'bz;  // Controlled_Buffer controlled_buffer_5
  Register #(.width(5)) register_8 (
    .D(controlled_buffer_2_out), .en(rom_1_data[48]), .clk(clock_1_out), .Q(register_8_q));  // open: clr
  Spliitter spliitter_1 (
    .Instruction(controlled_buffer_21_out), .WE(rom_1_data[52]), .clk(clock_1_out),
    .Add_B(spliitter_1_add_b), .Add_A(spliitter_1_add_a), .opcode(controlled_buffer_1_out),
    .flag(controlled_buffer_1_out_2[4]));
  // Probe on register_8_q
  // Probe on spliitter_1_add_b
  // Probe on controlled_buffer_1_out
  Register #(.width(16)) register_9 (
    .D(controlled_buffer_13_out), .en(rom_1_data[43]), .clk(clock_1_out), .Q(register_9_q));  // open: clr
  Register #(.width(16)) register_10 (
    .D(controlled_buffer_14_out), .en(rom_1_data[42]), .clk(clock_1_out), .Q(register_10_q));  // open: clr
  Counter #(.max('h1f), .width(5)) counter_2 (
    .clr(rom_1_data[32]), .up(1'b0), .count(rom_1_data[12]), .clk(clock_1_out), .Q(counter_2_q));  // open: load, D, carry
  // Probe on spliitter_1_add_a
  assign controlled_buffer_6_out = rom_1_data[29] ? register_4_q : 16'bz;  // Controlled_Buffer controlled_buffer_6
  Controlled_Buffer #(.width(16)) controlled_buffer_7 (.in(register_5_q), .out(controlled_buffer_6_out));  // open: en
  Register #(.width(16)) register_11 (
    .D(controlled_buffer_13_out), .en(rom_1_data[44]), .clk(clock_1_out), .Q(controlled_buffer_6_out));  // open: clr
  assign controlled_buffer_8_out = rom_1_data[28] ? register_6_q : 16'bz;  // Controlled_Buffer controlled_buffer_8
  Controlled_Buffer #(.width(16)) controlled_buffer_9 (.in(register_7_q), .out(controlled_buffer_8_out));  // open: en
  Register #(.width(16)) register_12 (
    .D(controlled_buffer_14_out), .en(rom_1_data[45]), .clk(clock_1_out), .Q(controlled_buffer_8_out));  // open: clr
  Register #(.width(5)) register_13 (
    .D(controlled_buffer_2_out), .en(rom_1_data[47]), .clk(clock_1_out), .Q(register_13_q));  // open: clr
  assign controlled_buffer_2_out = rom_1_data[9] ? spliitter_1_add_a : 5'bz;  // Controlled_Buffer controlled_buffer_10
  Controlled_Buffer #(.width(16)) controlled_buffer_11 (.in(register_9_q), .out(controlled_buffer_6_out));  // open: en
  assign controlled_buffer_8_out = rom_1_data[27] ? register_10_q : 16'bz;  // Controlled_Buffer controlled_buffer_12
  // Probe on controlled_buffer_4_out
  Controlled_Buffer #(.width(16)) controlled_buffer_13 (
    .in(controlled_buffer_6_out), .out(controlled_buffer_13_out));  // open: en
  Controlled_Buffer #(.width(16)) controlled_buffer_14 (
    .in(controlled_buffer_8_out), .out(controlled_buffer_14_out));  // open: en
  assign controlled_buffer_2_out = rom_1_data[11] ? counter_2_q : 5'bz;  // Controlled_Buffer controlled_buffer_15
  assign controlled_buffer_16_out = rom_1_data[7] ? controlled_buffer_2_out : 5'bz;  // Controlled_Buffer controlled_buffer_16
  Register #(.width(5)) register_14 (
    .D(controlled_buffer_16_out), .en(rom_1_data[46]), .clk(clock_1_out), .Q(register_14_q));  // open: clr
  assign controlled_buffer_16_out = rom_1_data[8] ? spliitter_1_add_b : 5'bz;  // Controlled_Buffer controlled_buffer_17
  Clock clock_1 (.out(clock_1_out));
  mat_mult_fix mat_mult_fix_1 (
    .OE(rom_1_data[6]), .reg_1(register_4_q), .reg_5(register_6_q), .reg_2(register_9_q),
    .reg_7(register_7_q), .reg_6(register_10_q), .reg_8(controlled_buffer_8_out), .reg_3(register_5_q),
    .reg_4(controlled_buffer_6_out), .out_10(mat_mult_fix_1_out_10), .out_11(mat_mult_fix_1_out_11),
    .out_12(mat_mult_fix_1_out_12), .out_13(mat_mult_fix_1_out_13));
  mux_for_mult mux_for_mult_1 (
    .A(mat_mult_fix_1_out_10), .B(mat_mult_fix_1_out_11), .C(mat_mult_fix_1_out_12),
    .D(mat_mult_fix_1_out_13), .cb_1(rom_1_data[1]), .cb_2(rom_1_data[2]), .cout(mux_for_mult_1_cout));
  sharah_e_faisal sharah_e_faisal_1 (
    .OE(rom_1_data[24]), .bit1(rom_1_data[23]), .bit2(rom_1_data[22]), .data_In(controlled_buffer_4_out),
    .Ram_system(sharah_e_faisal_1_ram_system), .Ram_A(sharah_e_faisal_1_ram_a),
    .Ram_B(sharah_e_faisal_1_ram_b));
  assign controlled_buffer_4_out = rom_1_data[5] ? mux_for_mult_1_cout : 16'bz;  // Controlled_Buffer controlled_buffer_18
  assign controlled_buffer_19_out = rom_1_data[3] ? sharah_e_faisal_1_ram_a : 16'bz;  // Controlled_Buffer controlled_buffer_19
  assign controlled_buffer_19_out = rom_1_data[4] ? sharah_e_faisal_1_ram_b : 16'bz;  // Controlled_Buffer controlled_buffer_20
  Register #(.width(16)) register_15 (
    .D(controlled_buffer_29_out), .en(rom_1_data[53]), .clk(clock_1_out), .Q(register_15_q));  // open: clr
  Register #(.width(16)) register_16 (
    .D(ram_2_dout), .en(rom_1_data[54]), .clk(clock_1_out), .Q(register_16_q));  // open: clr
  Register #(.width(16)) register_17 (
    .D(ram_4_dout), .en(rom_1_data[55]), .clk(clock_1_out), .Q(register_17_q));  // open: clr
  // Probe on mat_mult_fix_1_out_10
  // Probe on mat_mult_fix_1_out_11
  // Probe on mat_mult_fix_1_out_12
  // Probe on mat_mult_fix_1_out_13
  // Probe on mux_for_mult_1_cout
  assign controlled_buffer_21_out = rom_1_data[49] ? register_15_q : 16'bz;  // Controlled_Buffer controlled_buffer_21
  assign controlled_buffer_13_out = rom_1_data[50] ? register_16_q : 16'bz;  // Controlled_Buffer controlled_buffer_22
  assign controlled_buffer_14_out = rom_1_data[51] ? register_17_q : 16'bz;  // Controlled_Buffer controlled_buffer_23
  Register #(.width(16)) Temp_reg (
    .D(controlled_buffer_19_out), .en(rom_1_data[14]), .clk(clock_1_out), .Q(Temp_reg_q));  // open: clr
  assign controlled_buffer_13_out = rom_1_data[16] ? Temp_reg_q : 16'bz;  // Controlled_Buffer controlled_buffer_24
  Controlled_Buffer #(.width(5)) controlled_buffer_25 (.out(register_8_q), .en(rom_1_data[13]));  // open: in
  // Probe on register_8_q
  // Probe on controlled_buffer_21_out
  // Probe on register_16_q
  RAM #(.addrWidth(5), .dataWidth(16), .\type ("nonvolatile")) ram_1 (
    .addr(register_8_q), .we(rom_1_data[58]), .oe(rom_1_data[59]), .clk(clock_1_out),
    .din(controlled_buffer_21_out), .dout(ram_1_dout));
  RAM #(.addrWidth(5), .dataWidth(16), .\type ("nonvolatile")) ram_2 (
    .addr(register_13_q), .we(rom_1_data[63]), .oe(rom_1_data[62]), .clk(clock_1_out),
    .din(controlled_buffer_13_out), .dout(ram_2_dout));
  assign controlled_buffer_14_out = rom_1_data[17] ? controlled_buffer_13_out : 16'bz;  // Controlled_Buffer controlled_buffer_26
  // Probe on register_17_q
  // Probe on Temp_reg_q
  assign register_14_q = rom_1_data[18] ? register_13_q : 5'bz;  // Controlled_Buffer controlled_buffer_27
  terminus_uno mem_swap (
    .temp_reg_cb(rom_1_data[15]), .mbr_a(register_16_q), .mbr_b(register_17_q),
    .temp_reg_out(mem_swap_temp_reg_out));
  assign controlled_buffer_4_out = rom_1_data[16] ? mem_swap_temp_reg_out : 16'bz;  // Controlled_Buffer controlled_buffer_28
  // Probe on mem_swap_temp_reg_out
  // Probe on ram_1_dout
  assign controlled_buffer_29_out = rom_1_data[21] ? ram_1_dout : 16'bz;  // Controlled_Buffer controlled_buffer_29
  // Probe on ram_2_dout
  assign controlled_buffer_14_out = rom_1_data[18] ? terminus_des_1_ram_b : 16'bz;  // Controlled_Buffer controlled_buffer_30
  RAM #(.addrWidth(5), .dataWidth(16)) ram_3 (
    .addr(register_8_q), .we(rom_1_data[56]), .oe(rom_1_data[57]), .clk(clock_1_out), .din(register_18_q),
    .dout(ram_3_dout));
  // Probe on register_18_q
  RAM #(.addrWidth(5), .dataWidth(16), .\type ("nonvolatile")) ram_4 (
    .addr(register_14_q), .we(rom_1_data[60]), .oe(rom_1_data[61]), .clk(clock_1_out),
    .din(controlled_buffer_14_out), .dout(ram_4_dout));
  terminus_des terminus_des_1 (
    .temp_reg_cb(rom_1_data[18]), .mbr_z(controlled_buffer_21_out), .ram_a(terminus_des_1_ram_a),
    .ram_b(terminus_des_1_ram_b));
  assign controlled_buffer_13_out = rom_1_data[19] ? terminus_des_1_ram_a : 16'bz;  // Controlled_Buffer controlled_buffer_31
  not not_1 (not_1_out, rom_1_data[21]);
  assign controlled_buffer_29_out = not_1_out ? ram_3_dout : 16'bz;  // Controlled_Buffer controlled_buffer_32
  Controlled_Buffer #(.width(16)) controlled_buffer_33 (
    .in(terminus_des_1_ram_a), .out(controlled_buffer_14_out));  // open: en
  Register #(.width(16)) register_18 (
    .D(sharah_e_faisal_1_ram_system), .en(rom_1_data[10]), .clk(clock_1_out), .Q(register_18_q));  // open: clr
  // Probe on ram_4_dout
  ROM #(.addrWidth(9), .dataWidth(64)) rom_1 (
    .addr({register_1_q[5], register_1_q[3:0], counter_3_q}), .data(rom_1_data));
  not not_2 (not_2_out, rom_1_data[37]);
  assign clock_1_out = rom_1_data[37] ? not_2_out : 1'bz;  // Controlled_Buffer controlled_buffer_34
  Counter #(.max('hf), .width(4)) counter_3 (
    .clr(rom_1_data[20]), .up(1'b1), .count(1'b1), .clk(clock_1_out), .Q(counter_3_q));  // open: load, D, carry
  // also tied to GND on the sheet: {controlled_buffer_1_out_3[4], register_1_q[4]}

  // Notes on the sheet:
  //   program counter for instruction ram
  //   opcode
  //   alu register
  //   overflow
  //   couldn't complete 
  //   as of yet
  //   Alu reg cb
  //   Reg 5
  //   Reg 7
  //   MAR_Zero
  //   Reg 1
  //   Reg 3
  //   Reg 2
  //   RAM counter for the system ram
  //   Reg 6
  //   MAR_A
  //   Reg 4
  //   Reg 8
  //   MAR_B
  //   depending on the output
  //   turn on the control bits
  //   of the mux
  //   00 for A
  //   10 for B
  //   01 for C
  //   11 for D
  //   bit 2 system
  //   bit 1 ram a
  //   bit 1 and 2 ram b
  //   MBR_A
  //   MBR_B
  //   MBR_Z
  //   waste of time
  //   Instruction_Ram
  //   RAM_A
  //   move
  //   System_Ram
  //   0
  //   0
  //   0
  //   0
  //   0
  //   RAM_B
  //   8
  //   4
  //   2
  //   1
  //   8
  //   4
  //   2
  //   1
  //   8
  //   4
  //   system
  //   no connection needed
  //   8
  //   4
  //   2
  //   1
  //   8
  //   4
  //   2
  //   1
  //   8
  //   4
  //   2
  //   1
  //   2
  //   1
  //   8
  //   4
  //   2
  //   1
  //   8
  //   4
  //   2
  //   2
  //   1
  //   8
  //   4
  //   2
  //   move system ram to ram a
  //   mem swap ram_a to ram_b
  //   1
  //   8
  //   4
  //   2
  //   1
  //   8
  //   4
  //   2
  //   1
  //   8
  //   4
  //   1
  //   8
  //   4
  //   2
  //   1
  //   8
  //   4
  //   2
  //   1
  //   8
  //   4
  //   2
  //   1
  //   8
  //   4
  //   halt_but_no_sucess
  //   contents of rom_1 (hex, n*v repeats v):
  //   0 820000000200000 820000000200000 12000000000000 c00000000300 60c0000000000300 60c0000000000300
  //   80000000 0 400002000 1000000002000 100000 12*0 c001806000000 1400002000 1001000002000 100000 28*0
  //   c001806000000 1400002000 1001000002000 100000 12*0 1001800400200 1801400400 100001800002000
  //   400002000 1000000002000 100000 10*0 1c14010 1000000000030000 181c008 8000000000010000 400002000
  //   1000000002000 100000 17*0 cc28000001880 c00000000880 60c0c00000000880 60c0c00000000880 cf00000001880
  //   400002000 1000000002000 100000 cc14000001880 c00000000880 60c0c00000000880 60c0c00000000880
  //   ccc0000001880 c00000000880 60c0c00000000880 60c0c00000000880 1000000002000 100000 6*0 1400460
  //   100000001401862 1000001400c62 100000001401864 1000001400c64 100000001401866 1000001400c66
  //   100000400002000 1000000002000 100000 6*0 400002040 1000000002040 100040 13*0 c001806000000
  //   1400002000 1001000002000 100000 12*0 c001806000000 1400002000 1001000002000 100000 12*0
  //   c001806000000 1400002000 1001000002000 100000 12*0 c001806000000 1400002000 1001000002000 100000
  //   12*0 400002000 1000000002000 100000 13*0 1000000000001 220000000000000 220000000000000
  //   8002000000080000 400002000 1000000002000 100000 25*0 c001806000000 1400002000 1001000002000 100000
  //   204*0 2000000000 15*0 1000000000080 220000000000000 220000000000000 10020000000c0000 400002000
  //   1000000002000 100000
  //   zero pehle 
  //   20400120000
  //   8400800000
  //   8000E00000
  //   600000
  //   881800000000
  //   7800000000
  //   60FF000000
  //   00001 add
  //   00011 mult
  //   01010 comp
  //   01011 and
  //   01100 xor
  //   01101 not
  //   10001 sub
  //   01001 mat mult
  //   00111 block load
  //   01000 block store
  //   00101 mem swap
  //   01111 move w/o flag
  //   11111 move flag 
  //   00100 store
  //   11110 halt
  //   01110 nop
  //   18
  //   checked
  //   38
  //   checked
  //   a8
  //   b8
  //   c8
  //   d8
  //   118
  //   98
  //   78
  //   88
  //   58
  //   48
  //   1e8
  //   0e8
  //   checked
  //   checked
  //   checked
  //   checked
  //   checked
  //   checked
  //   checked
  //   checked
  //   checked
  //   f8
  //   checked
  //   1f8
  //   checked
  //   checked
  //   checked
  //   rom incrementer
  //   checked
endmodule
module J_16_Core_Final_2 (
  input  RAM_A_WE,
  input  RAM_A_OE,
  input  RAM_B_OE,
  input  RAM_B_WE,
  input  Inst_RAM_OE,
  input  Inst_RAM_WE,
  input  system_RAM_OE,
  input  system_RAM_WE,
  input  MBR_B_WE,
  input  MBR_A_WE,
  input  MBR_Z_WE,
  input  inst_splitter_we,
  input  MBR_B_CB,
  input  MBR_A_CB,
  input  MBR_Z_CB,
  input  MAR_Z_WE,
  input  MAR_A_WE,
  input  MAR_B_WE,
  input  reg_8_we,
  input  reg_4_we,
  input  reg_2_we,
  input  reg_6_we,
  input  reg_7_we,
  input  reg_5_we,
  input  reg_3_we,
  input  reg_1_we,
  input  reg_a_out_cb,
  input  halt_maybe,
  input  reg_b_out_cb,
  input  Alu_reg_cb,
  input  Alu_out_cb,
  input  counter_increment_by_1,
  input  counter_increment_on,
  input  decode_cb_ramb,
  input  counter_reset,
  input  opcode_reg_we,
  input  opcode_init_cb,
  input  reg1_cb,
  input  reg5_cb,
  input  reg7_cb,
  input  Alu_register_we,
  input  overflow_reg_we,
  input  bus_select_oe,
  input  bus_select_bit1,
  input  bus_select_bit2,
  input  inst_ram_cb,
  input  reset_shit,
  input  decode_cb_rama,
  input  decode_control,
  input  temp_reg_confl,
  input  temp_reg_cb_mux,
  input  mux_control,
  input  temp_reg_we,
  input  program_counter_cb,
  input  ram_increment,
  input  ram_increment_Cb,
  input  system_reg_we,
  input  mar_a_cb,
  input  mar_b_cb,
  input  mar_b_conf_cb,
  input  mat_mult_oe,
  input  matrix_mux_cb,
  input  ramb_bustrm_cb,
  input  rama_bustrm_cb,
  input  mat_mux_cb_2,
  input  mat_mux_cb_1,
  input  mar_b_conf_2
);

  wire alu_1_carry_out, clock_1_out, not_1_out, not_2_out;
  wire [3:0] counter_3_q;
  wire [4:0] controlled_buffer_1_out, controlled_buffer_2_out, controlled_buffer_16_out, counter_1_q,
       counter_2_q, register_8_q, register_13_q, register_14_q, spliitter_1_add_a, spliitter_1_add_b;
  wire [4:4] controlled_buffer_1_out_2, controlled_buffer_1_out_3;
  wire [5:0] register_1_q;
  wire [15:0] alu_1_result, controlled_buffer_3_out, controlled_buffer_4_out, controlled_buffer_6_out,
       controlled_buffer_8_out, controlled_buffer_13_out, controlled_buffer_14_out, controlled_buffer_19_out,
       controlled_buffer_21_out, controlled_buffer_29_out, mat_mult_fix_1_out_10, mat_mult_fix_1_out_11,
       mat_mult_fix_1_out_12, mat_mult_fix_1_out_13, mem_swap_temp_reg_out, mux_for_mult_1_cout, ram_1_dout,
       ram_2_dout, ram_3_dout, ram_4_dout, register_2_q, register_4_q, register_5_q, register_6_q,
       register_7_q, register_9_q, register_10_q, register_15_q, register_16_q, register_17_q, register_18_q,
       sharah_e_faisal_1_ram_a, sharah_e_faisal_1_ram_b, sharah_e_faisal_1_ram_system, Temp_reg_q,
       terminus_des_1_ram_a;
  wire [63:0] rom_1_data;

  Counter #(.max('h1f), .width(5)) counter_1 (
    .up(1'b1), .count(rom_1_data[34]), .clk(clock_1_out), .Q(counter_1_q));  // open: clr, load, D, carry
  Register #(.width(6)) register_1 (
    .D({controlled_buffer_1_out_2[4], controlled_buffer_1_out_3[4], controlled_buffer_1_out[3:0]}),
    .en(rom_1_data[31]), .clk(clock_1_out), .Q(register_1_q), .clr(rom_1_data[20]));
  Register #(.width(16)) register_2 (
    .D(controlled_buffer_3_out), .en(rom_1_data[26]), .clk(clock_1_out), .Q(register_2_q));  // open: clr
  Register #(.width(1)) register_3 (.D(alu_1_carry_out), .en(rom_1_data[25]), .clk(clock_1_out));  // open: Q, clr
  assign {controlled_buffer_1_out_2[4], controlled_buffer_1_out_3[4], controlled_buffer_1_out[3:0]} = rom_1_data[30] ? {6{1'b0}} : 6'bz;  // Controlled_Buffer controlled_buffer_1
  assign controlled_buffer_2_out = rom_1_data[13] ? counter_1_q : 5'bz;  // Controlled_Buffer controlled_buffer_2
  // Probe on alu_1_result
  assign controlled_buffer_3_out = rom_1_data[35] ? alu_1_result : 16'bz;  // Controlled_Buffer controlled_buffer_3
  ALU alu_1 (
    .opcode({controlled_buffer_1_out_2[4], controlled_buffer_1_out[3:0]}), .A(controlled_buffer_13_out),
    .B(controlled_buffer_14_out), .result(alu_1_result), .carry_out(alu_1_carry_out));
  assign controlled_buffer_4_out = rom_1_data[36] ? register_2_q : 16'bz;  // Controlled_Buffer controlled_buffer_4
  Register #(.width(16)) register_4 (
    .D(controlled_buffer_13_out), .en(rom_1_data[38]), .clk(clock_1_out), .Q(register_4_q));  // open: clr
  Register #(.width(16)) register_5 (
    .D(controlled_buffer_13_out), .en(rom_1_data[39]), .clk(clock_1_out), .Q(register_5_q));  // open: clr
  Register #(.width(16)) register_6 (
    .D(controlled_buffer_14_out), .en(rom_1_data[40]), .clk(clock_1_out), .Q(register_6_q));  // open: clr
  Register #(.width(16)) register_7 (
    .D(controlled_buffer_14_out), .en(rom_1_data[41]), .clk(clock_1_out), .Q(register_7_q));  // open: clr
  assign controlled_buffer_2_out = rom_1_data[0] ? register_14_q : 5'bz;  // Controlled_Buffer controlled_buffer_5
  Register #(.width(5)) register_8 (
    .D(controlled_buffer_2_out), .en(rom_1_data[48]), .clk(clock_1_out), .Q(register_8_q));  // open: clr
  Spliitter spliitter_1 (
    .Instruction(controlled_buffer_21_out), .WE(rom_1_data[52]), .clk(clock_1_out),
    .Add_B(spliitter_1_add_b), .Add_A(spliitter_1_add_a), .opcode(controlled_buffer_1_out),
    .flag(controlled_buffer_1_out_2[4]));
  // Probe on register_8_q
  // Probe on spliitter_1_add_b
  // Probe on controlled_buffer_1_out
  Register #(.width(16)) register_9 (
    .D(controlled_buffer_13_out), .en(rom_1_data[43]), .clk(clock_1_out), .Q(register_9_q));  // open: clr
  Register #(.width(16)) register_10 (
    .D(controlled_buffer_14_out), .en(rom_1_data[42]), .clk(clock_1_out), .Q(register_10_q));  // open: clr
  Counter #(.max('h1f), .width(5)) counter_2 (
    .clr(rom_1_data[32]), .up(1'b0), .count(rom_1_data[12]), .clk(clock_1_out), .Q(counter_2_q));  // open: load, D, carry
  // Probe on spliitter_1_add_a
  assign controlled_buffer_6_out = rom_1_data[29] ? register_4_q : 16'bz;  // Controlled_Buffer controlled_buffer_6
  Controlled_Buffer #(.width(16)) controlled_buffer_7 (.in(register_5_q), .out(controlled_buffer_6_out));  // open: en
  Register #(.width(16)) register_11 (
    .D(controlled_buffer_13_out), .en(rom_1_data[44]), .clk(clock_1_out), .Q(controlled_buffer_6_out));  // open: clr
  assign controlled_buffer_8_out = rom_1_data[28] ? register_6_q : 16'bz;  // Controlled_Buffer controlled_buffer_8
  Controlled_Buffer #(.width(16)) controlled_buffer_9 (.in(register_7_q), .out(controlled_buffer_8_out));  // open: en
  Register #(.width(16)) register_12 (
    .D(controlled_buffer_14_out), .en(rom_1_data[45]), .clk(clock_1_out), .Q(controlled_buffer_8_out));  // open: clr
  Register #(.width(5)) register_13 (
    .D(controlled_buffer_2_out), .en(rom_1_data[47]), .clk(clock_1_out), .Q(register_13_q));  // open: clr
  assign controlled_buffer_2_out = rom_1_data[9] ? spliitter_1_add_a : 5'bz;  // Controlled_Buffer controlled_buffer_10
  Controlled_Buffer #(.width(16)) controlled_buffer_11 (.in(register_9_q), .out(controlled_buffer_6_out));  // open: en
  assign controlled_buffer_8_out = rom_1_data[27] ? register_10_q : 16'bz;  // Controlled_Buffer controlled_buffer_12
  // Probe on controlled_buffer_4_out
  Controlled_Buffer #(.width(16)) controlled_buffer_13 (
    .in(controlled_buffer_6_out), .out(controlled_buffer_13_out));  // open: en
  Controlled_Buffer #(.width(16)) controlled_buffer_14 (
    .in(controlled_buffer_8_out), .out(controlled_buffer_14_out));  // open: en
  assign controlled_buffer_2_out = rom_1_data[11] ? counter_2_q : 5'bz;  // Controlled_Buffer controlled_buffer_15
  assign controlled_buffer_16_out = rom_1_data[7] ? controlled_buffer_2_out : 5'bz;  // Controlled_Buffer controlled_buffer_16
  Register #(.width(5)) register_14 (
    .D(controlled_buffer_16_out), .en(rom_1_data[46]), .clk(clock_1_out), .Q(register_14_q));  // open: clr
  assign controlled_buffer_16_out = rom_1_data[8] ? spliitter_1_add_b : 5'bz;  // Controlled_Buffer controlled_buffer_17
  Clock clock_1 (.out(clock_1_out));
  mat_mult_fix mat_mult_fix_1 (
    .OE(rom_1_data[6]), .reg_1(register_4_q), .reg_5(register_6_q), .reg_2(register_9_q),
    .reg_7(register_7_q), .reg_6(register_10_q), .reg_8(controlled_buffer_8_out), .reg_3(register_5_q),
    .reg_4(controlled_buffer_6_out), .out_10(mat_mult_fix_1_out_10), .out_11(mat_mult_fix_1_out_11),
    .out_12(mat_mult_fix_1_out_12), .out_13(mat_mult_fix_1_out_13));
  mux_for_mult mux_for_mult_1 (
    .A(mat_mult_fix_1_out_10), .B(mat_mult_fix_1_out_11), .C(mat_mult_fix_1_out_12),
    .D(mat_mult_fix_1_out_13), .cb_1(rom_1_data[1]), .cb_2(rom_1_data[2]), .cout(mux_for_mult_1_cout));
  sharah_e_faisal sharah_e_faisal_1 (
    .OE(rom_1_data[24]), .bit1(rom_1_data[23]), .bit2(rom_1_data[22]), .data_In(controlled_buffer_4_out),
    .Ram_system(sharah_e_faisal_1_ram_system), .Ram_A(sharah_e_faisal_1_ram_a),
    .Ram_B(sharah_e_faisal_1_ram_b));
  assign controlled_buffer_4_out = rom_1_data[5] ? mux_for_mult_1_cout : 16'bz;  // Controlled_Buffer controlled_buffer_18
  assign controlled_buffer_19_out = rom_1_data[3] ? sharah_e_faisal_1_ram_a : 16'bz;  // Controlled_Buffer controlled_buffer_19
  assign controlled_buffer_19_out = rom_1_data[4] ? sharah_e_faisal_1_ram_b : 16'bz;  // Controlled_Buffer controlled_buffer_20
  Register #(.width(16)) register_15 (
    .D(controlled_buffer_29_out), .en(rom_1_data[53]), .clk(clock_1_out), .Q(register_15_q));  // open: clr
  Register #(.width(16)) register_16 (
    .D(ram_2_dout), .en(rom_1_data[54]), .clk(clock_1_out), .Q(register_16_q));  // open: clr
  Register #(.width(16)) register_17 (
    .D(ram_4_dout), .en(rom_1_data[55]), .clk(clock_1_out), .Q(register_17_q));  // open: clr
  // Probe on mat_mult_fix_1_out_10
  // Probe on mat_mult_fix_1_out_11
  // Probe on mat_mult_fix_1_out_12
  // Probe on mat_mult_fix_1_out_13
  // Probe on mux_for_mult_1_cout
  assign controlled_buffer_21_out = rom_1_data[49] ? register_15_q : 16'bz;  // Controlled_Buffer controlled_buffer_21
  assign controlled_buffer_13_out = rom_1_data[50] ? register_16_q : 16'bz;  // Controlled_Buffer controlled_buffer_22
  assign controlled_buffer_14_out = rom_1_data[51] ? register_17_q : 16'bz;  // Controlled_Buffer controlled_buffer_23
  Register #(.width(16)) Temp_reg (
    .D(controlled_buffer_19_out), .en(rom_1_data[14]), .clk(clock_1_out), .Q(Temp_reg_q));  // open: clr
  assign controlled_buffer_13_out = rom_1_data[16] ? Temp_reg_q : 16'bz;  // Controlled_Buffer controlled_buffer_24
  Controlled_Buffer #(.width(5)) controlled_buffer_25 (.out(register_8_q), .en(rom_1_data[13]));  // open: in
  // Probe on register_8_q
  // Probe on controlled_buffer_21_out
  // Probe on register_16_q
  RAM #(.addrWidth(5), .dataWidth(16), .\type ("nonvolatile")) ram_1 (
    .addr(register_8_q), .we(rom_1_data[58]), .oe(rom_1_data[59]), .clk(clock_1_out),
    .din(controlled_buffer_21_out), .dout(ram_1_dout));
  RAM #(.addrWidth(5), .dataWidth(16), .\type ("nonvolatile")) ram_2 (
    .addr(register_13_q), .we(rom_1_data[63]), .oe(rom_1_data[62]), .clk(clock_1_out),
    .din(controlled_buffer_13_out), .dout(ram_2_dout));
  assign controlled_buffer_14_out = rom_1_data[17] ? controlled_buffer_13_out : 16'bz;  // Controlled_Buffer controlled_buffer_26
  // Probe on register_17_q
  // Probe on Temp_reg_q
  assign register_14_q = rom_1_data[18] ? register_13_q : 5'bz;  // Controlled_Buffer controlled_buffer_27
  terminus_uno mem_swap (
    .temp_reg_cb(rom_1_data[15]), .mbr_a(register_16_q), .mbr_b(register_17_q),
    .temp_reg_out(mem_swap_temp_reg_out));
  assign controlled_buffer_4_out = rom_1_data[16] ? mem_swap_temp_reg_out : 16'bz;  // Controlled_Buffer controlled_buffer_28
  // Probe on mem_swap_temp_reg_out
  // Probe on ram_1_dout
  assign controlled_buffer_29_out = rom_1_data[21] ? ram_1_dout : 16'bz;  // Controlled_Buffer controlled_buffer_29
  // Probe on ram_2_dout
  assign controlled_buffer_14_out = rom_1_data[18] ? terminus_des_1_ram_a : 16'bz;  // Controlled_Buffer controlled_buffer_30
  // Probe on register_18_q
  assign controlled_buffer_13_out = rom_1_data[19] ? terminus_des_1_ram_a : 16'bz;  // Controlled_Buffer controlled_buffer_31
  terminus_des terminus_des_1 (
    .temp_reg_cb(rom_1_data[18]), .mbr_z(controlled_buffer_21_out), .ram_a(terminus_des_1_ram_a),
    .ram_b(terminus_des_1_ram_a));
  not not_1 (not_1_out, rom_1_data[21]);
  Controlled_Buffer #(.width(16)) controlled_buffer_32 (
    .in(terminus_des_1_ram_a), .out(controlled_buffer_14_out));  // open: en
  RAM #(.addrWidth(5), .dataWidth(16)) ram_3 (
    .addr(register_8_q), .we(rom_1_data[56]), .oe(rom_1_data[57]), .clk(clock_1_out), .din(register_18_q),
    .dout(ram_3_dout));
  RAM #(.addrWidth(5), .dataWidth(16), .\type ("nonvolatile")) ram_4 (
    .addr(register_14_q), .we(rom_1_data[60]), .oe(rom_1_data[61]), .clk(clock_1_out),
    .din(controlled_buffer_14_out), .dout(ram_4_dout));
  assign controlled_buffer_29_out = not_1_out ? ram_3_dout : 16'bz;  // Controlled_Buffer controlled_buffer_33
  ROM #(.addrWidth(9), .dataWidth(64)) rom_1 (
    .addr({register_1_q[5], register_1_q[3:0], counter_3_q}), .data(rom_1_data));
  Register #(.width(16)) register_18 (
    .D(sharah_e_faisal_1_ram_system), .en(rom_1_data[10]), .clk(clock_1_out), .Q(register_18_q));  // open: clr
  not not_2 (not_2_out, rom_1_data[37]);
  // Probe on ram_4_dout
  assign clock_1_out = rom_1_data[37] ? not_2_out : 1'bz;  // Controlled_Buffer controlled_buffer_34
  Counter #(.max('hf), .width(4)) counter_3 (
    .clr(rom_1_data[20]), .up(1'b1), .count(1'b1), .clk(clock_1_out), .Q(counter_3_q));  // open: load, D, carry
  // also tied to GND on the sheet: {controlled_buffer_1_out_3[4], register_1_q[4]}

  // Notes on the sheet:
  //   program counter for instruction ram
  //   opcode
  //   alu register
  //   overflow
  //   couldn't complete 
  //   as of yet
  //   Alu reg cb
  //   Reg 5
  //   Reg 7
  //   MAR_Zero
  //   Reg 1
  //   Reg 3
  //   Reg 2
  //   RAM counter for the system ram
  //   Reg 6
  //   MAR_A
  //   Reg 4
  //   Reg 8
  //   MAR_B
  //   depending on the output
  //   turn on the control bits
  //   of the mux
  //   00 for A
  //   10 for B
  //   01 for C
  //   11 for D
  //   bit 2 system
  //   bit 1 ram a
  //   bit 1 and 2 ram b
  //   MBR_A
  //   MBR_B
  //   MBR_Z
  //   waste of time
  //   Instruction_Ram
  //   RAM_A
  //   move
  //   0
  //   0
  //   0
  //   0
  //   0
  //   8
  //   4
  //   2
  //   1
  //   8
  //   4
  //   2
  //   1
  //   8
  //   4
  //   no connection needed
  //   8
  //   4
  //   2
  //   1
  //   8
  //   4
  //   2
  //   1
  //   8
  //   4
  //   2
  //   1
  //   2
  //   1
  //   8
  //   4
  //   2
  //   1
  //   8
  //   4
  //   2
  //   2
  //   1
  //   8
  //   4
  //   2
  //   System_Ram
  //   1
  //   8
  //   4
  //   2
  //   1
  //   8
  //   4
  //   2
  //   1
  //   8
  //   4
  //   1
  //   8
  //   4
  //   2
  //   1
  //   8
  //   4
  //   2
  //   1
  //   8
  //   4
  //   2
  //   1
  //   8
  //   4
  //   halt_but_no_sucess
  //   RAM_B
  //   contents of rom_1 (hex, n*v repeats v):
  //   0 820000000200000 820000000200000 12000000000000 c00000000300 60c0000000000300 60c0000000000300
  //   80000000 0 400002000 1000000002000 100000 12*0 c001806000000 1400002000 1001000002000 100000 28*0
  //   c001806000000 1400002000 1001000002000 100000 12*0 1001800400200 1801400400 100001800002000
  //   400002000 1000000002000 100000 10*0 1c14010 1000000000030000 181c008 8000000000010000 400002000
  //   1000000002000 100000 17*0 cc28000001880 c00000000880 60c0c00000000880 60c0c00000000880 cf00000001880
  //   400002000 1000000002000 100000 cc14000001880 c00000000880 60c0c00000000880 60c0c00000000880
  //   ccc0000001880 c00000000880 60c0c00000000880 60c0c00000000880 1000000002000 100000 6*0 1400460
  //   100000001401862 1000001400c62 100000001401864 1000001400c64 100000001401866 1000001400c66
  //   100000400002000 1000000002000 100000 6*0 400002040 1000000002040 100040 13*0 c001806000000
  //   1400002000 1001000002000 100000 12*0 c001806000000 1400002000 1001000002000 100000 12*0
  //   c001806000000 1400002000 1001000002000 100000 12*0 c001806000000 1400002000 1001000002000 100000
  //   12*0 400002000 1000000002000 100000 13*0 1000000000001 220000000000000 220000000000000
  //   8002000000080000 400002000 1000000002000 100000 25*0 c001806000000 1400002000 1001000002000 100000
  //   204*0 2000000000 15*0 1000000000080 220000000000000 220000000000000 10020000000c0000 400002000
  //   1000000002000 100000
  //   system
  //   move system ram to ram a
  //   mem swap ram_a to ram_b
  //   zero pehle 
  //   20400120000
  //   8400800000
  //   8000E00000
  //   600000
  //   881800000000
  //   7800000000
  //   60FF000000
  //   00001 add
  //   00011 mult
  //   01010 comp
  //   01011 and
  //   01100 xor
  //   01101 not
  //   10001 sub
  //   01001 mat mult
  //   00111 block load
  //   01000 block store
  //   00101 mem swap
  //   01111 move w/o flag
  //   11111 move flag 
  //   00100 store
  //   11110 halt
  //   01110 nop
  //   18
  //   checked
  //   38
  //   checked
  //   a8
  //   b8
  //   c8
  //   d8
  //   118
  //   98
  //   78
  //   88
  //   58
  //   48
  //   1e8
  //   0e8
  //   checked
  //   checked
  //   checked
  //   checked
  //   checked
  //   checked
  //   checked
  //   checked
  //   checked
  //   f8
  //   checked
  //   1f8
  //   checked
  //   checked
  //   checked
  //   rom incrementer
  //   checked
endmodule

module J_16_Core_final_3 (
  input  RAM_A_WE,
  input  RAM_A_OE,
  input  RAM_B_OE,
  input  RAM_B_WE,
  input  Inst_RAM_OE,
  input  Inst_RAM_WE,
  input  system_RAM_OE,
  input  system_RAM_WE,
  input  MBR_B_WE,
  input  MBR_A_WE,
  input  MBR_Z_WE,
  input  inst_splitter_we,
  input  MBR_B_CB,
  input  MBR_A_CB,
  input  MBR_Z_CB,
  input  MAR_Z_WE,
  input  MAR_A_WE,
  input  MAR_B_WE,
  input  reg_8_we,
  input  reg_4_we,
  input  reg_2_we,
  input  reg_6_we,
  input  reg_7_we,
  input  reg_5_we,
  input  reg_3_we,
  input  reg_1_we,
  input  reg_a_out_cb,
  input  halt_maybe,
  input  reg_b_out_cb,
  input  Alu_reg_cb,
  input  Alu_out_cb,
  input  counter_increment_by_1,
  input  counter_increment_on,
  input  decode_cb_ramb,
  input  counter_reset,
  input  opcode_reg_we,
  input  opcode_init_cb,
  input  reg1_cb,
  input  reg5_cb,
  input  reg7_cb,
  input  Alu_register_we,
  input  overflow_reg_we,
  input  bus_select_oe,
  input  bus_select_bit1,
  input  bus_select_bit2,
  input  inst_ram_cb,
  input  reset_shit,
  input  decode_cb_rama_terminus_2,
  input  decode_control_termius_2,
  input  temp_reg_confl,
  input  temp_reg_cb_mux,
  input  mux_contro_terminus_1l,
  input  temp_reg_we,
  input  program_counter_cb,
  input  ram_increment,
  input  ram_increment_Cb,
  input  system_reg_we,
  input  mar_a_cb,
  input  mar_b_cb,
  input  mar_b_conf_cb,
  input  mat_mult_oe,
  input  matrix_mux_cb,
  input  ramb_bustrm_cb,
  input  rama_bustrm_cb,
  input  mat_mux_cb_2,
  input  mat_mux_cb_1,
  input  mar_b_conf_2
);

  wire alu_1_carry_out, clock_1_out, not_1_out, not_2_out;
  wire [3:0] counter_3_q;
  wire [4:0] controlled_buffer_1_out, controlled_buffer_2_out, controlled_buffer_16_out, counter_1_q,
       counter_2_q, register_8_q, register_13_q, register_14_q, spliitter_1_add_a, spliitter_1_add_b;
  wire [4:4] controlled_buffer_1_out_2, controlled_buffer_1_out_3;
  wire [5:0] register_1_q;
  wire [15:0] alu_1_result, controlled_buffer_3_out, controlled_buffer_4_out, controlled_buffer_6_out,
       controlled_buffer_8_out, controlled_buffer_13_out, controlled_buffer_14_out, controlled_buffer_19_out,
       controlled_buffer_21_out, controlled_buffer_29_out, mat_mult_fix_1_out_10, mat_mult_fix_1_out_11,
       mat_mult_fix_1_out_12, mat_mult_fix_1_out_13, mem_swap_temp_reg_out, mux_for_mult_1_cout, ram_1_dout,
       ram_2_dout, ram_3_dout, ram_4_dout, register_2_q, register_4_q, register_5_q, register_6_q,
       register_7_q, register_9_q, register_10_q, register_15_q, register_16_q, register_17_q, register_18_q,
       sharah_e_faisal_1_ram_a, sharah_e_faisal_1_ram_b, sharah_e_faisal_1_ram_system, Temp_reg_q,
       terminus_des_1_ram_a, terminus_des_1_ram_b;
  wire [63:0] rom_1_data;

  Counter #(.max('h1f), .width(5)) counter_1 (
    .up(1'b1), .count(rom_1_data[34]), .clk(clock_1_out), .Q(counter_1_q));  // open: clr, load, D, carry
  Register #(.width(6)) register_1 (
    .D({controlled_buffer_1_out_2[4], controlled_buffer_1_out_3[4], controlled_buffer_1_out[3:0]}),
    .en(rom_1_data[31]), .clk(clock_1_out), .Q(register_1_q), .clr(rom_1_data[20]));
  Register #(.width(16)) register_2 (
    .D(controlled_buffer_3_out), .en(rom_1_data[26]), .clk(clock_1_out), .Q(register_2_q));  // open: clr
  Register #(.width(1)) register_3 (.D(alu_1_carry_out), .en(rom_1_data[25]), .clk(clock_1_out));  // open: Q, clr
  assign {controlled_buffer_1_out_2[4], controlled_buffer_1_out_3[4], controlled_buffer_1_out[3:0]} = rom_1_data[30] ? {6{1'b0}} : 6'bz;  // Controlled_Buffer controlled_buffer_1
  assign controlled_buffer_2_out = rom_1_data[13] ? counter_1_q : 5'bz;  // Controlled_Buffer controlled_buffer_2
  // Probe on alu_1_result
  assign controlled_buffer_3_out = rom_1_data[35] ? alu_1_result : 16'bz;  // Controlled_Buffer controlled_buffer_3
  ALU alu_1 (
    .opcode({controlled_buffer_1_out_2[4], controlled_buffer_1_out[3:0]}), .A(controlled_buffer_13_out),
    .B(controlled_buffer_14_out), .result(alu_1_result), .carry_out(alu_1_carry_out));
  assign controlled_buffer_4_out = rom_1_data[36] ? register_2_q : 16'bz;  // Controlled_Buffer controlled_buffer_4
  Register #(.width(16)) register_4 (
    .D(controlled_buffer_13_out), .en(rom_1_data[38]), .clk(clock_1_out), .Q(register_4_q));  // open: clr
  Register #(.width(16)) register_5 (
    .D(controlled_buffer_13_out), .en(rom_1_data[39]), .clk(clock_1_out), .Q(register_5_q));  // open: clr
  Register #(.width(16)) register_6 (
    .D(controlled_buffer_14_out), .en(rom_1_data[40]), .clk(clock_1_out), .Q(register_6_q));  // open: clr
  Register #(.width(16)) register_7 (
    .D(controlled_buffer_14_out), .en(rom_1_data[41]), .clk(clock_1_out), .Q(register_7_q));  // open: clr
  assign controlled_buffer_2_out = rom_1_data[0] ? register_14_q : 5'bz;  // Controlled_Buffer controlled_buffer_5
  Register #(.width(5)) register_8 (
    .D(controlled_buffer_2_out), .en(rom_1_data[48]), .clk(clock_1_out), .Q(register_8_q));  // open: clr
  Spliitter spliitter_1 (
    .Instruction(controlled_buffer_21_out), .WE(rom_1_data[52]), .clk(clock_1_out),
    .Add_B(spliitter_1_add_b), .Add_A(spliitter_1_add_a), .opcode(controlled_buffer_1_out),
    .flag(controlled_buffer_1_out_2[4]));
  // Probe on register_8_q
  // Probe on spliitter_1_add_b
  // Probe on controlled_buffer_1_out
  Register #(.width(16)) register_9 (
    .D(controlled_buffer_13_out), .en(rom_1_data[43]), .clk(clock_1_out), .Q(register_9_q));  // open: clr
  Register #(.width(16)) register_10 (
    .D(controlled_buffer_14_out), .en(rom_1_data[42]), .clk(clock_1_out), .Q(register_10_q));  // open: clr
  Counter #(.max('h1f), .width(5)) counter_2 (
    .clr(rom_1_data[32]), .up(1'b0), .count(rom_1_data[12]), .clk(clock_1_out), .Q(counter_2_q));  // open: load, D, carry
  // Probe on spliitter_1_add_a
  assign controlled_buffer_6_out = rom_1_data[29] ? register_4_q : 16'bz;  // Controlled_Buffer controlled_buffer_6
  Controlled_Buffer #(.width(16)) controlled_buffer_7 (.in(register_5_q), .out(controlled_buffer_6_out));  // open: en
  Register #(.width(16)) register_11 (
    .D(controlled_buffer_13_out), .en(rom_1_data[44]), .clk(clock_1_out), .Q(controlled_buffer_6_out));  // open: clr
  assign controlled_buffer_8_out = rom_1_data[28] ? register_6_q : 16'bz;  // Controlled_Buffer controlled_buffer_8
  Controlled_Buffer #(.width(16)) controlled_buffer_9 (.in(register_7_q), .out(controlled_buffer_8_out));  // open: en
  Register #(.width(16)) register_12 (
    .D(controlled_buffer_14_out), .en(rom_1_data[45]), .clk(clock_1_out), .Q(controlled_buffer_8_out));  // open: clr
  Register #(.width(5)) register_13 (
    .D(controlled_buffer_2_out), .en(rom_1_data[47]), .clk(clock_1_out), .Q(register_13_q));  // open: clr
  assign controlled_buffer_2_out = rom_1_data[9] ? spliitter_1_add_a : 5'bz;  // Controlled_Buffer controlled_buffer_10
  Controlled_Buffer #(.width(16)) controlled_buffer_11 (.in(register_9_q), .out(controlled_buffer_6_out));  // open: en
  assign controlled_buffer_8_out = rom_1_data[27] ? register_10_q : 16'bz;  // Controlled_Buffer controlled_buffer_12
  // Probe on controlled_buffer_4_out
  Controlled_Buffer #(.width(16)) controlled_buffer_13 (
    .in(controlled_buffer_6_out), .out(controlled_buffer_13_out));  // open: en
  Controlled_Buffer #(.width(16)) controlled_buffer_14 (
    .in(controlled_buffer_8_out), .out(controlled_buffer_14_out));  // open: en
  assign controlled_buffer_2_out = rom_1_data[11] ? counter_2_q : 5'bz;  // Controlled_Buffer controlled_buffer_15
  assign controlled_buffer_16_out = rom_1_data[7] ? controlled_buffer_2_out : 5'bz;  // Controlled_Buffer controlled_buffer_16
  Register #(.width(5)) register_14 (
    .D(controlled_buffer_16_out), .en(rom_1_data[46]), .clk(clock_1_out), .Q(register_14_q));  // open: clr
  assign controlled_buffer_16_out = rom_1_data[8] ? spliitter_1_add_b : 5'bz;  // Controlled_Buffer controlled_buffer_17
  Clock clock_1 (.out(clock_1_out));
  mat_mult_fix mat_mult_fix_1 (
    .OE(rom_1_data[6]), .reg_1(register_4_q), .reg_5(register_6_q), .reg_2(register_9_q),
    .reg_7(register_7_q), .reg_6(register_10_q), .reg_8(controlled_buffer_8_out), .reg_3(register_5_q),
    .reg_4(controlled_buffer_6_out), .out_10(mat_mult_fix_1_out_10), .out_11(mat_mult_fix_1_out_11),
    .out_12(mat_mult_fix_1_out_12), .out_13(mat_mult_fix_1_out_13));
  mux_for_mult mux_for_mult_1 (
    .A(mat_mult_fix_1_out_10), .B(mat_mult_fix_1_out_11), .C(mat_mult_fix_1_out_12),
    .D(mat_mult_fix_1_out_13), .cb_1(rom_1_data[1]), .cb_2(rom_1_data[2]), .cout(mux_for_mult_1_cout));
  sharah_e_faisal sharah_e_faisal_1 (
    .OE(rom_1_data[24]), .bit1(rom_1_data[23]), .bit2(rom_1_data[22]), .data_In(controlled_buffer_4_out),
    .Ram_system(sharah_e_faisal_1_ram_system), .Ram_A(sharah_e_faisal_1_ram_a),
    .Ram_B(sharah_e_faisal_1_ram_b));
  assign controlled_buffer_4_out = rom_1_data[5] ? mux_for_mult_1_cout : 16'bz;  // Controlled_Buffer controlled_buffer_18
  assign controlled_buffer_19_out = rom_1_data[3] ? sharah_e_faisal_1_ram_a : 16'bz;  // Controlled_Buffer controlled_buffer_19
  assign controlled_buffer_19_out = rom_1_data[4] ? sharah_e_faisal_1_ram_b : 16'bz;  // Controlled_Buffer controlled_buffer_20
  Register #(.width(16)) register_15 (
    .D(controlled_buffer_29_out), .en(rom_1_data[53]), .clk(clock_1_out), .Q(register_15_q));  // open: clr
  Register #(.width(16)) register_16 (
    .D(ram_2_dout), .en(rom_1_data[54]), .clk(clock_1_out), .Q(register_16_q));  // open: clr
  Register #(.width(16)) register_17 (
    .D(ram_4_dout), .en(rom_1_data[55]), .clk(clock_1_out), .Q(register_17_q));  // open: clr
  // Probe on mat_mult_fix_1_out_10
  // Probe on mat_mult_fix_1_out_11
  // Probe on mat_mult_fix_1_out_12
  // Probe on mat_mult_fix_1_out_13
  // Probe on mux_for_mult_1_cout
  assign controlled_buffer_21_out = rom_1_data[49] ? register_15_q : 16'bz;  // Controlled_Buffer controlled_buffer_21
  assign controlled_buffer_13_out = rom_1_data[50] ? register_16_q : 16'bz;  // Controlled_Buffer controlled_buffer_22
  assign controlled_buffer_14_out = rom_1_data[51] ? register_17_q : 16'bz;  // Controlled_Buffer controlled_buffer_23
  Register #(.width(16)) Temp_reg (
    .D(controlled_buffer_19_out), .en(rom_1_data[14]), .clk(clock_1_out), .Q(Temp_reg_q));  // open: clr
  assign controlled_buffer_13_out = rom_1_data[16] ? Temp_reg_q : 16'bz;  // Controlled_Buffer controlled_buffer_24
  Controlled_Buffer #(.width(5)) controlled_buffer_25 (.out(register_8_q), .en(rom_1_data[13]));  // open: in
  // Probe on register_8_q
  // Probe on controlled_buffer_21_out
  // Probe on register_16_q
  RAM #(.addrWidth(5), .dataWidth(16), .\type ("nonvolatile")) ram_1 (
    .addr(register_8_q), .we(rom_1_data[58]), .oe(rom_1_data[59]), .clk(clock_1_out),
    .din(controlled_buffer_21_out), .dout(ram_1_dout));
  RAM #(.addrWidth(5), .dataWidth(16), .\type ("nonvolatile")) ram_2 (
    .addr(register_13_q), .we(rom_1_data[63]), .oe(rom_1_data[62]), .clk(clock_1_out),
    .din(controlled_buffer_13_out), .dout(ram_2_dout));
  assign controlled_buffer_14_out = rom_1_data[17] ? controlled_buffer_13_out : 16'bz;  // Controlled_Buffer controlled_buffer_26
  // Probe on register_17_q
  // Probe on Temp_reg_q
  assign register_14_q = rom_1_data[18] ? register_13_q : 5'bz;  // Controlled_Buffer controlled_buffer_27
  terminus_uno mem_swap (
    .temp_reg_cb(rom_1_data[15]), .mbr_a(register_16_q), .mbr_b(register_17_q),
    .temp_reg_out(mem_swap_temp_reg_out));
  assign controlled_buffer_4_out = rom_1_data[16] ? mem_swap_temp_reg_out : 16'bz;  // Controlled_Buffer controlled_buffer_28
  // Probe on mem_swap_temp_reg_out
  // Probe on ram_1_dout
  assign controlled_buffer_29_out = rom_1_data[21] ? ram_1_dout : 16'bz;  // Controlled_Buffer controlled_buffer_29
  // Probe on ram_2_dout
  assign controlled_buffer_14_out = rom_1_data[18] ? terminus_des_1_ram_b : 16'bz;  // Controlled_Buffer controlled_buffer_30
  RAM #(.addrWidth(5), .dataWidth(16)) ram_3 (
    .addr(register_8_q), .we(rom_1_data[56]), .oe(rom_1_data[57]), .clk(clock_1_out), .din(register_18_q),
    .dout(ram_3_dout));
  // Probe on register_18_q
  RAM #(.addrWidth(5), .dataWidth(16), .\type ("nonvolatile")) ram_4 (
    .addr(register_14_q), .we(rom_1_data[60]), .oe(rom_1_data[61]), .clk(clock_1_out),
    .din(controlled_buffer_14_out), .dout(ram_4_dout));
  terminus_des terminus_des_1 (
    .temp_reg_cb(rom_1_data[18]), .mbr_z(controlled_buffer_21_out), .ram_a(terminus_des_1_ram_a),
    .ram_b(terminus_des_1_ram_b));
  assign controlled_buffer_13_out = rom_1_data[19] ? terminus_des_1_ram_a : 16'bz;  // Controlled_Buffer controlled_buffer_31
  not not_1 (not_1_out, rom_1_data[21]);
  assign controlled_buffer_29_out = not_1_out ? ram_3_dout : 16'bz;  // Controlled_Buffer controlled_buffer_32
  Controlled_Buffer #(.width(16)) controlled_buffer_33 (
    .in(terminus_des_1_ram_a), .out(controlled_buffer_14_out));  // open: en
  Register #(.width(16)) register_18 (
    .D(sharah_e_faisal_1_ram_system), .en(rom_1_data[10]), .clk(clock_1_out), .Q(register_18_q));  // open: clr
  // Probe on ram_4_dout
  ROM #(.addrWidth(9), .dataWidth(64)) rom_1 (
    .addr({register_1_q[5], register_1_q[3:0], counter_3_q}), .data(rom_1_data));
  not not_2 (not_2_out, rom_1_data[37]);
  assign clock_1_out = rom_1_data[37] ? not_2_out : 1'bz;  // Controlled_Buffer controlled_buffer_34
  Counter #(.max('hf), .width(4)) counter_3 (
    .clr(rom_1_data[20]), .up(1'b1), .count(1'b1), .clk(clock_1_out), .Q(counter_3_q));  // open: load, D, carry
  // also tied to GND on the sheet: {controlled_buffer_1_out_3[4], register_1_q[4]}

  // Notes on the sheet:
  //   program counter for instruction ram
  //   opcode
  //   alu register
  //   overflow
  //   couldn't complete 
  //   as of yet
  //   Alu reg cb
  //   Reg 5
  //   Reg 7
  //   MAR_Zero
  //   Reg 1
  //   Reg 3
  //   Reg 2
  //   RAM counter for the system ram
  //   Reg 6
  //   MAR_A
  //   Reg 4
  //   Reg 8
  //   MAR_B
  //   depending on the output
  //   turn on the control bits
  //   of the mux
  //   00 for A
  //   10 for B
  //   01 for C
  //   11 for D
  //   bit 2 system
  //   bit 1 ram a
  //   bit 1 and 2 ram b
  //   MBR_A
  //   MBR_B
  //   MBR_Z
  //   waste of time
  //   Instruction_Ram
  //   RAM_A
  //   move
  //   System_Ram
  //   0
  //   0
  //   0
  //   0
  //   0
  //   RAM_B
  //   8
  //   4
  //   2
  //   1
  //   8
  //   4
  //   2
  //   1
  //   8
  //   4
  //   system
  //   move system ram to ram a
  //   mem swap ram_a to ram_b
  //   no connection needed
  //   8
  //   4
  //   2
  //   1
  //   8
  //   4
  //   2
  //   1
  //   8
  //   4
  //   2
  //   1
  //   2
  //   1
  //   8
  //   4
  //   2
  //   1
  //   8
  //   4
  //   2
  //   2
  //   1
  //   8
  //   4
  //   2
  //   1
  //   8
  //   4
  //   2
  //   1
  //   8
  //   4
  //   2
  //   1
  //   8
  //   4
  //   1
  //   8
  //   4
  //   2
  //   1
  //   8
  //   4
  //   2
  //   1
  //   8
  //   4
  //   2
  //   1
  //   8
  //   4
  //   halt_but_no_sucess
  //   contents of rom_1 (hex, n*v repeats v):
  //   0 820000000200000 820000000200000 12000000000000 c00000000300 60c0000000000300 60c0000000000300
  //   80000000 0 400002000 1000000002000 100000 12*0 c001806000000 1400002000 1001000002000 100000 28*0
  //   c001806000000 1400002000 1001000002000 100000 12*0 1001800400200 1801400400 100001800002000
  //   400002000 1000000002000 100000 10*0 1c14010 1000000000030000 181c008 8000000000010000 400002000
  //   1000000002000 100000 17*0 cc28000001880 c00000000880 60c0c00000000880 60c0c00000000880 cf00000001880
  //   400002000 1000000002000 100000 cc14000001880 c00000000880 60c0c00000000880 60c0c00000000880
  //   ccc0000001880 c00000000880 60c0c00000000880 60c0c00000000880 1000000002000 100000 6*0 1400460
  //   100000001401862 1000001400c62 100000001401864 1000001400c64 100000001401866 1000001400c66
  //   100000400002000 1000000002000 100000 6*0 400002040 1000000002040 100040 13*0 c001806000000
  //   1400002000 1001000002000 100000 12*0 c001806000000 1400002000 1001000002000 100000 12*0
  //   c001806000000 1400002000 1001000002000 100000 12*0 c001806000000 1400002000 1001000002000 100000
  //   12*0 400002000 1000000002000 100000 13*0 1000000000001 220000000000000 220000000000000
  //   8002000000080000 400002000 1000000002000 100000 25*0 c001806000000 1400002000 1001000002000 100000
  //   204*0 2000000000 15*0 1000000000080 220000000000000 220000000000000 10020000000c0000 400002000
  //   1000000002000 100000
  //   zero pehle 
  //   20400120000
  //   8400800000
  //   8000E00000
  //   600000
  //   881800000000
  //   7800000000
  //   60FF000000
  //   00001 add
  //   00011 mult
  //   01010 comp
  //   01011 and
  //   01100 xor
  //   01101 not
  //   10001 sub
  //   01001 mat mult
  //   00111 block load
  //   01000 block store
  //   00101 mem swap
  //   01111 move w/o flag
  //   11111 move flag 
  //   00100 store
  //   11110 halt
  //   01110 nop
  //   18
  //   checked
  //   38
  //   checked
  //   a8
  //   b8
  //   c8
  //   d8
  //   118
  //   98
  //   78
  //   88
  //   58
  //   48
  //   1e8
  //   0e8
  //   checked
  //   checked
  //   checked
  //   checked
  //   checked
  //   checked
  //   checked
  //   checked
  //   checked
  //   f8
  //   checked
  //   1f8
  //   checked
  //   checked
  //   checked
  //   rom incrementer
  //   checked
  //   part is useless
  //   store in system ram
  //   and ram b
  //   defining opcodes
  //   all logical operations the opcode contains
  //   the address of data in ram a ,ram b
  //   store contains only the address of where it
  //   will be stored in system ram
  //   only the first part defines address second 
  //   halt , nop adress doesn't matter
  //   block load contains adress of data in ram a
  //   mat mult address doesn't matters
  //   block store contains address of where to
  //   mem swap contains address of data in ram a 
  //   move with and without flag in both adress a
  //   defines location in ram while address b defines
  //   and ram b the other adresses should be subsequent of it
  //   location in system ram where data is to be moved from
endmodule

module J_16_Core_final_4 (
  input  RAM_A_WE,
  input  RAM_A_OE,
  input  RAM_B_OE,
  input  RAM_B_WE,
  input  Inst_RAM_OE,
  input  Inst_RAM_WE,
  input  system_RAM_OE,
  input  system_RAM_WE,
  input  MBR_B_WE,
  input  MBR_A_WE,
  input  MBR_Z_WE,
  input  inst_splitter_we,
  input  MBR_B_CB,
  input  MBR_A_CB,
  input  MBR_Z_CB,
  input  MAR_Z_WE,
  input  MAR_A_WE,
  input  MAR_B_WE,
  input  reg_8_we,
  input  reg_4_we,
  input  reg_2_we,
  input  reg_6_we,
  input  reg_7_we,
  input  reg_5_we,
  input  reg_3_we,
  input  reg_1_we,
  input  reg_a_out_cb,
  input  halt_maybe,
  input  reg_b_out_cb,
  input  Alu_reg_cb,
  input  Alu_out_cb,
  input  counter_increment_by_1,
  input  counter_increment_on,
  input  decode_cb_ramb,
  input  counter_reset,
  input  opcode_reg_we,
  input  opcode_init_cb,
  input  reg1_cb,
  input  reg5_cb,
  input  reg7_cb,
  input  Alu_register_we,
  input  overflow_reg_we,
  input  bus_select_oe,
  input  bus_select_bit1,
  input  bus_select_bit2,
  input  inst_ram_cb,
  input  reset_shit,
  input  decode_cb_rama_terminus_2,
  input  decode_control_termius_2,
  input  temp_reg_confl,
  input  temp_reg_cb_mux,
  input  mux_contro_terminus_1l,
  input  temp_reg_we,
  input  program_counter_cb,
  input  ram_increment,
  input  ram_increment_Cb,
  input  system_reg_we,
  input  mar_a_cb,
  input  mar_b_cb,
  input  mar_b_conf_cb,
  input  mat_mult_oe,
  input  matrix_mux_cb,
  input  ramb_bustrm_cb,
  input  rama_bustrm_cb,
  input  mat_mux_cb_2,
  input  mat_mux_cb_1,
  input  mar_b_conf_2
);

  wire alu_1_carry_out, clock_1_out, not_1_out, not_2_out;
  wire [3:0] counter_3_q;
  wire [4:0] controlled_buffer_1_out, controlled_buffer_2_out, controlled_buffer_16_out, counter_1_q,
       counter_2_q, register_8_q, register_13_q, register_14_q, spliitter_1_add_a, spliitter_1_add_b;
  wire [4:4] controlled_buffer_1_out_2, controlled_buffer_1_out_3;
  wire [5:0] register_1_q;
  wire [15:0] alu_1_result, controlled_buffer_3_out, controlled_buffer_4_out, controlled_buffer_6_out,
       controlled_buffer_8_out, controlled_buffer_13_out, controlled_buffer_14_out, controlled_buffer_19_out,
       controlled_buffer_21_out, controlled_buffer_29_out, mat_mult_fix_1_out_10, mat_mult_fix_1_out_11,
       mat_mult_fix_1_out_12, mat_mult_fix_1_out_13, mem_swap_temp_reg_out, mux_for_mult_1_cout, ram_1_dout,
       ram_2_dout, ram_3_dout, ram_4_dout, register_2_q, register_4_q, register_5_q, register_6_q,
       register_7_q, register_9_q, register_10_q, register_15_q, register_16_q, register_17_q, register_18_q,
       sharah_e_faisal_1_ram_a, sharah_e_faisal_1_ram_b, sharah_e_faisal_1_ram_system, Temp_reg_q,
       terminus_des_1_ram_a, terminus_des_1_ram_b;
  wire [63:0] rom_1_data;

  Counter #(.max('h1f), .width(5)) counter_1 (
    .up(1'b1), .count(rom_1_data[34]), .clk(clock_1_out), .Q(counter_1_q));  // open: clr, load, D, carry
  Register #(.width(6)) register_1 (
    .D({controlled_buffer_1_out_2[4], controlled_buffer_1_out_3[4], controlled_buffer_1_out[3:0]}),
    .en(rom_1_data[31]), .clk(clock_1_out), .Q(register_1_q), .clr(rom_1_data[20]));
  Register #(.width(16)) register_2 (
    .D(controlled_buffer_3_out), .en(rom_1_data[26]), .clk(clock_1_out), .Q(register_2_q));  // open: clr
  Register #(.width(1)) register_3 (.D(alu_1_carry_out), .en(rom_1_data[25]), .clk(clock_1_out));  // open: Q, clr
  assign {controlled_buffer_1_out_2[4], controlled_buffer_1_out_3[4], controlled_buffer_1_out[3:0]} = rom_1_data[30] ? {6{1'b0}} : 6'bz;  // Controlled_Buffer controlled_buffer_1
  assign controlled_buffer_2_out = rom_1_data[13] ? counter_1_q : 5'bz;  // Controlled_Buffer controlled_buffer_2
  // Probe on alu_1_result
  assign controlled_buffer_3_out = rom_1_data[35] ? alu_1_result : 16'bz;  // Controlled_Buffer controlled_buffer_3
  ALU alu_1 (
    .opcode({controlled_buffer_1_out_2[4], controlled_buffer_1_out[3:0]}), .A(controlled_buffer_13_out),
    .B(controlled_buffer_14_out), .result(alu_1_result), .carry_out(alu_1_carry_out));
  assign controlled_buffer_4_out = rom_1_data[36] ? register_2_q : 16'bz;  // Controlled_Buffer controlled_buffer_4
  Register #(.width(16)) register_4 (
    .D(controlled_buffer_13_out), .en(rom_1_data[38]), .clk(clock_1_out), .Q(register_4_q));  // open: clr
  Register #(.width(16)) register_5 (
    .D(controlled_buffer_13_out), .en(rom_1_data[39]), .clk(clock_1_out), .Q(register_5_q));  // open: clr
  Register #(.width(16)) register_6 (
    .D(controlled_buffer_14_out), .en(rom_1_data[40]), .clk(clock_1_out), .Q(register_6_q));  // open: clr
  Register #(.width(16)) register_7 (
    .D(controlled_buffer_14_out), .en(rom_1_data[41]), .clk(clock_1_out), .Q(register_7_q));  // open: clr
  assign controlled_buffer_2_out = rom_1_data[0] ? register_14_q : 5'bz;  // Controlled_Buffer controlled_buffer_5
  Register #(.width(5)) register_8 (
    .D(controlled_buffer_2_out), .en(rom_1_data[48]), .clk(clock_1_out), .Q(register_8_q));  // open: clr
  Spliitter spliitter_1 (
    .Instruction(controlled_buffer_21_out), .WE(rom_1_data[52]), .clk(clock_1_out),
    .Add_B(spliitter_1_add_b), .Add_A(spliitter_1_add_a), .opcode(controlled_buffer_1_out),
    .flag(controlled_buffer_1_out_2[4]));
  // Probe on register_8_q
  // Probe on spliitter_1_add_b
  // Probe on controlled_buffer_1_out
  Register #(.width(16)) register_9 (
    .D(controlled_buffer_13_out), .en(rom_1_data[43]), .clk(clock_1_out), .Q(register_9_q));  // open: clr
  Register #(.width(16)) register_10 (
    .D(controlled_buffer_14_out), .en(rom_1_data[42]), .clk(clock_1_out), .Q(register_10_q));  // open: clr
  Counter #(.max('h1f), .width(5)) counter_2 (
    .clr(rom_1_data[32]), .up(1'b0), .count(rom_1_data[12]), .clk(clock_1_out), .Q(counter_2_q));  // open: load, D, carry
  // Probe on spliitter_1_add_a
  assign controlled_buffer_6_out = rom_1_data[29] ? register_4_q : 16'bz;  // Controlled_Buffer controlled_buffer_6
  Controlled_Buffer #(.width(16)) controlled_buffer_7 (.in(register_5_q), .out(controlled_buffer_6_out));  // open: en
  Register #(.width(16)) register_11 (
    .D(controlled_buffer_13_out), .en(rom_1_data[44]), .clk(clock_1_out), .Q(controlled_buffer_6_out));  // open: clr
  assign controlled_buffer_8_out = rom_1_data[28] ? register_6_q : 16'bz;  // Controlled_Buffer controlled_buffer_8
  Controlled_Buffer #(.width(16)) controlled_buffer_9 (.in(register_7_q), .out(controlled_buffer_8_out));  // open: en
  Register #(.width(16)) register_12 (
    .D(controlled_buffer_14_out), .en(rom_1_data[45]), .clk(clock_1_out), .Q(controlled_buffer_8_out));  // open: clr
  Register #(.width(5)) register_13 (
    .D(controlled_buffer_2_out), .en(rom_1_data[47]), .clk(clock_1_out), .Q(register_13_q));  // open: clr
  assign controlled_buffer_2_out = rom_1_data[9] ? spliitter_1_add_a : 5'bz;  // Controlled_Buffer controlled_buffer_10
  Controlled_Buffer #(.width(16)) controlled_buffer_11 (.in(register_9_q), .out(controlled_buffer_6_out));  // open: en
  assign controlled_buffer_8_out = rom_1_data[27] ? register_10_q : 16'bz;  // Controlled_Buffer controlled_buffer_12
  // Probe on controlled_buffer_4_out
  // Probe on register_13_q
  Controlled_Buffer #(.width(16)) controlled_buffer_13 (
    .in(controlled_buffer_6_out), .out(controlled_buffer_13_out));  // open: en
  Controlled_Buffer #(.width(16)) controlled_buffer_14 (
    .in(controlled_buffer_8_out), .out(controlled_buffer_14_out));  // open: en
  assign controlled_buffer_2_out = rom_1_data[11] ? counter_2_q : 5'bz;  // Controlled_Buffer controlled_buffer_15
  assign controlled_buffer_16_out = rom_1_data[7] ? controlled_buffer_2_out : 5'bz;  // Controlled_Buffer controlled_buffer_16
  Register #(.width(5)) register_14 (
    .D(controlled_buffer_16_out), .en(rom_1_data[46]), .clk(clock_1_out), .Q(register_14_q));  // open: clr
  assign controlled_buffer_16_out = rom_1_data[8] ? spliitter_1_add_b : 5'bz;  // Controlled_Buffer controlled_buffer_17
  Clock clock_1 (.out(clock_1_out));
  // Probe on nothing
  mat_mult_fix mat_mult_fix_1 (
    .OE(rom_1_data[6]), .reg_1(register_4_q), .reg_5(register_6_q), .reg_2(register_9_q),
    .reg_7(register_7_q), .reg_6(register_10_q), .reg_8(controlled_buffer_8_out), .reg_3(register_5_q),
    .reg_4(controlled_buffer_6_out), .out_10(mat_mult_fix_1_out_10), .out_11(mat_mult_fix_1_out_11),
    .out_12(mat_mult_fix_1_out_12), .out_13(mat_mult_fix_1_out_13));
  mux_for_mult mux_for_mult_1 (
    .A(mat_mult_fix_1_out_10), .B(mat_mult_fix_1_out_11), .C(mat_mult_fix_1_out_12),
    .D(mat_mult_fix_1_out_13), .cb_1(rom_1_data[1]), .cb_2(rom_1_data[2]), .cout(mux_for_mult_1_cout));
  sharah_e_faisal sharah_e_faisal_1 (
    .OE(rom_1_data[24]), .bit1(rom_1_data[23]), .bit2(rom_1_data[22]), .data_In(controlled_buffer_4_out),
    .Ram_system(sharah_e_faisal_1_ram_system), .Ram_A(sharah_e_faisal_1_ram_a),
    .Ram_B(sharah_e_faisal_1_ram_b));
  assign controlled_buffer_4_out = rom_1_data[5] ? mux_for_mult_1_cout : 16'bz;  // Controlled_Buffer controlled_buffer_18
  assign controlled_buffer_19_out = rom_1_data[3] ? sharah_e_faisal_1_ram_a : 16'bz;  // Controlled_Buffer controlled_buffer_19
  assign controlled_buffer_19_out = rom_1_data[4] ? sharah_e_faisal_1_ram_b : 16'bz;  // Controlled_Buffer controlled_buffer_20
  Register #(.width(16)) register_15 (
    .D(controlled_buffer_29_out), .en(rom_1_data[53]), .clk(clock_1_out), .Q(register_15_q));  // open: clr
  Register #(.width(16)) register_16 (
    .D(ram_2_dout), .en(rom_1_data[54]), .clk(clock_1_out), .Q(register_16_q));  // open: clr
  Register #(.width(16)) register_17 (
    .D(ram_4_dout), .en(rom_1_data[55]), .clk(clock_1_out), .Q(register_17_q));  // open: clr
  // Probe on mat_mult_fix_1_out_10
  // Probe on mat_mult_fix_1_out_11
  // Probe on mat_mult_fix_1_out_12
  // Probe on mat_mult_fix_1_out_13
  // Probe on mux_for_mult_1_cout
  assign controlled_buffer_21_out = rom_1_data[49] ? register_15_q : 16'bz;  // Controlled_Buffer controlled_buffer_21
  assign controlled_buffer_13_out = rom_1_data[50] ? register_16_q : 16'bz;  // Controlled_Buffer controlled_buffer_22
  assign controlled_buffer_14_out = rom_1_data[51] ? register_17_q : 16'bz;  // Controlled_Buffer controlled_buffer_23
  Register #(.width(16)) Temp_reg (
    .D(controlled_buffer_19_out), .en(rom_1_data[14]), .clk(clock_1_out), .Q(Temp_reg_q));  // open: clr
  assign controlled_buffer_13_out = rom_1_data[16] ? Temp_reg_q : 16'bz;  // Controlled_Buffer controlled_buffer_24
  Controlled_Buffer #(.width(5)) controlled_buffer_25 (.out(register_8_q), .en(rom_1_data[13]));  // open: in
  // Probe on register_8_q
  // Probe on controlled_buffer_21_out
  // Probe on register_16_q
  RAM #(.addrWidth(5), .dataWidth(16), .\type ("nonvolatile")) ram_1 (
    .addr(register_8_q), .we(rom_1_data[58]), .oe(rom_1_data[59]), .clk(clock_1_out),
    .din(controlled_buffer_21_out), .dout(ram_1_dout));
  RAM #(.addrWidth(5), .dataWidth(16), .\type ("nonvolatile")) ram_2 (
    .addr(register_13_q), .we(rom_1_data[63]), .oe(rom_1_data[62]), .clk(clock_1_out),
    .din(controlled_buffer_13_out), .dout(ram_2_dout));
  assign controlled_buffer_14_out = rom_1_data[17] ? controlled_buffer_13_out : 16'bz;  // Controlled_Buffer controlled_buffer_26
  // Probe on register_17_q
  // Probe on Temp_reg_q
  assign register_14_q = rom_1_data[18] ? register_13_q : 5'bz;  // Controlled_Buffer controlled_buffer_27
  terminus_uno mem_swap (
    .temp_reg_cb(rom_1_data[15]), .mbr_a(register_16_q), .mbr_b(register_17_q),
    .temp_reg_out(mem_swap_temp_reg_out));
  assign controlled_buffer_4_out = rom_1_data[16] ? mem_swap_temp_reg_out : 16'bz;  // Controlled_Buffer controlled_buffer_28
  // Probe on mem_swap_temp_reg_out
  // Probe on ram_1_dout
  assign controlled_buffer_29_out = rom_1_data[21] ? ram_1_dout : 16'bz;  // Controlled_Buffer controlled_buffer_29
  // Probe on ram_2_dout
  assign controlled_buffer_14_out = rom_1_data[18] ? terminus_des_1_ram_b : 16'bz;  // Controlled_Buffer controlled_buffer_30
  RAM #(.addrWidth(5), .dataWidth(16)) ram_3 (
    .addr(register_8_q), .we(rom_1_data[56]), .oe(rom_1_data[57]), .clk(clock_1_out), .din(register_18_q),
    .dout(ram_3_dout));
  // Probe on register_18_q
  RAM #(.addrWidth(5), .dataWidth(16), .\type ("nonvolatile")) ram_4 (
    .addr(register_14_q), .we(rom_1_data[60]), .oe(rom_1_data[61]), .clk(clock_1_out),
    .din(controlled_buffer_14_out), .dout(ram_4_dout));
  terminus_des terminus_des_1 (
    .temp_reg_cb(rom_1_data[18]), .mbr_z(controlled_buffer_21_out), .ram_a(terminus_des_1_ram_a),
    .ram_b(terminus_des_1_ram_b));
  assign controlled_buffer_13_out = rom_1_data[19] ? terminus_des_1_ram_a : 16'bz;  // Controlled_Buffer controlled_buffer_31
  not not_1 (not_1_out, rom_1_data[21]);
  assign controlled_buffer_29_out = not_1_out ? ram_3_dout : 16'bz;  // Controlled_Buffer controlled_buffer_32
  Controlled_Buffer #(.width(16)) controlled_buffer_33 (
    .in(terminus_des_1_ram_a), .out(controlled_buffer_14_out));  // open: en
  Register #(.width(16)) register_18 (
    .D(sharah_e_faisal_1_ram_system), .en(rom_1_data[10]), .clk(clock_1_out), .Q(register_18_q));  // open: clr
  // Probe on ram_4_dout
  ROM #(.addrWidth(9), .dataWidth(64)) rom_1 (
    .addr({register_1_q[5], register_1_q[3:0], counter_3_q}), .data(rom_1_data));
  not not_2 (not_2_out, rom_1_data[37]);
  assign clock_1_out = rom_1_data[37] ? not_2_out : 1'bz;  // Controlled_Buffer controlled_buffer_34
  Counter #(.max('hf), .width(4)) counter_3 (
    .clr(rom_1_data[20]), .up(1'b1), .count(1'b1), .clk(clock_1_out), .Q(counter_3_q));  // open: load, D, carry
  // also tied to GND on the sheet: {controlled_buffer_1_out_3[4], register_1_q[4]}

  // Notes on the sheet:
  //   program counter for instruction ram
  //   opcode
  //   alu register
  //   overflow
  //   couldn't complete 
  //   as of yet
  //   Alu reg cb
  //   Reg 5
  //   Reg 7
  //   MAR_Zero
  //   Reg 1
  //   Reg 3
  //   Reg 2
  //   RAM counter 
  //   Reg 6
  //   MAR_A
  //   Reg 4
  //   Reg 8
  //   MAR_B
  //   depending on the output
  //   turn on the control bits
  //   of the mux
  //   00 for A
  //   10 for B
  //   01 for C
  //   11 for D
  //   bit 2 system
  //   bit 1 ram a
  //   bit 1 and 2 ram b
  //   MBR_A
  //   MBR_B
  //   MBR_Z
  //   waste of time
  //   Instruction_Ram
  //   RAM_A
  //   move
  //   System_Ram
  //   0
  //   0
  //   0
  //   0
  //   0
  //   RAM_B
  //   8
  //   4
  //   2
  //   1
  //   8
  //   4
  //   2
  //   1
  //   8
  //   4
  //   system
  //   move system ram to ram a
  //   mem swap ram_a to ram_b
  //   no connection needed
  //   8
  //   4
  //   2
  //   1
  //   8
  //   4
  //   2
  //   1
  //   8
  //   4
  //   2
  //   1
  //   2
  //   1
  //   8
  //   4
  //   2
  //   1
  //   8
  //   4
  //   2
  //   2
  //   1
  //   8
  //   4
  //   2
  //   1
  //   8
  //   4
  //   2
  //   1
  //   8
  //   4
  //   2
  //   1
  //   8
  //   4
  //   1
  //   8
  //   4
  //   2
  //   1
  //   8
  //   4
  //   2
  //   1
  //   8
  //   4
  //   2
  //   1
  //   8
  //   4
  //   halt_but_no_sucess
  //   contents of rom_1 (hex, n*v repeats v):
  //   0 820000000200000 820000000200000 12000000000000 c00000000300 60c0000000000300 60c0000000000300
  //   80000000 0 400002000 1000000002000 100000 12*0 c001806000000 1400002000 1001000002000 100000 28*0
  //   c001806000000 1400002000 1001000002000 100000 12*0 1001800400200 1801400400 100001800002000
  //   400002000 1000000002000 100000 10*0 1c14010 1000000000030000 181c008 8000000000010000 400002000
  //   1000000002000 100000 17*0 cc28000001880 c00000000880 60c0c00000000880 60c0c00000000880 cf00000001880
  //   400002000 1000000002000 100000 cc14000001880 c00000000880 60c0c00000000880 60c0c00000000880
  //   ccc0000001880 c00000000880 60c0c00000000880 60c0c00000000880 1000000002000 100000 6*0 1400460
  //   100000001401862 1000001400c62 100000001401864 1000001400c64 100000001401866 1000001400c66
  //   100000400002000 1000000002000 100000 6*0 400002040 1000000002040 100040 13*0 c001806000000
  //   1400002000 1001000002000 100000 12*0 c001806000000 1400002000 1001000002000 100000 12*0
  //   c001806000000 1400002000 1001000002000 100000 12*0 c001806000000 1400002000 1001000002000 100000
  //   12*0 400002000 1000000002000 100000 13*0 1000000000001 220000000000000 220000000000000
  //   8002000000080000 400002000 1000000002000 100000 25*0 c001806000000 1400002000 1001000002000 100000
  //   204*0 2000000000 15*0 1000000000080 220000000000000 220000000000000 10020000000c0000 400002000
  //   1000000002000 100000
  //   zero pehle 
  //   20400120000
  //   8400800000
  //   8000E00000
  //   600000
  //   881800000000
  //   7800000000
  //   60FF000000
  //   00001 add
  //   00011 mult
  //   01010 comp
  //   01011 and
  //   01100 xor
  //   01101 not
  //   10001 sub
  //   01001 mat mult
  //   00111 block load
  //   01000 block store
  //   00101 mem swap
  //   01111 move w/o flag
  //   11111 move flag 
  //   00100 store
  //   11110 halt
  //   01110 nop
  //   18
  //   checked
  //   38
  //   checked
  //   a8
  //   b8
  //   c8
  //   d8
  //   118
  //   98
  //   78
  //   88
  //   58
  //   48
  //   1e8
  //   0e8
  //   checked
  //   checked
  //   checked
  //   checked
  //   checked
  //   checked
  //   checked
  //   checked
  //   checked
  //   f8
  //   checked
  //   1f8
  //   checked
  //   checked
  //   checked
  //   rom incrementer
  //   checked
  //   part is useless
  //   store in system ram
  //   and ram b
  //   defining opcodes
  //   all logical operations the opcode contains
  //   the address of data in ram a ,ram b
  //   store contains only the address of where it
  //   will be stored in system ram
  //   only the first part defines address second 
  //   halt , nop adress doesn't matter
  //   block load contains adress of data in ram a
  //   mat mult address doesn't matters
  //   block store contains address of where to
  //   mem swap contains address of data in ram a 
  //   move with and without flag in both adress a
  //   defines location in ram while address b defines
  //   and ram b the other adresses should be subsequent of it
  //   location in system ram where data is to be moved from
  //   logical (advanced) 000C001806000000 0000001400002000 0001001000002000 0000000000100000
  //   store (advanced) 0001001800400200 0000001801400400 0100001800002000 0000000400002000 0001000000002000 0000000000100000
endmodule

module final_thing (
  input  RAM_A_WE,
  input  RAM_A_OE,
  input  RAM_B_OE,
  input  RAM_B_WE,
  input  Inst_RAM_OE,
  input  Inst_RAM_WE,
  input  system_RAM_OE,
  input  system_RAM_WE,
  input  MBR_B_WE,
  input  MBR_A_WE,
  input  MBR_Z_WE,
  input  inst_splitter_we,
  input  MBR_B_CB,
  input  MBR_A_CB,
  input  MBR_Z_CB,
  input  MAR_Z_WE,
  input  MAR_A_WE,
  input  MAR_B_WE,
  input  reg_8_we,
  input  reg_4_we,
  input  reg_2_we,
  input  reg_6_we,
  input  reg_7_we,
  input  reg_5_we,
  input  reg_3_we,
  input  reg_1_we,
  input  reg_a_out_cb,
  input  halt_maybe,
  input  reg_b_out_cb,
  input  Alu_reg_cb,
  input  Alu_out_cb,
  input  counter_increment_by_1,
  input  counter_increment_on,
  input  decode_cb_ramb,
  input  counter_reset,
  input  opcode_reg_we,
  input  opcode_init_cb,
  input  reg1_cb,
  input  reg5_cb,
  input  minc_regb,
  input  reg7_cb,
  input  Alu_register_we,
  input  overflow_reg_we,
  input  bus_select_oe,
  input  bus_select_bit1,
  input  bus_select_bit2,
  input  inst_ram_cb,
  input  reset_shit,
  input  decode_cb_rama_terminus_2,
  input  decode_control_termius_2,
  input  temp_reg_confl,
  input  temp_reg_cb_mux,
  input  mux_contro_terminus_1l,
  input  temp_reg_we,
  input  program_counter_cb,
  input  ram_increment,
  input  ram_increment_Cb,
  input  system_reg_we,
  input  mar_a_cb,
  input  mar_b_cb,
  input  mar_b_conf_cb,
  input  mat_mult_oe,
  input  matrix_mux_cb,
  input  ramb_bustrm_cb,
  input  rama_bustrm_cb,
  input  mat_mux_cb_2,
  input  mat_mux_cb_1,
  input  mar_b_conf_2
);

  wire alu_1_carry_out, clock_1_out, not_1_out, not_2_out;
  wire [3:0] counter_3_q;
  wire [4:0] controlled_buffer_1_out, controlled_buffer_2_out, controlled_buffer_20_out, counter_1_q,
       counter_2_q, register_8_q, register_13_q, register_14_q, spliitter_1_add_a, spliitter_1_add_b;
  wire [4:4] controlled_buffer_1_out_2, controlled_buffer_1_out_3;
  wire [5:0] register_1_q;
  wire [15:0] alu_1_result, controlled_buffer_3_out, controlled_buffer_4_out, controlled_buffer_6_out,
       controlled_buffer_8_out, controlled_buffer_15_out, controlled_buffer_18_out, controlled_buffer_23_out,
       controlled_buffer_25_out, controlled_buffer_33_out, max_increment_1_out_7, max_increment_1_out_8,
       max_increment_1_out_9, max_increment_1_out_10, mem_swap_temp_reg_out, mux_for_mult_1_cout, ram_1_dout,
       ram_2_dout, ram_3_dout, ram_4_dout, register_2_q, register_4_q, register_5_q, register_6_q,
       register_7_q, register_9_q, register_10_q, register_15_q, register_16_q, register_17_q, register_18_q,
       sharah_e_faisal_1_ram_a, sharah_e_faisal_1_ram_b, sharah_e_faisal_1_ram_system, Temp_reg_q,
       terminus_des_1_ram_a, terminus_des_1_ram_b;
  wire [63:0] rom_1_data;

  Counter #(.max('h1f), .width(5)) counter_1 (
    .up(1'b1), .count(rom_1_data[34]), .clk(clock_1_out), .Q(counter_1_q));  // open: clr, load, D, carry
  Register #(.width(6)) register_1 (
    .D({controlled_buffer_1_out_2[4], controlled_buffer_1_out_3[4], controlled_buffer_1_out[3:0]}),
    .en(rom_1_data[31]), .clk(clock_1_out), .Q(register_1_q), .clr(rom_1_data[20]));
  Register #(.width(16)) register_2 (
    .D(controlled_buffer_3_out), .en(rom_1_data[26]), .clk(clock_1_out), .Q(register_2_q));  // open: clr
  Register #(.width(1)) register_3 (.D(alu_1_carry_out), .en(rom_1_data[25]), .clk(clock_1_out));  // open: Q, clr
  assign {controlled_buffer_1_out_2[4], controlled_buffer_1_out_3[4], controlled_buffer_1_out[3:0]} = rom_1_data[30] ? {6{1'b0}} : 6'bz;  // Controlled_Buffer controlled_buffer_1
  assign controlled_buffer_2_out = rom_1_data[13] ? counter_1_q : 5'bz;  // Controlled_Buffer controlled_buffer_2
  // Probe on alu_1_result
  assign controlled_buffer_3_out = rom_1_data[35] ? alu_1_result : 16'bz;  // Controlled_Buffer controlled_buffer_3
  ALU alu_1 (
    .opcode({controlled_buffer_1_out_2[4], controlled_buffer_1_out[3:0]}), .A(controlled_buffer_15_out),
    .B(controlled_buffer_18_out), .result(alu_1_result), .carry_out(alu_1_carry_out));
  assign controlled_buffer_4_out = rom_1_data[36] ? register_2_q : 16'bz;  // Controlled_Buffer controlled_buffer_4
  Register #(.width(16)) register_4 (
    .D(controlled_buffer_15_out), .en(rom_1_data[38]), .clk(clock_1_out), .Q(register_4_q));  // open: clr
  Register #(.width(16)) register_5 (
    .D(controlled_buffer_15_out), .en(rom_1_data[39]), .clk(clock_1_out), .Q(register_5_q));  // open: clr
  Register #(.width(16)) register_6 (
    .D(controlled_buffer_18_out), .en(rom_1_data[40]), .clk(clock_1_out), .Q(register_6_q));  // open: clr
  Register #(.width(16)) register_7 (
    .D(controlled_buffer_18_out), .en(rom_1_data[41]), .clk(clock_1_out), .Q(register_7_q));  // open: clr
  assign controlled_buffer_2_out = rom_1_data[0] ? register_14_q : 5'bz;  // Controlled_Buffer controlled_buffer_5
  Register #(.width(5)) register_8 (
    .D(controlled_buffer_2_out), .en(rom_1_data[48]), .clk(clock_1_out), .Q(register_8_q));  // open: clr
  Spliitter spliitter_1 (
    .Instruction(controlled_buffer_25_out), .WE(rom_1_data[52]), .clk(clock_1_out),
    .Add_B(spliitter_1_add_b), .Add_A(spliitter_1_add_a), .opcode(controlled_buffer_1_out),
    .flag(controlled_buffer_1_out_2[4]));
  // Probe on register_8_q
  // Probe on spliitter_1_add_b
  // Probe on controlled_buffer_1_out
  Register #(.width(16)) register_9 (
    .D(controlled_buffer_15_out), .en(rom_1_data[43]), .clk(clock_1_out), .Q(register_9_q));  // open: clr
  Register #(.width(16)) register_10 (
    .D(controlled_buffer_18_out), .en(rom_1_data[42]), .clk(clock_1_out), .Q(register_10_q));  // open: clr
  Counter #(.max('h1f), .width(5)) counter_2 (
    .clr(rom_1_data[32]), .up(1'b0), .count(rom_1_data[12]), .clk(clock_1_out), .Q(counter_2_q));  // open: load, D, carry
  // Probe on spliitter_1_add_a
  assign controlled_buffer_6_out = rom_1_data[29] ? register_4_q : 16'bz;  // Controlled_Buffer controlled_buffer_6
  Controlled_Buffer #(.width(16)) controlled_buffer_7 (.in(register_5_q), .out(controlled_buffer_6_out));  // open: en
  Register #(.width(16)) register_11 (
    .D(controlled_buffer_15_out), .en(rom_1_data[44]), .clk(clock_1_out), .Q(controlled_buffer_6_out));  // open: clr
  Controlled_Buffer #(.width(16)) controlled_buffer_8 (.in(register_6_q), .out(controlled_buffer_8_out));  // open: en
  assign register_4_q = rom_1_data[28] ? register_6_q : 16'bz;  // Controlled_Buffer controlled_buffer_9
  assign controlled_buffer_8_out = rom_1_data[28] ? register_7_q : 16'bz;  // Controlled_Buffer controlled_buffer_10
  Register #(.width(16)) register_12 (
    .D(controlled_buffer_18_out), .en(rom_1_data[45]), .clk(clock_1_out), .Q(controlled_buffer_8_out));  // open: clr
  Register #(.width(5)) register_13 (
    .D(controlled_buffer_2_out), .en(rom_1_data[47]), .clk(clock_1_out), .Q(register_13_q));  // open: clr
  assign controlled_buffer_2_out = rom_1_data[9] ? spliitter_1_add_a : 5'bz;  // Controlled_Buffer controlled_buffer_11
  Controlled_Buffer #(.width(16)) controlled_buffer_12 (.in(register_9_q), .out(controlled_buffer_6_out));  // open: en
  assign register_9_q = rom_1_data[28] ? register_10_q : 16'bz;  // Controlled_Buffer controlled_buffer_13
  assign controlled_buffer_8_out = rom_1_data[27] ? register_10_q : 16'bz;  // Controlled_Buffer controlled_buffer_14
  // Probe on controlled_buffer_4_out
  // Probe on register_13_q
  Controlled_Buffer #(.width(16)) controlled_buffer_15 (
    .in(controlled_buffer_6_out), .out(controlled_buffer_15_out));  // open: en
  assign register_5_q = rom_1_data[28] ? register_7_q : 16'bz;  // Controlled_Buffer controlled_buffer_16
  assign controlled_buffer_6_out = rom_1_data[28] ? controlled_buffer_8_out : 16'bz;  // Controlled_Buffer controlled_buffer_17
  assign controlled_buffer_18_out = rom_1_data[28] ? controlled_buffer_8_out : 16'bz;  // Controlled_Buffer controlled_buffer_18
  assign controlled_buffer_2_out = rom_1_data[11] ? counter_2_q : 5'bz;  // Controlled_Buffer controlled_buffer_19
  assign controlled_buffer_20_out = rom_1_data[7] ? controlled_buffer_2_out : 5'bz;  // Controlled_Buffer controlled_buffer_20
  Register #(.width(5)) register_14 (
    .D(controlled_buffer_20_out), .en(rom_1_data[46]), .clk(clock_1_out), .Q(register_14_q));  // open: clr
  assign controlled_buffer_20_out = rom_1_data[8] ? spliitter_1_add_b : 5'bz;  // Controlled_Buffer controlled_buffer_21
  Clock clock_1 (.out(clock_1_out));
  // Probe on nothing
  max_increment max_increment_1 (
    .OE(rom_1_data[6]), .reg_1(register_4_q), .reg_5(register_9_q), .reg_2(register_5_q),
    .reg_7(controlled_buffer_6_out), .out_7(max_increment_1_out_7), .out_8(max_increment_1_out_8),
    .out_9(max_increment_1_out_9), .out_10(max_increment_1_out_10));  // open: control_reg
  mux_for_mult mux_for_mult_1 (
    .A(max_increment_1_out_7), .B(max_increment_1_out_8), .C(max_increment_1_out_9),
    .D(max_increment_1_out_10), .cb_1(rom_1_data[1]), .cb_2(rom_1_data[2]), .cout(mux_for_mult_1_cout));
  sharah_e_faisal sharah_e_faisal_1 (
    .OE(rom_1_data[24]), .bit1(rom_1_data[23]), .bit2(rom_1_data[22]), .data_In(controlled_buffer_4_out),
    .Ram_system(sharah_e_faisal_1_ram_system), .Ram_A(sharah_e_faisal_1_ram_a),
    .Ram_B(sharah_e_faisal_1_ram_b));
  assign controlled_buffer_4_out = rom_1_data[5] ? mux_for_mult_1_cout : 16'bz;  // Controlled_Buffer controlled_buffer_22
  assign controlled_buffer_23_out = rom_1_data[3] ? sharah_e_faisal_1_ram_a : 16'bz;  // Controlled_Buffer controlled_buffer_23
  assign controlled_buffer_23_out = rom_1_data[4] ? sharah_e_faisal_1_ram_b : 16'bz;  // Controlled_Buffer controlled_buffer_24
  Register #(.width(16)) register_15 (
    .D(controlled_buffer_33_out), .en(rom_1_data[53]), .clk(clock_1_out), .Q(register_15_q));  // open: clr
  Register #(.width(16)) register_16 (
    .D(ram_2_dout), .en(rom_1_data[54]), .clk(clock_1_out), .Q(register_16_q));  // open: clr
  Register #(.width(16)) register_17 (
    .D(ram_4_dout), .en(rom_1_data[55]), .clk(clock_1_out), .Q(register_17_q));  // open: clr
  // Probe on max_increment_1_out_7
  // Probe on max_increment_1_out_8
  // Probe on max_increment_1_out_9
  // Probe on max_increment_1_out_10
  // Probe on mux_for_mult_1_cout
  assign controlled_buffer_25_out = rom_1_data[49] ? register_15_q : 16'bz;  // Controlled_Buffer controlled_buffer_25
  assign controlled_buffer_15_out = rom_1_data[50] ? register_16_q : 16'bz;  // Controlled_Buffer controlled_buffer_26
  assign controlled_buffer_18_out = rom_1_data[51] ? register_17_q : 16'bz;  // Controlled_Buffer controlled_buffer_27
  Register #(.width(16)) Temp_reg (
    .D(controlled_buffer_23_out), .en(rom_1_data[14]), .clk(clock_1_out), .Q(Temp_reg_q));  // open: clr
  assign controlled_buffer_15_out = rom_1_data[16] ? Temp_reg_q : 16'bz;  // Controlled_Buffer controlled_buffer_28
  Controlled_Buffer #(.width(5)) controlled_buffer_29 (.out(register_8_q), .en(rom_1_data[13]));  // open: in
  // Probe on register_8_q
  // Probe on controlled_buffer_25_out
  // Probe on register_16_q
  RAM #(.addrWidth(5), .dataWidth(16), .\type ("nonvolatile")) ram_1 (
    .addr(register_8_q), .we(rom_1_data[58]), .oe(rom_1_data[59]), .clk(clock_1_out),
    .din(controlled_buffer_25_out), .dout(ram_1_dout));
  RAM #(.addrWidth(5), .dataWidth(16), .\type ("nonvolatile")) ram_2 (
    .addr(register_13_q), .we(rom_1_data[63]), .oe(rom_1_data[62]), .clk(clock_1_out),
    .din(controlled_buffer_15_out), .dout(ram_2_dout));
  assign controlled_buffer_18_out = rom_1_data[17] ? controlled_buffer_15_out : 16'bz;  // Controlled_Buffer controlled_buffer_30
  // Probe on register_17_q
  // Probe on Temp_reg_q
  assign register_14_q = rom_1_data[18] ? register_13_q : 5'bz;  // Controlled_Buffer controlled_buffer_31
  terminus_uno mem_swap (
    .temp_reg_cb(rom_1_data[15]), .mbr_a(register_16_q), .mbr_b(register_17_q),
    .temp_reg_out(mem_swap_temp_reg_out));
  assign controlled_buffer_4_out = rom_1_data[16] ? mem_swap_temp_reg_out : 16'bz;  // Controlled_Buffer controlled_buffer_32
  // Probe on mem_swap_temp_reg_out
  // Probe on ram_1_dout
  assign controlled_buffer_33_out = rom_1_data[21] ? ram_1_dout : 16'bz;  // Controlled_Buffer controlled_buffer_33
  // Probe on ram_2_dout
  assign controlled_buffer_18_out = rom_1_data[18] ? terminus_des_1_ram_b : 16'bz;  // Controlled_Buffer controlled_buffer_34
  RAM #(.addrWidth(5), .dataWidth(16)) ram_3 (
    .addr(register_8_q), .we(rom_1_data[56]), .oe(rom_1_data[57]), .clk(clock_1_out), .din(register_18_q),
    .dout(ram_3_dout));
  // Probe on register_18_q
  RAM #(.addrWidth(5), .dataWidth(16), .\type ("nonvolatile")) ram_4 (
    .addr(register_14_q), .we(rom_1_data[60]), .oe(rom_1_data[61]), .clk(clock_1_out),
    .din(controlled_buffer_18_out), .dout(ram_4_dout));
  terminus_des terminus_des_1 (
    .temp_reg_cb(rom_1_data[18]), .mbr_z(controlled_buffer_25_out), .ram_a(terminus_des_1_ram_a),
    .ram_b(terminus_des_1_ram_b));
  assign controlled_buffer_15_out = rom_1_data[19] ? terminus_des_1_ram_a : 16'bz;  // Controlled_Buffer controlled_buffer_35
  not not_1 (not_1_out, rom_1_data[21]);
  assign controlled_buffer_33_out = not_1_out ? ram_3_dout : 16'bz;  // Controlled_Buffer controlled_buffer_36
  Controlled_Buffer #(.width(16)) controlled_buffer_37 (
    .in(terminus_des_1_ram_a), .out(controlled_buffer_18_out));  // open: en
  Register #(.width(16)) register_18 (
    .D(sharah_e_faisal_1_ram_system), .en(rom_1_data[10]), .clk(clock_1_out), .Q(register_18_q));  // open: clr
  // Probe on ram_4_dout
  ROM #(.addrWidth(9), .dataWidth(64)) rom_1 (
    .addr({register_1_q[5], register_1_q[3:0], counter_3_q}), .data(rom_1_data));
  not not_2 (not_2_out, rom_1_data[37]);
  assign clock_1_out = rom_1_data[37] ? not_2_out : 1'bz;  // Controlled_Buffer controlled_buffer_38
  Counter #(.max('hf), .width(4)) counter_3 (
    .clr(rom_1_data[20]), .up(1'b1), .count(1'b1), .clk(clock_1_out), .Q(counter_3_q));  // open: load, D, carry
  // also tied to GND on the sheet: {controlled_buffer_1_out_3[4], register_1_q[4]}

  // Notes on the sheet:
  //   program counter for instruction ram
  //   opcode
  //   alu register
  //   overflow
  //   couldn't complete 
  //   as of yet
  //   Alu reg cb
  //   Reg 5
  //   Reg 7
  //   MAR_Zero
  //   Reg 1
  //   Reg 3
  //   Reg 2
  //   RAM counter 
  //   Reg 6
  //   MAR_A
  //   Reg 4
  //   Reg 8
  //   MAR_B
  //   depending on the output
  //   turn on the control bits
  //   of the mux
  //   00 for A
  //   10 for B
  //   01 for C
  //   11 for D
  //   bit 2 system
  //   bit 1 ram a
  //   bit 1 and 2 ram b
  //   MBR_A
  //   MBR_B
  //   MBR_Z
  //   waste of time
  //   Instruction_Ram
  //   RAM_A
  //   move
  //   System_Ram
  //   0
  //   0
  //   0
  //   0
  //   RAM_B
  //   system
  //   move system ram to ram a
  //   mem swap ram_a to ram_b
  //   no connection needed
  //   halt_but_no_sucess
  //   contents of rom_1 (hex, n*v repeats v):
  //   0 820000000200000 820000000200000 12000000000000 c00000000300 60c0000000000300 60c0000000000300
  //   80000000 0 400002000 1000000002000 100000 12*0 c001806000000 1400002000 1001000002000 100000 28*0
  //   c001806000000 1400002000 1001000002000 100000 12*0 1001800400200 1801400400 100001800002000
  //   400002000 1000000002000 100000 10*0 1c14010 1000000000030000 181c008 8000000000010000 400002000
  //   1000000002000 100000 17*0 cc28000001880 c00000000880 60c0c00000000880 60c0c00000000880 cf00000001880
  //   400002000 1000000002000 100000 cc14000001880 c00000000880 60c0c00000000880 60c0c00000000880
  //   ccc0000001880 c00000000880 60c0c00000000880 60c0c00000000880 1000000002000 100000 6*0 1400460
  //   100000001401862 1000001400c62 100000001401864 1000001400c64 100000001401866 1000001400c66
  //   100000400002000 1000000002000 100000 6*0 400002040 1000000002040 100040 13*0 c001806000000
  //   1400002000 1001000002000 100000 12*0 c001806000000 1400002000 1001000002000 100000 12*0
  //   c001806000000 1400002000 1001000002000 100000 12*0 c001806000000 1400002000 1001000002000 100000
  //   12*0 400002000 1000000002000 100000 13*0 1000000000001 220000000000000 220000000000000
  //   8002000000080000 400002000 1000000002000 100000 25*0 c001806000000 1400002000 1001000002000 100000
  //   124*0 410002040 1000010002040 100040 77*0 2000000000 15*0 1000000000080 220000000000000
  //   220000000000000 10020000000c0000 400002000 1000000002000 100000
  //   zero pehle 
  //   20400120000
  //   8400800000
  //   8000E00000
  //   600000
  //   881800000000
  //   7800000000
  //   60FF000000
  //   00001 add
  //   00011 mult
  //   01010 comp
  //   01011 and
  //   01100 xor
  //   01101 not
  //   10001 sub
  //   01001 mat mult
  //   00111 block load
  //   01000 block store
  //   00101 mem swap
  //   01111 move w/o flag
  //   11111 move flag 
  //   00100 store
  //   11110 halt
  //   01110 nop
  //   18
  //   checked
  //   38
  //   checked
  //   a8
  //   b8
  //   c8
  //   d8
  //   118
  //   98
  //   78
  //   88
  //   58
  //   48
  //   1e8
  //   0e8
  //   jumps at 98 for mat power
  //   checked
  //   checked
  //   checked
  //   checked
  //   checked
  //   checked
  //   checked
  //   checked
  //   checked
  //   f8
  //   checked
  //   1f8
  //   checked
  //   checked
  //   checked
  //   rom incrementer
  //   checked
  //   part is useless
  //   store in system ram
  //   and ram b
  //   defining opcodes
  //   all logical operations the opcode contains
  //   the address of data in ram a ,ram b
  //   store contains only the address of where it
  //   will be stored in system ram
  //   only the first part defines address second 
  //   halt , nop adress doesn't matter
  //   block load contains adress of data in ram a
  //   mat mult address doesn't matters
  //   block store contains address of where to
  //   mem swap contains address of data in ram a 
  //   move with and without flag in both adress a
  //   defines location in ram while address b defines
  //   and ram b the other adresses should be subsequent of it
  //   location in system ram where data is to be moved from
  //   logical (advanced) 000C001806000000 0000001400002000 0001001000002000 0000000000100000
  //   store (advanced) 0001001800400200 0000001801400400 0100001800002000 0000000400002000 0001000000002000 0000000000100000
endmodule

module max_increment (
  input  OE,
  input  [15:0] control_reg,
  input  [15:0] reg_1,
  input  [15:0] reg_5,
  input  [15:0] reg_2,
  input  [15:0] reg_7,
  output [15:0] out_7,
  output [15:0] out_8,
  output [15:0] out_9,
  output [15:0] out_10
);

  wire [7:0] bit_extender_2_out, bit_extender_3_out, bit_extender_4_out, bit_extender_5_out,
       bit_extender_6_out, bit_extender_7_out, bit_extender_8_out, bit_extender_9_out, bit_extender_10_out,
       bit_extender_11_out, bit_extender_12_out, bit_extender_13_out, bit_extender_14_out,
       bit_extender_15_out, bit_extender_16_out, bit_extender_17_out;
  wire [15:0] and_3_out, bit_extender_1_out, mult_8_1_product, mult_8_2_product, mult_8_3_product,
       mult_8_4_product, mult_8_5_product, mult_8_6_product, mult_8_7_product, mult_8_8_product,
       mult_8_9_product, mult_8_10_product, mult_8_11_product, mult_8_12_product, mult_8_13_product,
       mult_8_14_product, mult_8_15_product, mult_8_16_product, undriven;

  assign bit_extender_1_out = {{15{OE}}, OE};  // Bit_Extender bit_extender_1
  Bit_Extender #(.in_width(16), .out_width(8)) bit_extender_2 (.in(reg_1), .out(bit_extender_2_out));
  Bit_Extender #(.in_width(16), .out_width(8)) bit_extender_3 (.in(reg_5), .out(bit_extender_3_out));
  Bit_Extender #(.in_width(16), .out_width(8)) bit_extender_4 (.in(reg_2), .out(bit_extender_4_out));
  Bit_Extender #(.in_width(16), .out_width(8)) bit_extender_5 (.in(reg_7), .out(bit_extender_5_out));
  // AND_Gate and_1 is placed but not wired
  // AND_Gate and_2 is placed but not wired
  mult_8 mult_8_1 (.A(bit_extender_2_out), .B(bit_extender_2_out), .product(mult_8_1_product));  // open: carry_out
  mult_8 mult_8_2 (.A(bit_extender_3_out), .B(bit_extender_3_out), .product(mult_8_2_product));  // open: carry_out
  mult_8 mult_8_3 (.A(bit_extender_4_out), .B(bit_extender_4_out), .product(mult_8_3_product));  // open: carry_out
  mult_8 mult_8_4 (.A(bit_extender_5_out), .B(bit_extender_5_out), .product(mult_8_4_product));  // open: carry_out
  assign and_3_out = control_reg & undriven;  // AND_Gate and_3, 16 bits wide
  Bit_Extender #(.in_width(16), .out_width(8)) bit_extender_6 (.in(mult_8_1_product), .out(bit_extender_6_out));
  Bit_Extender #(.in_width(16), .out_width(8)) bit_extender_7 (.in(mult_8_2_product), .out(bit_extender_7_out));
  Bit_Extender #(.in_width(16), .out_width(8)) bit_extender_8 (.in(mult_8_3_product), .out(bit_extender_8_out));
  Bit_Extender #(.in_width(16), .out_width(8)) bit_extender_9 (.in(mult_8_4_product), .out(bit_extender_9_out));
  mult_8 mult_8_5 (.A(bit_extender_2_out), .B(bit_extender_6_out), .product(mult_8_5_product));  // open: carry_out
  mult_8 mult_8_6 (.A(bit_extender_7_out), .B(bit_extender_3_out), .product(mult_8_6_product));  // open: carry_out
  mult_8 mult_8_7 (.A(bit_extender_8_out), .B(bit_extender_4_out), .product(mult_8_7_product));  // open: carry_out
  mult_8 mult_8_8 (.A(bit_extender_9_out), .B(bit_extender_5_out), .product(mult_8_8_product));  // open: carry_out
  Bit_Extender #(.in_width(16), .out_width(8)) bit_extender_10 (.in(mult_8_5_product), .out(bit_extender_10_out));
  Bit_Extender #(.in_width(16), .out_width(8)) bit_extender_11 (.in(mult_8_6_product), .out(bit_extender_11_out));
  Bit_Extender #(.in_width(16), .out_width(8)) bit_extender_12 (.in(mult_8_7_product), .out(bit_extender_12_out));
  Bit_Extender #(.in_width(16), .out_width(8)) bit_extender_13 (.in(mult_8_8_product), .out(bit_extender_13_out));
  mult_8 mult_8_9 (.A(bit_extender_2_out), .B(bit_extender_10_out), .product(mult_8_9_product));  // open: carry_out
  mult_8 mult_8_10 (.A(bit_extender_11_out), .B(bit_extender_3_out), .product(mult_8_10_product));  // open: carry_out
  mult_8 mult_8_11 (.A(bit_extender_12_out), .B(bit_extender_4_out), .product(mult_8_11_product));  // open: carry_out
  mult_8 mult_8_12 (.A(bit_extender_13_out), .B(bit_extender_5_out), .product(mult_8_12_product));  // open: carry_out
  Bit_Extender #(.in_width(16), .out_width(8)) bit_extender_14 (.in(mult_8_9_product), .out(bit_extender_14_out));
  Bit_Extender #(.in_width(16), .out_width(8)) bit_extender_15 (.in(mult_8_10_product), .out(bit_extender_15_out));
  Bit_Extender #(.in_width(16), .out_width(8)) bit_extender_16 (.in(mult_8_11_product), .out(bit_extender_16_out));
  Bit_Extender #(.in_width(16), .out_width(8)) bit_extender_17 (.in(mult_8_12_product), .out(bit_extender_17_out));
  mult_8 mult_8_13 (.A(bit_extender_2_out), .B(bit_extender_14_out), .product(mult_8_13_product));  // open: carry_out
  mult_8 mult_8_14 (.A(bit_extender_15_out), .B(bit_extender_3_out), .product(mult_8_14_product));  // open: carry_out
  mult_8 mult_8_15 (.A(bit_extender_16_out), .B(bit_extender_4_out), .product(mult_8_15_product));  // open: carry_out
  mult_8 mult_8_16 (.A(bit_extender_17_out), .B(bit_extender_5_out), .product(mult_8_16_product));  // open: carry_out
  assign out_7 = mult_8_13_product & bit_extender_1_out;  // AND_Gate and_4, 16 bits wide
  assign out_8 = mult_8_14_product & bit_extender_1_out;  // AND_Gate and_5, 16 bits wide
  assign out_9 = mult_8_15_product & bit_extender_1_out;  // AND_Gate and_6, 16 bits wide
  assign out_10 = mult_8_16_product & bit_extender_1_out;  // AND_Gate and_7, 16 bits wide

  // Notes on the sheet:
  //   squared
  //   cube
  //   fouth
  //   fifth
endmodule

module max_power (
  input  OE,
  input  [15:0] control_reg,
  input  [15:0] reg_1,
  input  [15:0] reg_5,
  input  [15:0] reg_2,
  input  [15:0] reg_7,
  output [15:0] out_7,
  output [15:0] out_8,
  output [15:0] out_9,
  output [15:0] out_10
);

  wire [7:0] bit_extender_2_out, bit_extender_3_out, bit_extender_4_out, bit_extender_5_out,
       bit_extender_6_out, bit_extender_7_out, bit_extender_8_out, bit_extender_9_out, bit_extender_10_out,
       bit_extender_11_out, bit_extender_12_out, bit_extender_13_out, bit_extender_14_out,
       bit_extender_15_out, bit_extender_16_out, bit_extender_17_out;
  wire [15:0] bit_extender_1_out, mult_8_1_product, mult_8_2_product, mult_8_3_product, mult_8_4_product,
       mult_8_5_product, mult_8_6_product, mult_8_7_product, mult_8_8_product, mult_8_9_product,
       mult_8_10_product, mult_8_11_product, mult_8_12_product, mult_8_13_product, mult_8_14_product,
       mult_8_15_product, mult_8_16_product;

  assign bit_extender_1_out = {{15{OE}}, OE};  // Bit_Extender bit_extender_1
  Bit_Extender #(.in_width(16), .out_width(8)) bit_extender_2 (.in(reg_1), .out(bit_extender_2_out));
  Bit_Extender #(.in_width(16), .out_width(8)) bit_extender_3 (.in(reg_5), .out(bit_extender_3_out));
  Bit_Extender #(.in_width(16), .out_width(8)) bit_extender_4 (.in(reg_2), .out(bit_extender_4_out));
  Bit_Extender #(.in_width(16), .out_width(8)) bit_extender_5 (.in(reg_7), .out(bit_extender_5_out));
  mult_8 mult_8_1 (.A(bit_extender_2_out), .B(bit_extender_2_out), .product(mult_8_1_product));  // open: carry_out
  mult_8 mult_8_2 (.A(bit_extender_3_out), .B(bit_extender_3_out), .product(mult_8_2_product));  // open: carry_out
  mult_8 mult_8_3 (.A(bit_extender_4_out), .B(bit_extender_4_out), .product(mult_8_3_product));  // open: carry_out
  mult_8 mult_8_4 (.A(bit_extender_5_out), .B(bit_extender_5_out), .product(mult_8_4_product));  // open: carry_out
  Bit_Extender #(.in_width(16), .out_width(8)) bit_extender_6 (.in(mult_8_1_product), .out(bit_extender_6_out));
  Bit_Extender #(.in_width(16), .out_width(8)) bit_extender_7 (.in(mult_8_2_product), .out(bit_extender_7_out));
  Bit_Extender #(.in_width(16), .out_width(8)) bit_extender_8 (.in(mult_8_3_product), .out(bit_extender_8_out));
  Bit_Extender #(.in_width(16), .out_width(8)) bit_extender_9 (.in(mult_8_4_product), .out(bit_extender_9_out));
  mult_8 mult_8_5 (.A(bit_extender_2_out), .B(bit_extender_6_out), .product(mult_8_5_product));  // open: carry_out
  mult_8 mult_8_6 (.A(bit_extender_7_out), .B(bit_extender_3_out), .product(mult_8_6_product));  // open: carry_out
  mult_8 mult_8_7 (.A(bit_extender_8_out), .B(bit_extender_4_out), .product(mult_8_7_product));  // open: carry_out
  mult_8 mult_8_8 (.A(bit_extender_9_out), .B(bit_extender_5_out), .product(mult_8_8_product));  // open: carry_out
  Bit_Extender #(.in_width(16), .out_width(8)) bit_extender_10 (.in(mult_8_5_product), .out(bit_extender_10_out));
  Bit_Extender #(.in_width(16), .out_width(8)) bit_extender_11 (.in(mult_8_6_product), .out(bit_extender_11_out));
  Bit_Extender #(.in_width(16), .out_width(8)) bit_extender_12 (.in(mult_8_7_product), .out(bit_extender_12_out));
  Bit_Extender #(.in_width(16), .out_width(8)) bit_extender_13 (.in(mult_8_8_product), .out(bit_extender_13_out));
  mult_8 mult_8_9 (.A(bit_extender_2_out), .B(bit_extender_10_out), .product(mult_8_9_product));  // open: carry_out
  mult_8 mult_8_10 (.A(bit_extender_11_out), .B(bit_extender_3_out), .product(mult_8_10_product));  // open: carry_out
  mult_8 mult_8_11 (.A(bit_extender_12_out), .B(bit_extender_4_out), .product(mult_8_11_product));  // open: carry_out
  mult_8 mult_8_12 (.A(bit_extender_13_out), .B(bit_extender_5_out), .product(mult_8_12_product));  // open: carry_out
  Bit_Extender #(.in_width(16), .out_width(8)) bit_extender_14 (.in(mult_8_9_product), .out(bit_extender_14_out));
  Bit_Extender #(.in_width(16), .out_width(8)) bit_extender_15 (.in(mult_8_10_product), .out(bit_extender_15_out));
  Bit_Extender #(.in_width(16), .out_width(8)) bit_extender_16 (.in(mult_8_11_product), .out(bit_extender_16_out));
  Bit_Extender #(.in_width(16), .out_width(8)) bit_extender_17 (.in(mult_8_12_product), .out(bit_extender_17_out));
  mult_8 mult_8_13 (.A(bit_extender_2_out), .B(bit_extender_14_out), .product(mult_8_13_product));  // open: carry_out
  mult_8 mult_8_14 (.A(bit_extender_15_out), .B(bit_extender_3_out), .product(mult_8_14_product));  // open: carry_out
  mult_8 mult_8_15 (.A(bit_extender_16_out), .B(bit_extender_4_out), .product(mult_8_15_product));  // open: carry_out
  mult_8 mult_8_16 (.A(bit_extender_17_out), .B(bit_extender_5_out), .product(mult_8_16_product));  // open: carry_out
  assign out_7 = bit_extender_1_out;  // AND_Gate and_1, 16 bits wide AND_Gate
  assign out_8 = bit_extender_1_out;  // AND_Gate and_2, 16 bits wide AND_Gate
  assign out_9 = bit_extender_1_out;  // AND_Gate and_3, 16 bits wide AND_Gate
  assign out_10 = bit_extender_1_out;  // AND_Gate and_4, 16 bits wide AND_Gate

  // Notes on the sheet:
  //   squared
  //   cube
  //   fouth
  //   fifth
endmodule

module max_power_2 (
  input  [15:0] in_1,
  input  [15:0] in_2,
  input  [15:0] in_3,
  input  [15:0] in_4,
  input  [15:0] in_5
);

  wire [7:0] bit_extender_1_out;

  Bit_Extender #(.in_width(16), .out_width(8)) bit_extender_1 (.in(in_2), .out(bit_extender_1_out));
  Bit_Extender #(.in_width(16), .out_width(8)) bit_extender_2 (.in(in_3));  // open: out
  Bit_Extender #(.in_width(16), .out_width(8)) bit_extender_3 ();  // open: in, out
  Bit_Extender #(.in_width(16), .out_width(8)) bit_extender_4 ();  // open: in, out
  Divider divider_1 ();  // open: a, b, out, upper, rem
endmodule
